// Logisim project SAP 1.5.circ as structural Verilog: 20 circuits, main circuit SAP
module SAP (
  output HLT,
  output MI,
  output RI,
  output RO,
  output IO,
  output II,
  output AI,
  output AO,
  output EO,
  output SU,
  output BI,
  output BO,
  output OI,
  output CE,
  output CO,
  output J,
  output FI
);

  wire a_register_1_o0, a_register_1_o1, a_register_1_o2, a_register_1_o3, a_register_1_o4, a_register_1_o5,
       a_register_1_o6, a_register_1_o7, ADDRESS_p1, ADDRESS_p2, ADDRESS_p3, ADDRESS_p4, ADDRESS_p5,
       ADDRESS_p6, ADDRESS_p7, ADDRESS_p8, alu_1_jc, and_1_out, and_2_out, AUTO_MANUAL_p1, b_register_1_o0,
       b_register_1_o1, b_register_1_o2, b_register_1_o3, b_register_1_o4, b_register_1_o5, b_register_1_o6,
       b_register_1_o7, binary_decoder_1_s, clock_1_out, CLR_RAM_out, CONTENT_p1, CONTENT_p2, CONTENT_p3,
       CONTENT_p4, controller_counter_1_b0, controller_counter_1_b1, controller_counter_1_b2,
       displaydecoder_1_p1, displaydecoder_1_p2, displaydecoder_1_p3, displaydecoder_1_p5,
       displaydecoder_1_p6, displaydecoder_1_p7, displaydecoder_1_p8, displaydecoder_2_p1,
       displaydecoder_2_p2, displaydecoder_2_p3, displaydecoder_2_p5, displaydecoder_2_p6,
       displaydecoder_2_p7, displaydecoder_2_p8, displaydecoder_3_p1, displaydecoder_3_p2,
       displaydecoder_3_p3, displaydecoder_3_p5, displaydecoder_3_p6, displaydecoder_3_p7,
       displaydecoder_3_p8, flag_register_1_cf, flag_register_1_zf, instruction_register_1_o0,
       instruction_register_1_o1, instruction_register_1_o2, instruction_register_1_o3,
       instruction_register_1_o4, instruction_register_1_o5, instruction_register_1_o6,
       instruction_register_1_o7, mem_address_register_1_o0, mem_address_register_1_o1,
       mem_address_register_1_o2, mem_address_register_1_o3, multiplexer_1_out, not_1_out, not_2_out,
       not_3_out, output_register_1_o0, output_register_1_o1, output_register_1_o2, output_register_1_o3,
       output_register_1_o4, output_register_1_o5, output_register_1_o6, output_register_1_o7, PM_p1,
       ram_1_o4, ram_1_o5, ram_1_o6, ram_1_o7, RST_SYS_out, selector_4_bit_1_o0, selector_4_bit_1_o1,
       selector_4_bit_1_o2, selector_4_bit_1_o3, selector_8_bit_1_o0, selector_8_bit_1_o1,
       selector_8_bit_1_o2, selector_8_bit_1_o3, selector_8_bit_1_o4, selector_8_bit_1_o5,
       selector_8_bit_1_o6, selector_8_bit_1_o7, SIGN_UNSIGNED_p1, TCK_out, WR_out, zero_detector_1_out;
  wire [1:0] flag_register_1_dsp;
  wire [3:0] binary_decoder_1_b00, binary_decoder_1_b10, binary_decoder_1_b20, mem_address_register_1_dsp,
       program_counter_1_dsp;
  wire [7:0] a_register_1_dsp, alu_1_dsp, b_register_1_dsp, instruction_register_1_dsp, ram_1_dsp;

  Button WR (.out(WR_out));
  // DipSwitch #(.NSwitches(1)) PM: pin names not known; wires that end beside it: PM_p1
  // DipSwitch #(.NSwitches(8)) CONTENT: pin names not known; wires that end beside it: CONTENT_p1, CONTENT_p2, CONTENT_p3, CONTENT_p4
  and and_1 (and_1_out, RI, and_2_out);
  not not_1 (not_1_out, not_3_out);
  and and_2 (and_2_out, not_1_out, clock_1_out);
  Multiplexer #(.enable("false")) multiplexer_1 (.in0(and_1_out), .in1(WR_out), .out(multiplexer_1_out), .sel(PM_p1));
  not not_2 (not_2_out, clock_1_out);
  not not_3 (not_3_out, not_2_out);
  // DipSwitch ADDRESS: pin names not known; wires that end beside it: ADDRESS_p1, ADDRESS_p2, ADDRESS_p3, ADDRESS_p4, ADDRESS_p5, ADDRESS_p6, ADDRESS_p7, ADDRESS_p8
  DotMatrix #(.matrixcols(4), .matrixrows(1)) dotmatrix_1 (
    .col0(mem_address_register_1_dsp[3]), .col1(mem_address_register_1_dsp[2]),
    .col2(mem_address_register_1_dsp[1]), .col3(mem_address_register_1_dsp[0]));
  DotMatrix #(.matrixcols(8), .matrixrows(1)) dotmatrix_2 (
    .col0(ram_1_dsp[7]), .col1(ram_1_dsp[6]), .col2(ram_1_dsp[5]), .col3(ram_1_dsp[4]), .col4(ram_1_dsp[3]),
    .col5(ram_1_dsp[2]), .col6(ram_1_dsp[1]), .col7(ram_1_dsp[0]));
  DotMatrix #(.matrixcols(8), .matrixrows(1)) dotmatrix_3 (
    .col0(instruction_register_1_dsp[7]), .col1(instruction_register_1_dsp[6]),
    .col2(instruction_register_1_dsp[5]), .col3(instruction_register_1_dsp[4]),
    .col4(instruction_register_1_dsp[3]), .col5(instruction_register_1_dsp[2]),
    .col6(instruction_register_1_dsp[1]), .col7(instruction_register_1_dsp[0]));
  Button RST_SYS (.out(RST_SYS_out));
  Button TCK (.out(TCK_out));
  // DipSwitch #(.NSwitches(1)) AUTO_MANUAL: pin names not known; wires that end beside it: AUTO_MANUAL_p1
  Button CLR_RAM (.out(CLR_RAM_out));
  Clock clock_1 (.TK(TCK_out), .TGL(AUTO_MANUAL_p1), .HT(HLT), .OUT(clock_1_out));
  Controller_Counter controller_counter_1 (
    .CLK(clock_1_out), .CLR(RST_SYS_out), .B0(controller_counter_1_b0), .B1(controller_counter_1_b1),
    .B2(controller_counter_1_b2));
  Selector_4_Bit selector_4_bit_1 (
    .O3(selector_4_bit_1_o3), .O2(selector_4_bit_1_o2), .O1(selector_4_bit_1_o1), .O0(selector_4_bit_1_o0),
    .A3(ADDRESS_p5), .A2(ADDRESS_p6), .A1(ADDRESS_p7), .A0(ADDRESS_p8), .B3(mem_address_register_1_o3),
    .B2(mem_address_register_1_o2), .B1(mem_address_register_1_o1), .B0(mem_address_register_1_o0), .SL(PM_p1));
  Selector_8_Bit selector_8_bit_1 (
    .O7(selector_8_bit_1_o7), .O6(selector_8_bit_1_o6), .O5(selector_8_bit_1_o5), .O4(selector_8_bit_1_o4),
    .O3(selector_8_bit_1_o3), .O2(selector_8_bit_1_o2), .O1(selector_8_bit_1_o1), .O0(selector_8_bit_1_o0),
    .A7(CONTENT_p1), .A6(CONTENT_p2), .A5(CONTENT_p3), .A4(CONTENT_p4), .A3(ADDRESS_p1), .A2(ADDRESS_p2),
    .A1(ADDRESS_p3), .A0(ADDRESS_p4), .B7(ram_1_o7), .B6(ram_1_o6), .B5(ram_1_o5), .B4(ram_1_o4),
    .B3(instruction_register_1_o3), .B2(instruction_register_1_o2), .B1(instruction_register_1_o1),
    .B0(instruction_register_1_o0), .SL(PM_p1));
  Instruction_Register instruction_register_1 (
    .I0(instruction_register_1_o0), .I1(instruction_register_1_o1), .I2(instruction_register_1_o2),
    .I3(instruction_register_1_o3), .I4(ram_1_o4), .I5(ram_1_o5), .I6(ram_1_o6), .I7(ram_1_o7),
    .O0(instruction_register_1_o0), .O1(instruction_register_1_o1), .O2(instruction_register_1_o2),
    .O3(instruction_register_1_o3), .O4(instruction_register_1_o4), .O5(instruction_register_1_o5),
    .O6(instruction_register_1_o6), .O7(instruction_register_1_o7), .GND(1'b0), .Vcc(1'b1),
    .CLK(clock_1_out), .CLR(RST_SYS_out), .II(II), .IO(IO), .DSP(instruction_register_1_dsp));
  Mem_Address_Register mem_address_register_1 (
    .I0(instruction_register_1_o0), .I1(instruction_register_1_o1), .I2(instruction_register_1_o2),
    .I3(instruction_register_1_o3), .O0(mem_address_register_1_o0), .O1(mem_address_register_1_o1),
    .O2(mem_address_register_1_o2), .O3(mem_address_register_1_o3), .CLK(clock_1_out), .CLR(RST_SYS_out),
    .MI(MI), .Vcc(1'b1), .GND(1'b0), .DSP(mem_address_register_1_dsp));
  RAM ram_1 (
    .A3(selector_4_bit_1_o0), .A2(selector_4_bit_1_o1), .A1(selector_4_bit_1_o2), .A0(selector_4_bit_1_o3),
    .D0(selector_8_bit_1_o0), .D1(selector_8_bit_1_o1), .D2(selector_8_bit_1_o2), .D3(selector_8_bit_1_o3),
    .D4(selector_8_bit_1_o4), .D5(selector_8_bit_1_o5), .D6(selector_8_bit_1_o6), .D7(selector_8_bit_1_o7),
    .Vcc(1'b1), .GND(1'b0), .RI(multiplexer_1_out), .RO(RO), .CLR(CLR_RAM_out),
    .O0(instruction_register_1_o0), .O1(instruction_register_1_o1), .O2(instruction_register_1_o2),
    .O3(instruction_register_1_o3), .O4(ram_1_o4), .O5(ram_1_o5), .O6(ram_1_o6), .O7(ram_1_o7),
    .DSP(ram_1_dsp));
  DotMatrix #(.matrixcols(8), .matrixrows(1)) dotmatrix_4 (
    .col0(ram_1_o7), .col1(ram_1_o6), .col2(ram_1_o5), .col3(ram_1_o4), .col4(instruction_register_1_o3),
    .col5(instruction_register_1_o2), .col6(instruction_register_1_o1), .col7(instruction_register_1_o0));
  Pull_Resistor pull_resistor_1 (.node(instruction_register_1_o1));
  Pull_Resistor pull_resistor_2 (.node(ram_1_o7));
  Pull_Resistor pull_resistor_3 (.node(instruction_register_1_o2));
  Pull_Resistor pull_resistor_4 (.node(instruction_register_1_o3));
  Pull_Resistor pull_resistor_5 (.node(ram_1_o5));
  Pull_Resistor pull_resistor_6 (.node(ram_1_o4));
  Pull_Resistor pull_resistor_7 (.node(ram_1_o6));
  Controller controller_1 (
    .I3(instruction_register_1_o7), .HLT(HLT), .I2(instruction_register_1_o6),
    .I1(instruction_register_1_o5), .I0(instruction_register_1_o4), .CF(flag_register_1_cf),
    .ZF(flag_register_1_zf), .C2(controller_counter_1_b2), .MI(MI), .C1(controller_counter_1_b1),
    .C0(controller_counter_1_b0), .RI(RI), .RO(RO), .IO(IO), .II(II), .AI(AI), .AO(AO), .EO(EO), .SU(SU),
    .BI(BI), .BO(BO), .OI(OI), .CE(CE), .CO(CO), .J(J), .FI(FI));
  Program_Counter program_counter_1 (
    .J(J), .Vcc(1'b1), .GND(1'b0), .CO(CO), .CLK(clock_1_out), .CE(CE), .CLR(RST_SYS_out),
    .D0(instruction_register_1_o0), .D1(instruction_register_1_o1), .D2(instruction_register_1_o2),
    .D3(instruction_register_1_o3), .B0(instruction_register_1_o0), .B1(instruction_register_1_o1),
    .B2(instruction_register_1_o2), .B3(instruction_register_1_o3), .DSP(program_counter_1_dsp));
  Pull_Resistor pull_resistor_8 (.node(instruction_register_1_o0));
  A_Register a_register_1 (
    .I0(instruction_register_1_o0), .I1(instruction_register_1_o1), .I2(instruction_register_1_o2),
    .I3(instruction_register_1_o3), .I4(ram_1_o4), .I5(ram_1_o5), .I6(ram_1_o6), .I7(ram_1_o7),
    .O0(a_register_1_o0), .O1(a_register_1_o1), .O2(a_register_1_o2), .O3(a_register_1_o3),
    .O4(a_register_1_o4), .O5(a_register_1_o5), .O7(a_register_1_o7), .GND(1'b0), .Vcc(1'b1),
    .CLK(clock_1_out), .CLR(RST_SYS_out), .AI(AI), .AO(AO), .O6(a_register_1_o6), .DSP(a_register_1_dsp));
  ALU alu_1 (
    .SU(SU), .X7(ram_1_o7), .X6(ram_1_o6), .X5(ram_1_o5), .X4(ram_1_o4), .X3(instruction_register_1_o3),
    .X2(instruction_register_1_o2), .X1(instruction_register_1_o1), .X0(instruction_register_1_o0),
    .Vcc(1'b1), .GND(1'b0), .A7(a_register_1_o7), .A6(a_register_1_o6), .A5(a_register_1_o5),
    .A4(a_register_1_o4), .A3(a_register_1_o3), .A2(a_register_1_o2), .A1(a_register_1_o1),
    .A0(a_register_1_o0), .B7(b_register_1_o7), .B6(b_register_1_o6), .B5(b_register_1_o5),
    .B4(b_register_1_o4), .B3(b_register_1_o3), .B2(b_register_1_o2), .B1(b_register_1_o1),
    .B0(b_register_1_o0), .E0(EO), .JC(alu_1_jc), .DSP(alu_1_dsp));
  B_Register b_register_1 (
    .I0(instruction_register_1_o0), .I1(instruction_register_1_o1), .I2(instruction_register_1_o2),
    .I3(instruction_register_1_o3), .I4(ram_1_o4), .I5(ram_1_o5), .I6(ram_1_o6), .I7(ram_1_o7),
    .O0(b_register_1_o0), .O1(b_register_1_o1), .O2(b_register_1_o2), .O3(b_register_1_o3),
    .O4(b_register_1_o4), .O5(b_register_1_o5), .O6(b_register_1_o6), .O7(b_register_1_o7), .GND(1'b0),
    .Vcc(1'b1), .CLK(clock_1_out), .CLR(RST_SYS_out), .BI(BI), .BO(BO), .DSP(b_register_1_dsp));
  Output_Register output_register_1 (
    .I0(instruction_register_1_o0), .I1(instruction_register_1_o1), .I2(instruction_register_1_o2),
    .I3(instruction_register_1_o3), .I4(ram_1_o4), .I5(ram_1_o5), .I6(ram_1_o6), .I7(ram_1_o7),
    .O0(output_register_1_o0), .O1(output_register_1_o1), .O2(output_register_1_o2),
    .O3(output_register_1_o3), .O4(output_register_1_o4), .O5(output_register_1_o5),
    .O6(output_register_1_o6), .O7(output_register_1_o7), .GND(1'b0), .Vcc(1'b1), .CLK(clock_1_out),
    .CLR(RST_SYS_out), .OI(OI));
  Zero_Detector zero_detector_1 (
    .I7(alu_1_dsp[7]), .I6(alu_1_dsp[6]), .I5(alu_1_dsp[5]), .I4(alu_1_dsp[4]), .I3(alu_1_dsp[3]),
    .I2(alu_1_dsp[2]), .I1(alu_1_dsp[1]), .I0(alu_1_dsp[0]), .OUT(zero_detector_1_out));
  Flag_Register flag_register_1 (
    .ZFI(zero_detector_1_out), .CFI(alu_1_jc), .DSP(flag_register_1_dsp), .ZF(flag_register_1_zf),
    .CF(flag_register_1_cf), .CLK(clock_1_out), .CLR(RST_SYS_out), .FI(FI), .Vcc(1'b1), .GND(1'b0));
  DotMatrix #(.matrixcols(4), .matrixrows(1)) dotmatrix_5 (
    .col0(program_counter_1_dsp[3]), .col1(program_counter_1_dsp[2]), .col2(program_counter_1_dsp[1]),
    .col3(program_counter_1_dsp[0]));
  DotMatrix #(.matrixcols(2), .matrixrows(1)) dotmatrix_6 (
    .col0(flag_register_1_dsp[1]), .col1(flag_register_1_dsp[0]));
  DotMatrix #(.matrixcols(8), .matrixrows(1)) dotmatrix_7 (
    .col0(a_register_1_dsp[7]), .col1(a_register_1_dsp[6]), .col2(a_register_1_dsp[5]),
    .col3(a_register_1_dsp[4]), .col4(a_register_1_dsp[3]), .col5(a_register_1_dsp[2]),
    .col6(a_register_1_dsp[1]), .col7(a_register_1_dsp[0]));
  DotMatrix #(.matrixcols(8), .matrixrows(1)) dotmatrix_8 (
    .col0(alu_1_dsp[7]), .col1(alu_1_dsp[6]), .col2(alu_1_dsp[5]), .col3(alu_1_dsp[4]), .col4(alu_1_dsp[3]),
    .col5(alu_1_dsp[2]), .col6(alu_1_dsp[1]), .col7(alu_1_dsp[0]));
  DotMatrix #(.matrixcols(8), .matrixrows(1)) dotmatrix_9 (
    .col0(b_register_1_dsp[7]), .col1(b_register_1_dsp[6]), .col2(b_register_1_dsp[5]),
    .col3(b_register_1_dsp[4]), .col4(b_register_1_dsp[3]), .col5(b_register_1_dsp[2]),
    .col6(b_register_1_dsp[1]), .col7(b_register_1_dsp[0]));
  // DipSwitch #(.NSwitches(1)) SIGN_UNSIGNED: pin names not known; wires that end beside it: SIGN_UNSIGNED_p1
  Binary_Decoder binary_decoder_1 (
    .TGL(SIGN_UNSIGNED_p1), .I7(output_register_1_o7), .I6(output_register_1_o6), .I5(output_register_1_o5),
    .I4(output_register_1_o4), .I3(output_register_1_o3), .I2(output_register_1_o2),
    .I1(output_register_1_o1), .I0(output_register_1_o0), .S(binary_decoder_1_s),
    .B23(binary_decoder_1_b20[3]), .B22(binary_decoder_1_b20[2]), .B21(binary_decoder_1_b20[1]),
    .B20(binary_decoder_1_b20[0]), .B13(binary_decoder_1_b10[3]), .B12(binary_decoder_1_b10[2]),
    .B11(binary_decoder_1_b10[1]), .B10(binary_decoder_1_b10[0]), .B03(binary_decoder_1_b00[3]),
    .B02(binary_decoder_1_b00[2]), .B01(binary_decoder_1_b00[1]), .B00(binary_decoder_1_b00[0]));
  _7_Segment_Display u_7_segment_display_1 (.g(binary_decoder_1_s));  // open: f, a, b, e, d, c, dp
  // DisplayDecoder displaydecoder_1: pin names not known; wires that end beside it: displaydecoder_1_p1, displaydecoder_1_p2, displaydecoder_1_p3, binary_decoder_1_b20, displaydecoder_1_p5, displaydecoder_1_p6, displaydecoder_1_p7, displaydecoder_1_p8
  _7_Segment_Display u_7_segment_display_2 (
    .g(displaydecoder_1_p8), .f(displaydecoder_1_p7), .a(displaydecoder_1_p1), .b(displaydecoder_1_p2),
    .e(displaydecoder_1_p6), .d(displaydecoder_1_p5), .c(displaydecoder_1_p3));  // open: dp
  // DisplayDecoder displaydecoder_2: pin names not known; wires that end beside it: displaydecoder_2_p1, displaydecoder_2_p2, displaydecoder_2_p3, binary_decoder_1_b10, displaydecoder_2_p5, displaydecoder_2_p6, displaydecoder_2_p7, displaydecoder_2_p8
  _7_Segment_Display u_7_segment_display_3 (
    .g(displaydecoder_2_p8), .f(displaydecoder_2_p7), .a(displaydecoder_2_p1), .b(displaydecoder_2_p2),
    .e(displaydecoder_2_p6), .d(displaydecoder_2_p5), .c(displaydecoder_2_p3));  // open: dp
  // DisplayDecoder displaydecoder_3: pin names not known; wires that end beside it: displaydecoder_3_p1, displaydecoder_3_p2, displaydecoder_3_p3, binary_decoder_1_b00, displaydecoder_3_p5, displaydecoder_3_p6, displaydecoder_3_p7, displaydecoder_3_p8
  _7_Segment_Display u_7_segment_display_4 (
    .g(displaydecoder_3_p8), .f(displaydecoder_3_p7), .a(displaydecoder_3_p1), .b(displaydecoder_3_p2),
    .e(displaydecoder_3_p6), .d(displaydecoder_3_p5), .c(displaydecoder_3_p3));  // open: dp
endmodule

// PC
module Program_Counter (
  input  D0,
  input  D1,
  input  D2,
  input  D3,
  input  J,
  input  Vcc,
  input  GND,
  input  CO,
  input  CLK,
  input  CE,
  input  CLR,
  output [3:0] DSP,
  output B0,
  output B1,
  output B2,
  output B3
);

  wire and_1_out, and_2_out, controlled_buffer_1_out, controlled_buffer_2_out, controlled_buffer_3_out,
       controlled_buffer_4_out, j_k_ff_1_qn, j_k_ff_2_qn, j_k_ff_3_qn, n74125_1__3, n74125_1__6, n74125_1__8,
       n74125_1__11, not_1_out, not_2_out, not_3_out, not_4_out, not_5_out, not_6_out, or_1_out, or_2_out,
       or_3_out, or_4_out, or_5_out;

  Pull_Resistor pull_resistor_1 (.node(D2));
  Pull_Resistor pull_resistor_2 (.node(D3));
  Pull_Resistor pull_resistor_3 (.node(D0));
  Pull_Resistor pull_resistor_4 (.node(D1));
  and and_1 (and_1_out, J, CLK);
  Pull_Resistor pull_resistor_5 (.node(and_1_out));
  Pull_Resistor pull_resistor_6 (.node(CLR));
  Pull_Resistor pull_resistor_7 (.node(CO));
  Pull_Resistor pull_resistor_8 (.node(CLK));
  Pull_Resistor pull_resistor_9 (.node(CE));
  or or_1 (or_1_out, CLR, and_1_out);
  not not_1 (not_1_out, and_1_out);
  not not_2 (not_2_out, CO);
  and and_2 (and_2_out, CLK, CE);
  _74125 u_74125_1 (
    .Vcc(Vcc), ._13(not_1_out), ._12(D2), ._11(n74125_1__11), ._10(not_1_out), ._9(D3), ._8(n74125_1__8),
    ._1(not_1_out), ._2(D0), ._3(n74125_1__3), ._4(not_1_out), ._5(D1), ._6(n74125_1__6), .GND(GND));
  J_K_Flip_Flop j_k_ff_1 (
    .J(1'b1), .clk(and_2_out), .K(1'b1), .Q(DSP[0]), .Qn(j_k_ff_1_qn), .preset(n74125_1__3),
    .reset(controlled_buffer_1_out));
  assign controlled_buffer_1_out = or_1_out ? or_2_out : 1'bz;  // Controlled_Buffer controlled_buffer_1
  or or_2 (or_2_out, CLR, not_3_out);
  not not_3 (not_3_out, D0);
  J_K_Flip_Flop j_k_ff_2 (
    .J(1'b1), .clk(j_k_ff_1_qn), .K(1'b1), .Q(DSP[1]), .Qn(j_k_ff_2_qn), .preset(n74125_1__6),
    .reset(controlled_buffer_2_out));
  assign controlled_buffer_2_out = or_1_out ? or_3_out : 1'bz;  // Controlled_Buffer controlled_buffer_2
  or or_3 (or_3_out, CLR, not_4_out);
  not not_4 (not_4_out, D1);
  assign controlled_buffer_3_out = or_1_out ? or_4_out : 1'bz;  // Controlled_Buffer controlled_buffer_3
  or or_4 (or_4_out, CLR, not_5_out);
  not not_5 (not_5_out, D2);
  J_K_Flip_Flop j_k_ff_3 (
    .J(1'b1), .clk(j_k_ff_2_qn), .K(1'b1), .Q(DSP[2]), .Qn(j_k_ff_3_qn), .preset(n74125_1__11),
    .reset(controlled_buffer_3_out));
  J_K_Flip_Flop j_k_ff_4 (
    .J(1'b1), .clk(j_k_ff_3_qn), .K(1'b1), .Q(DSP[3]), .preset(n74125_1__8), .reset(controlled_buffer_4_out));  // open: Qn
  assign controlled_buffer_4_out = or_1_out ? or_5_out : 1'bz;  // Controlled_Buffer controlled_buffer_4
  or or_5 (or_5_out, CLR, not_6_out);
  not not_6 (not_6_out, D3);
  _74125 u_74125_2 (
    .Vcc(Vcc), ._13(not_2_out), ._12(DSP[2]), ._11(B2), ._10(not_2_out), ._9(DSP[3]), ._8(B3),
    ._1(not_2_out), ._2(DSP[1]), ._3(B1), ._4(not_2_out), ._5(DSP[0]), ._6(B0), .GND(GND));
endmodule

// CC
module Controller_Counter (
  input  CLK,
  input  CLR,
  output B0,
  output B1,
  output B2
);

  wire and_1_out, j_k_ff_1_qn, j_k_ff_2_qn, not_1_out, or_1_out;

  or or_1 (or_1_out, CLR, and_1_out);
  and and_1 (and_1_out, B2, B1);
  not not_1 (not_1_out, CLK);
  J_K_Flip_Flop #(.enable("true")) j_k_ff_1 (
    .J(1'b1), .clk(not_1_out), .K(1'b1), .Q(B0), .Qn(j_k_ff_1_qn), .reset(or_1_out));  // open: preset, en
  J_K_Flip_Flop #(.enable("true")) j_k_ff_2 (
    .J(1'b1), .clk(j_k_ff_1_qn), .K(1'b1), .Q(B1), .Qn(j_k_ff_2_qn), .reset(or_1_out));  // open: preset, en
  J_K_Flip_Flop #(.enable("true")) j_k_ff_3 (
    .J(1'b1), .clk(j_k_ff_2_qn), .K(1'b1), .Q(B2), .reset(or_1_out));  // open: Qn, preset, en
endmodule

// REGISTER A
module A_Register (
  input  GND,
  input  Vcc,
  input  I0,
  input  I1,
  input  I2,
  input  I3,
  input  I4,
  input  I5,
  input  I6,
  input  I7,
  input  CLK,
  input  CLR,
  input  AI,
  input  AO,
  output [7:0] DSP,
  output O0,
  output O1,
  output O2,
  output O3,
  output O4,
  output O5,
  output O6,
  output O7
);

  wire not_1_out;

  Pull_Resistor pull_resistor_1 (.node(I7));
  Pull_Resistor pull_resistor_2 (.node(I5));
  Pull_Resistor pull_resistor_3 (.node(I1));
  Pull_Resistor pull_resistor_4 (.node(I3));
  Pull_Resistor pull_resistor_5 (.node(I6));
  Pull_Resistor pull_resistor_6 (.node(I2));
  Pull_Resistor pull_resistor_7 (.node(I4));
  Pull_Resistor pull_resistor_8 (.node(I0));
  Register #(.width(4), .Select("low")) register_1 (.D({I3, I2, I1, I0}), .en(AI), .Q(DSP[3:0]), .clk(CLK), .clr(CLR));
  Register #(.width(4), .Select("low")) register_2 (.D({I7, I6, I5, I4}), .en(AI), .Q(DSP[7:4]), .clk(CLK), .clr(CLR));
  not not_1 (not_1_out, AO);
  Pull_Resistor pull_resistor_9 (.node(AO));
  Pull_Resistor pull_resistor_10 (.node(AI));
  Pull_Resistor pull_resistor_11 (.node(CLR));
  Pull_Resistor pull_resistor_12 (.node(CLK));
  _74125 u_74125_1 (
    .Vcc(Vcc), ._13(not_1_out), ._12(DSP[3]), ._11(O3), ._10(not_1_out), ._9(DSP[2]), ._8(O2),
    ._1(not_1_out), ._2(DSP[4]), ._3(O4), ._4(not_1_out), ._5(DSP[5]), ._6(O5), .GND(GND));
  _74125 u_74125_2 (
    .Vcc(Vcc), ._13(not_1_out), ._12(DSP[1]), ._11(O1), ._10(not_1_out), ._9(DSP[0]), ._8(O0),
    ._1(not_1_out), ._2(DSP[6]), ._3(O6), ._4(not_1_out), ._5(DSP[7]), ._6(O7), .GND(GND));
  Pull_Resistor pull_resistor_13 (.node(O6));
  Pull_Resistor pull_resistor_14 (.node(O4));
  Pull_Resistor pull_resistor_15 (.node(O2));
  Pull_Resistor pull_resistor_16 (.node(O3));
  Pull_Resistor pull_resistor_17 (.node(O5));
  Pull_Resistor pull_resistor_18 (.node(O7));
  Pull_Resistor pull_resistor_19 (.node(O1));
  Pull_Resistor pull_resistor_20 (.node(O0));
endmodule

// REGISTER B
module B_Register (
  input  GND,
  input  Vcc,
  input  I0,
  input  I1,
  input  I2,
  input  I3,
  input  I4,
  input  I5,
  input  I6,
  input  I7,
  input  CLK,
  input  CLR,
  input  BI,
  input  BO,
  output [7:0] DSP,
  output O0,
  output O1,
  output O2,
  output O3,
  output O4,
  output O5,
  output O6,
  output O7
);

  wire not_1_out;

  Pull_Resistor pull_resistor_1 (.node(I2));
  Pull_Resistor pull_resistor_2 (.node(I1));
  Pull_Resistor pull_resistor_3 (.node(I3));
  Pull_Resistor pull_resistor_4 (.node(I6));
  Pull_Resistor pull_resistor_5 (.node(I5));
  Pull_Resistor pull_resistor_6 (.node(I4));
  Pull_Resistor pull_resistor_7 (.node(I7));
  Pull_Resistor pull_resistor_8 (.node(I0));
  Register #(.width(4), .Select("low")) register_1 (.D({I3, I2, I1, I0}), .en(BI), .Q(DSP[3:0]), .clk(CLK), .clr(CLR));
  Register #(.width(4), .Select("low")) register_2 (.D({I7, I6, I5, I4}), .en(BI), .Q(DSP[7:4]), .clk(CLK), .clr(CLR));
  not not_1 (not_1_out, BO);
  Pull_Resistor pull_resistor_9 (.node(BO));
  Pull_Resistor pull_resistor_10 (.node(BI));
  Pull_Resistor pull_resistor_11 (.node(CLR));
  Pull_Resistor pull_resistor_12 (.node(CLK));
  _74125 u_74125_1 (
    .Vcc(Vcc), ._13(not_1_out), ._12(DSP[3]), ._11(O3), ._10(not_1_out), ._9(DSP[2]), ._8(O2),
    ._1(not_1_out), ._2(DSP[4]), ._3(O4), ._4(not_1_out), ._5(DSP[5]), ._6(O5), .GND(GND));
  _74125 u_74125_2 (
    .Vcc(Vcc), ._13(not_1_out), ._12(DSP[1]), ._11(O1), ._10(not_1_out), ._9(DSP[0]), ._8(O0),
    ._1(not_1_out), ._2(DSP[6]), ._3(O6), ._4(not_1_out), ._5(DSP[7]), ._6(O7), .GND(GND));
  Pull_Resistor pull_resistor_13 (.node(O5));
  Pull_Resistor pull_resistor_14 (.node(O6));
  Pull_Resistor pull_resistor_15 (.node(O1));
  Pull_Resistor pull_resistor_16 (.node(O3));
  Pull_Resistor pull_resistor_17 (.node(O7));
  Pull_Resistor pull_resistor_18 (.node(O4));
  Pull_Resistor pull_resistor_19 (.node(O2));
  Pull_Resistor pull_resistor_20 (.node(O0));
endmodule

// MAR
module Mem_Address_Register (
  input  I0,
  input  I1,
  input  I2,
  input  I3,
  input  CLK,
  input  CLR,
  input  MI,
  input  Vcc,
  input  GND,
  output [3:0] DSP,
  output O0,
  output O1,
  output O2,
  output O3
);

  Pull_Resistor pull_resistor_1 (.node(CLK));
  Pull_Resistor pull_resistor_2 (.node(I1));
  Pull_Resistor pull_resistor_3 (.node(I2));
  Pull_Resistor pull_resistor_4 (.node(I3));
  Pull_Resistor pull_resistor_5 (.node(I0));
  Pull_Resistor pull_resistor_6 (.node(MI));
  Pull_Resistor pull_resistor_7 (.node(CLR));
  Register #(.width(4), .Select("low")) register_1 (.D({I3, I2, I1, I0}), .en(MI), .Q(DSP), .clk(CLK), .clr(CLR));
  Pull_Resistor pull_resistor_8 (.node(DSP[3]));
  Pull_Resistor pull_resistor_9 (.node(DSP[1]));
  Pull_Resistor pull_resistor_10 (.node(DSP[0]));
  Pull_Resistor pull_resistor_11 (.node(DSP[2]));

  assign O0 = DSP[0];
  assign O1 = DSP[1];
  assign O2 = DSP[2];
  assign O3 = DSP[3];
endmodule

// INSTRUCT REG
module Instruction_Register (
  input  GND,
  input  Vcc,
  input  I0,
  input  I1,
  input  I2,
  input  I3,
  input  I4,
  input  I5,
  input  I6,
  input  I7,
  input  CLK,
  input  CLR,
  input  II,
  input  IO,
  output [7:0] DSP,
  output O0,
  output O1,
  output O2,
  output O3,
  output O4,
  output O5,
  output O6,
  output O7
);

  wire not_1_out;

  Pull_Resistor pull_resistor_1 (.node(I7));
  Pull_Resistor pull_resistor_2 (.node(I3));
  Pull_Resistor pull_resistor_3 (.node(I4));
  Pull_Resistor pull_resistor_4 (.node(I2));
  Pull_Resistor pull_resistor_5 (.node(I6));
  Pull_Resistor pull_resistor_6 (.node(I5));
  Pull_Resistor pull_resistor_7 (.node(I0));
  Pull_Resistor pull_resistor_8 (.node(I1));
  Pull_Resistor pull_resistor_9 (.node(II));
  Pull_Resistor pull_resistor_10 (.node(CLK));
  Pull_Resistor pull_resistor_11 (.node(CLR));
  Register #(.width(4), .Select("low")) register_1 (.D({I3, I2, I1, I0}), .en(II), .Q(DSP[3:0]), .clk(CLK), .clr(CLR));
  Register #(.width(4), .Select("low")) register_2 (.D({I7, I6, I5, I4}), .en(II), .Q(DSP[7:4]), .clk(CLK), .clr(CLR));
  not not_1 (not_1_out, IO);
  Pull_Resistor pull_resistor_12 (.node(IO));
  _74125 u_74125_1 (
    .Vcc(Vcc), ._13(not_1_out), ._12(DSP[3]), ._11(O3), ._10(not_1_out), ._9(DSP[2]), ._8(O2),
    ._1(not_1_out), ._4(not_1_out), .GND(GND));  // open: _2, _3, _5, _6
  _74125 u_74125_2 (
    .Vcc(Vcc), ._13(not_1_out), ._12(DSP[1]), ._11(O1), ._10(not_1_out), ._9(DSP[0]), ._8(O0),
    ._1(not_1_out), ._4(not_1_out), .GND(GND));  // open: _2, _3, _5, _6
  Pull_Resistor pull_resistor_13 (.node(DSP[7]));
  Pull_Resistor pull_resistor_14 (.node(DSP[4]));
  Pull_Resistor pull_resistor_15 (.node(DSP[5]));
  Pull_Resistor pull_resistor_16 (.node(DSP[6]));

  assign O4 = DSP[4];
  assign O5 = DSP[5];
  assign O6 = DSP[6];
  assign O7 = DSP[7];
endmodule

// OUTPUT REG
module Output_Register (
  input  GND,
  input  Vcc,
  input  I0,
  input  I1,
  input  I2,
  input  I3,
  input  I4,
  input  I5,
  input  I6,
  input  I7,
  input  CLK,
  input  CLR,
  input  OI,
  output O0,
  output O1,
  output O2,
  output O3,
  output O4,
  output O5,
  output O6,
  output O7
);

  wire not_1_out;
  wire [3:0] register_1_q, register_2_q;

  Pull_Resistor pull_resistor_1 (.node(I3));
  Pull_Resistor pull_resistor_2 (.node(I4));
  Pull_Resistor pull_resistor_3 (.node(I5));
  Pull_Resistor pull_resistor_4 (.node(I0));
  Pull_Resistor pull_resistor_5 (.node(I6));
  Pull_Resistor pull_resistor_6 (.node(I7));
  Pull_Resistor pull_resistor_7 (.node(I1));
  Pull_Resistor pull_resistor_8 (.node(I2));
  Register #(.width(4), .Select("low")) register_1 (
    .D({I3, I2, I1, I0}), .en(OI), .Q(register_1_q), .clk(CLK), .clr(CLR));
  Register #(.width(4), .Select("low")) register_2 (
    .D({I7, I6, I5, I4}), .en(OI), .Q(register_2_q), .clk(CLK), .clr(CLR));
  not not_1 (not_1_out, 1'b1);
  Pull_Resistor pull_resistor_9 (.node(CLR));
  Pull_Resistor pull_resistor_10 (.node(OI));
  Pull_Resistor pull_resistor_11 (.node(CLK));
  _74125 u_74125_1 (
    .Vcc(Vcc), ._13(not_1_out), ._12(register_1_q[3]), ._11(O3), ._10(not_1_out), ._9(register_1_q[2]),
    ._8(O2), ._1(not_1_out), ._2(register_2_q[0]), ._3(O4), ._4(not_1_out), ._5(register_2_q[1]), ._6(O5),
    .GND(GND));
  _74125 u_74125_2 (
    .Vcc(Vcc), ._13(not_1_out), ._12(register_1_q[1]), ._11(O1), ._10(not_1_out), ._9(register_1_q[0]),
    ._8(O0), ._1(not_1_out), ._2(register_2_q[2]), ._3(O6), ._4(not_1_out), ._5(register_2_q[3]), ._6(O7),
    .GND(GND));
  Pull_Resistor pull_resistor_12 (.node(O4));
  Pull_Resistor pull_resistor_13 (.node(O5));
  Pull_Resistor pull_resistor_14 (.node(O7));
  Pull_Resistor pull_resistor_15 (.node(O6));
  Pull_Resistor pull_resistor_16 (.node(O3));
  Pull_Resistor pull_resistor_17 (.node(O1));
  Pull_Resistor pull_resistor_18 (.node(O0));
  Pull_Resistor pull_resistor_19 (.node(O2));
endmodule

// FLAG REG
module Flag_Register (
  input  ZFI,
  input  CFI,
  input  CLK,
  input  CLR,
  input  FI,
  input  Vcc,
  input  GND,
  output [1:0] DSP,
  output ZF,
  output CF
);

  Pull_Resistor pull_resistor_1 (.node(CLK));
  Pull_Resistor pull_resistor_2 (.node(ZFI));
  Pull_Resistor pull_resistor_3 (.node(CFI));
  Pull_Resistor pull_resistor_4 (.node(CLR));
  Pull_Resistor pull_resistor_5 (.node(FI));
  Register #(.width(2), .Select("low")) register_1 (.D({CFI, ZFI}), .en(FI), .Q({CF, DSP[0]}), .clk(CLK), .clr(CLR));
  Pull_Resistor pull_resistor_6 (.node(CF));
  Pull_Resistor pull_resistor_7 (.node(DSP[0]));

  assign DSP[1] = CF;
  assign ZF = DSP[0];
endmodule

module RAM_Register (
  input  I0,
  input  I1,
  input  I2,
  input  I3,
  input  I4,
  input  I5,
  input  I6,
  input  I7,
  input  SL,
  input  CLR,
  output O0,
  output O1,
  output O2,
  output O3,
  output O4,
  output O5,
  output O6,
  output O7
);

  wire not_1_out;
  wire [7:0] register_1_q;

  Register #(.trigger("high"), .Select("low")) register_1 (
    .D({I7, I6, I5, I4, I3, I2, I1, I0}), .en(SL), .Q(register_1_q), .clk(1'b1), .clr(CLR));
  not not_1 (not_1_out, SL);
  _74125 u_74125_1 (
    ._13(not_1_out), ._12(register_1_q[3]), ._11(O3), ._10(not_1_out), ._9(register_1_q[2]), ._8(O2),
    ._1(not_1_out), ._2(register_1_q[4]), ._3(O4), ._4(not_1_out), ._5(register_1_q[5]), ._6(O5));  // open: Vcc, GND
  _74125 u_74125_2 (
    ._13(not_1_out), ._12(register_1_q[1]), ._11(O1), ._10(not_1_out), ._9(register_1_q[0]), ._8(O0),
    ._1(not_1_out), ._2(register_1_q[6]), ._3(O6), ._4(not_1_out), ._5(register_1_q[7]), ._6(O7));  // open: Vcc, GND
endmodule

// CONTROLLER
module Controller (
  input  I3,
  input  I2,
  input  I1,
  input  I0,
  input  CF,
  input  ZF,
  input  C2,
  input  C1,
  input  C0,
  output HLT,
  output MI,
  output RI,
  output RO,
  output IO,
  output II,
  output AI,
  output AO,
  output EO,
  output SU,
  output BI,
  output BO,
  output OI,
  output CE,
  output CO,
  output J,
  output FI
);

  wire and_2_out, and_3_out, and_4_out, and_5_out, and_7_out, and_8_out, and_9_out, and_10_out, and_11_out,
       and_12_out, and_13_out, and_14_out, and_16_out, and_17_out, and_18_out, and_19_out, and_20_out,
       and_21_out, and_22_out, and_23_out, and_24_out, and_31_out, and_32_out, and_33_out, not_1_out,
       not_2_out, not_3_out, not_4_out, not_5_out, not_6_out, not_7_out, not_8_out, not_9_out, not_10_out,
       not_11_out, not_12_out, not_13_out, not_14_out, not_15_out, not_16_out, not_17_out, not_18_out,
       not_19_out, not_20_out, not_21_out, not_22_out, not_23_out, not_24_out, not_25_out, not_26_out,
       not_27_out, not_28_out, not_29_out, not_30_out, not_31_out, not_32_out, not_33_out, not_34_out,
       not_35_out, not_36_out, not_37_out, not_38_out, not_39_out, not_40_out, not_41_out, not_42_out,
       not_43_out, not_44_out, not_45_out, not_46_out, not_47_out, not_48_out, not_49_out, not_50_out,
       not_51_out, not_52_out, not_53_out, not_54_out, not_55_out, not_56_out, not_57_out, not_58_out,
       not_59_out, not_60_out, not_61_out, not_62_out, not_63_out, not_64_out, not_65_out, not_66_out,
       not_67_out, not_68_out, not_69_out, not_70_out, not_71_out, not_72_out, not_73_out, not_74_out,
       not_75_out, not_76_out, not_77_out, not_78_out, not_79_out, not_80_out, not_81_out, not_82_out,
       not_83_out, not_84_out, not_85_out, not_86_out, not_87_out, not_88_out, not_89_out, not_90_out,
       not_91_out, not_92_out, not_93_out, not_94_out, not_95_out, not_96_out, not_97_out, not_98_out,
       not_99_out, not_100_out, not_101_out, not_102_out, not_103_out, not_104_out, not_105_out, not_106_out,
       not_107_out, not_108_out, not_109_out, not_110_out, not_111_out, not_112_out, not_113_out,
       not_114_out, not_115_out, not_116_out, not_117_out;

  not not_1 (not_1_out, C2);
  not not_2 (not_2_out, C0);
  not not_3 (not_3_out, C2);
  not not_4 (not_4_out, C1);
  not not_5 (not_5_out, C0);
  not not_6 (not_6_out, I3);
  not not_7 (not_7_out, I2);
  not not_8 (not_8_out, C2);
  not not_9 (not_9_out, C0);
  not not_10 (not_10_out, I3);
  not not_11 (not_11_out, I2);
  not not_12 (not_12_out, C2);
  not not_13 (not_13_out, C0);
  not not_14 (not_14_out, I3);
  not not_15 (not_15_out, I1);
  not not_16 (not_16_out, I0);
  not not_17 (not_17_out, C2);
  not not_18 (not_18_out, C0);
  not not_19 (not_19_out, I3);
  not not_20 (not_20_out, I1);
  not not_21 (not_21_out, I0);
  not not_22 (not_22_out, C2);
  not not_23 (not_23_out, C2);
  not not_24 (not_24_out, C1);
  not not_25 (not_25_out, I3);
  not not_26 (not_26_out, I2);
  not not_27 (not_27_out, C2);
  not not_28 (not_28_out, I3);
  not not_29 (not_29_out, I2);
  not not_30 (not_30_out, C2);
  not not_31 (not_31_out, I3);
  not not_32 (not_32_out, I1);
  not not_33 (not_33_out, C2);
  not not_34 (not_34_out, C0);
  not not_35 (not_35_out, I3);
  not not_36 (not_36_out, I2);
  not not_37 (not_37_out, C2);
  not not_38 (not_38_out, C0);
  not not_39 (not_39_out, I3);
  not not_40 (not_40_out, I0);
  not not_41 (not_41_out, C2);
  not not_42 (not_42_out, C0);
  not not_43 (not_43_out, I3);
  not not_44 (not_44_out, C2);
  not not_45 (not_45_out, I2);
  not not_46 (not_46_out, I1);
  not not_47 (not_47_out, I0);
  not not_48 (not_48_out, C2);
  not not_49 (not_49_out, C2);
  not not_50 (not_50_out, C1);
  not not_51 (not_51_out, I3);
  not not_52 (not_52_out, I2);
  not not_53 (not_53_out, I1);
  not not_54 (not_54_out, C2);
  not not_55 (not_55_out, I3);
  not not_56 (not_56_out, I2);
  not not_57 (not_57_out, C1);
  not not_58 (not_58_out, C0);
  not not_59 (not_59_out, I3);
  not not_60 (not_60_out, I1);
  not not_61 (not_61_out, C2);
  not not_62 (not_62_out, C0);
  not not_63 (not_63_out, I3);
  not not_64 (not_64_out, I2);
  not not_65 (not_65_out, C1);
  not not_66 (not_66_out, C0);
  not not_67 (not_67_out, I3);
  not not_68 (not_68_out, I1);
  not not_69 (not_69_out, I0);
  not not_70 (not_70_out, C2);
  not not_71 (not_71_out, I0);
  not not_72 (not_72_out, C2);
  not not_73 (not_73_out, C0);
  not not_74 (not_74_out, I3);
  not not_75 (not_75_out, I2);
  not not_76 (not_76_out, C1);
  not not_77 (not_77_out, C0);
  not not_78 (not_78_out, I3);
  not not_79 (not_79_out, I1);
  not not_80 (not_80_out, I0);
  not not_81 (not_81_out, C2);
  not not_82 (not_82_out, I0);
  not not_83 (not_83_out, C2);
  not not_84 (not_84_out, C0);
  not not_85 (not_85_out, I3);
  not not_86 (not_86_out, I2);
  not not_87 (not_87_out, C1);
  not not_88 (not_88_out, C0);
  not not_89 (not_89_out, I3);
  not not_90 (not_90_out, I2);
  not not_91 (not_91_out, C2);
  not not_92 (not_92_out, I3);
  not not_93 (not_93_out, I2);
  not not_94 (not_94_out, C1);
  not not_95 (not_95_out, C0);
  not not_96 (not_96_out, I0);
  not not_97 (not_97_out, C2);
  not not_98 (not_98_out, C0);
  not not_99 (not_99_out, C2);
  not not_100 (not_100_out, C1);
  not not_101 (not_101_out, C2);
  not not_102 (not_102_out, C1);
  not not_103 (not_103_out, C0);
  not not_104 (not_104_out, I3);
  not not_105 (not_105_out, I0);
  not not_106 (not_106_out, C2);
  not not_107 (not_107_out, C0);
  not not_108 (not_108_out, I3);
  not not_109 (not_109_out, C2);
  not not_110 (not_110_out, I2);
  not not_111 (not_111_out, I1);
  not not_112 (not_112_out, I0);
  not not_113 (not_113_out, C2);
  not not_114 (not_114_out, I3);
  not not_115 (not_115_out, I2);
  not not_116 (not_116_out, C1);
  not not_117 (not_117_out, C0);
  and and_1 (HLT, I3, I2, I1, I0, not_1_out, C1, not_2_out);
  and and_2 (and_2_out, not_3_out, not_4_out, not_5_out);
  and and_3 (and_3_out, not_6_out, not_7_out, I0, not_8_out, not_9_out);
  and and_4 (and_4_out, not_10_out, not_11_out, I1, not_12_out, not_13_out);
  and and_5 (and_5_out, not_14_out, I2, not_15_out, not_16_out, not_17_out, not_18_out);
  and and_6 (RI, not_19_out, I2, not_20_out, not_21_out, not_22_out, C1, C0);
  and and_7 (and_7_out, not_23_out, not_24_out, C0);
  and and_8 (and_8_out, not_25_out, not_26_out, I0, not_27_out, C0);
  and and_9 (and_9_out, not_28_out, not_29_out, I1, not_30_out, C0);
  and and_10 (and_10_out, not_31_out, not_32_out, I0, not_33_out, C1, not_34_out);
  and and_11 (and_11_out, not_35_out, not_36_out, I1, not_37_out, C1, not_38_out);
  and and_12 (and_12_out, not_39_out, I2, not_40_out, not_41_out, C1, not_42_out);
  and and_13 (and_13_out, not_43_out, I2, I1, I0, CF, not_44_out, C1, C0);
  and and_14 (and_14_out, I3, not_45_out, not_46_out, not_47_out, ZF, not_48_out, C1, C0);
  and and_15 (II, not_49_out, not_50_out, C0);
  and and_16 (and_16_out, not_51_out, not_52_out, not_53_out, I0, not_54_out, C1, C0);
  and and_17 (and_17_out, not_55_out, not_56_out, I1, C2, not_57_out, not_58_out);
  and and_18 (and_18_out, not_59_out, I2, not_60_out, I0, not_61_out, C1, not_62_out);
  and and_19 (and_19_out, not_63_out, not_64_out, I1, C2, not_65_out, not_66_out);
  and and_20 (and_20_out, not_67_out, I2, not_68_out, not_69_out, not_70_out, C1, C0);
  and and_21 (and_21_out, I3, I2, I1, not_71_out, not_72_out, C1, not_73_out);
  and and_22 (and_22_out, not_74_out, not_75_out, I1, C2, not_76_out, not_77_out);
  and and_23 (and_23_out, not_78_out, I2, not_79_out, not_80_out, not_81_out, C1, C0);
  and and_24 (and_24_out, I3, I2, I1, not_82_out, not_83_out, C1, not_84_out);
  and and_25 (SU, not_85_out, not_86_out, I1, I0, C2, not_87_out, not_88_out);
  and and_26 (BI, not_89_out, not_90_out, I1, not_91_out, C1, C0);
  and and_27 (BO, not_92_out, not_93_out, I1, C2, not_94_out, not_95_out);
  and and_28 (OI, I3, I2, I1, not_96_out, not_97_out, C1, not_98_out);
  and and_29 (CE, not_99_out, not_100_out, C0);
  and and_30 (CO, not_101_out, not_102_out, not_103_out);
  and and_31 (and_31_out, not_104_out, I2, I1, not_105_out, not_106_out, C1, not_107_out);
  and and_32 (and_32_out, not_108_out, I2, I1, I0, CF, not_109_out, C1, C0);
  and and_33 (and_33_out, I3, not_110_out, not_111_out, not_112_out, ZF, not_113_out, C1, C0);
  and and_34 (FI, not_114_out, not_115_out, I1, C2, not_116_out, not_117_out);
  or or_1 (MI, and_2_out, and_3_out, and_4_out, and_5_out);
  or or_2 (RO, and_7_out, and_8_out, and_9_out);
  or or_3 (IO, and_10_out, and_11_out, and_12_out, and_13_out, and_14_out);
  or or_4 (AI, and_16_out, and_17_out, and_18_out);
  or or_5 (AO, and_19_out, and_20_out, and_21_out);
  or or_6 (EO, and_22_out, and_23_out, and_24_out);
  or or_7 (J, and_31_out, and_32_out, and_33_out);
endmodule

module ALU (
  input  A7,
  input  A6,
  input  A5,
  input  A4,
  input  A3,
  input  A2,
  input  A1,
  input  A0,
  input  Vcc,
  input  GND,
  input  SU,
  input  E0,
  input  B7,
  input  B6,
  input  B5,
  input  B4,
  input  B3,
  input  B2,
  input  B1,
  input  B0,
  output [7:0] DSP,
  output JC,
  output X7,
  output X6,
  output X5,
  output X4,
  output X3,
  output X2,
  output X1,
  output X0
);

  wire n74283_1_pin3, n74283_1_pin6, n74283_1_pin7, n74283_1_pin11, n74283_1_pin15, n74283_2_pin2,
       n74283_2_pin6, n74283_2_pin11, n74283_2_pin15, not_1_out;

  _74125 u_74125_1 (
    .Vcc(Vcc), ._13(not_1_out), ._12(DSP[6]), ._11(X6), ._10(not_1_out), ._9(DSP[7]), ._8(X7),
    ._1(not_1_out), ._2(DSP[5]), ._3(X5), ._4(not_1_out), ._5(DSP[4]), ._6(X4), .GND(GND));
  _74125 u_74125_2 (
    .Vcc(Vcc), ._13(not_1_out), ._12(DSP[2]), ._11(X2), ._10(not_1_out), ._9(DSP[3]), ._8(X3),
    ._1(not_1_out), ._2(DSP[1]), ._3(X1), ._4(not_1_out), ._5(DSP[0]), ._6(X0), .GND(GND));
  _74283 #(.VccGndPorts("true")) u_74283_1 (
    .pin1(DSP[5]), .pin2(A5), .pin3(n74283_1_pin3), .pin4(DSP[4]), .pin5(A4), .pin6(n74283_1_pin6),
    .pin7(n74283_1_pin7), .pin8(GND), .pin16(Vcc), .pin15(n74283_1_pin15), .pin14(A6), .pin13(DSP[6]),
    .pin12(A7), .pin11(n74283_1_pin11), .pin10(DSP[7]), .pin9(JC));
  Pull_Resistor pull_resistor_1 (.node(A0));
  _74283 #(.VccGndPorts("true")) u_74283_2 (
    .pin1(DSP[1]), .pin2(n74283_2_pin2), .pin3(A1), .pin4(DSP[0]), .pin5(A0), .pin6(n74283_2_pin6),
    .pin7(SU), .pin8(GND), .pin16(Vcc), .pin15(n74283_2_pin15), .pin14(A2), .pin13(DSP[2]), .pin12(A3),
    .pin11(n74283_2_pin11), .pin10(DSP[3]), .pin9(n74283_1_pin7));
  Pull_Resistor pull_resistor_2 (.node(A1));
  Pull_Resistor pull_resistor_3 (.node(A3));
  Pull_Resistor pull_resistor_4 (.node(A6));
  Pull_Resistor pull_resistor_5 (.node(A7));
  Pull_Resistor pull_resistor_6 (.node(A4));
  Pull_Resistor pull_resistor_7 (.node(A5));
  Pull_Resistor pull_resistor_8 (.node(A2));
  _7486 #(.VccGndPorts("true")) u_7486_1 (
    .pin1(SU), .pin2(B3), .pin3(n74283_2_pin11), .pin4(SU), .pin5(B2), .pin6(n74283_2_pin15), .pin7(GND),
    .pin14(Vcc), .pin13(B4), .pin12(SU), .pin11(n74283_1_pin6), .pin10(B5), .pin9(SU), .pin8(n74283_1_pin3));
  _7486 #(.VccGndPorts("true")) u_7486_2 (
    .pin1(SU), .pin2(B1), .pin3(n74283_2_pin2), .pin4(SU), .pin5(B0), .pin6(n74283_2_pin6), .pin7(GND),
    .pin14(Vcc), .pin13(B6), .pin12(SU), .pin11(n74283_1_pin15), .pin10(B7), .pin9(SU), .pin8(n74283_1_pin11));
  Pull_Resistor pull_resistor_9 (.node(B0));
  Pull_Resistor pull_resistor_10 (.node(B3));
  Pull_Resistor pull_resistor_11 (.node(B5));
  Pull_Resistor pull_resistor_12 (.node(B2));
  Pull_Resistor pull_resistor_13 (.node(B1));
  Pull_Resistor pull_resistor_14 (.node(B6));
  Pull_Resistor pull_resistor_15 (.node(B4));
  Pull_Resistor pull_resistor_16 (.node(B7));
  not not_1 (not_1_out, E0);
  Pull_Resistor pull_resistor_17 (.node(SU));
  Pull_Resistor pull_resistor_18 (.node(E0));
endmodule

module RAM (
  input  A3,
  input  A2,
  input  A1,
  input  A0,
  input  D0,
  input  D1,
  input  D2,
  input  D3,
  input  D4,
  input  D5,
  input  D6,
  input  D7,
  input  Vcc,
  input  GND,
  input  RI,
  input  RO,
  input  CLR,
  output O0,
  output O1,
  output O2,
  output O3,
  output O4,
  output O5,
  output O6,
  output O7,
  output [7:0] DSP
);

  wire address_decoder_1_en0, address_decoder_1_en1, address_decoder_1_en2, address_decoder_1_en3,
       address_decoder_1_en4, address_decoder_1_en5, address_decoder_1_en6, address_decoder_1_en7,
       address_decoder_1_en8, address_decoder_1_en9, address_decoder_1_en10, address_decoder_1_en11,
       address_decoder_1_en12, address_decoder_1_en13, address_decoder_1_en14, address_decoder_1_en15,
       n74125_1__3, n74125_1__6, n74125_1__8, n74125_1__11, n74125_2__3, n74125_2__6, n74125_2__8,
       n74125_2__11, not_1_out, not_2_out;

  RAM_Register ram_register_1 (
    .I0(n74125_2__8), .I1(n74125_2__11), .I2(n74125_1__8), .I3(n74125_1__11), .I4(n74125_1__3),
    .I5(n74125_1__6), .I6(n74125_2__3), .I7(n74125_2__6), .O0(DSP[0]), .O1(DSP[1]), .O2(DSP[2]), .O3(DSP[3]),
    .O4(DSP[4]), .O5(DSP[5]), .O6(DSP[6]), .O7(DSP[7]), .SL(address_decoder_1_en15), .CLR(CLR));
  RAM_Register ram_register_2 (
    .I0(n74125_2__8), .I1(n74125_2__11), .I2(n74125_1__8), .I3(n74125_1__11), .I4(n74125_1__3),
    .I5(n74125_1__6), .I6(n74125_2__3), .I7(n74125_2__6), .O0(DSP[0]), .O1(DSP[1]), .O2(DSP[2]), .O3(DSP[3]),
    .O4(DSP[4]), .O5(DSP[5]), .O6(DSP[6]), .O7(DSP[7]), .SL(address_decoder_1_en14), .CLR(CLR));
  RAM_Register ram_register_3 (
    .I0(n74125_2__8), .I1(n74125_2__11), .I2(n74125_1__8), .I3(n74125_1__11), .I4(n74125_1__3),
    .I5(n74125_1__6), .I6(n74125_2__3), .I7(n74125_2__6), .O0(DSP[0]), .O1(DSP[1]), .O2(DSP[2]), .O3(DSP[3]),
    .O4(DSP[4]), .O5(DSP[5]), .O6(DSP[6]), .O7(DSP[7]), .SL(address_decoder_1_en13), .CLR(CLR));
  RAM_Register ram_register_4 (
    .I0(n74125_2__8), .I1(n74125_2__11), .I2(n74125_1__8), .I3(n74125_1__11), .I4(n74125_1__3),
    .I5(n74125_1__6), .I6(n74125_2__3), .I7(n74125_2__6), .O0(DSP[0]), .O1(DSP[1]), .O2(DSP[2]), .O3(DSP[3]),
    .O4(DSP[4]), .O5(DSP[5]), .O6(DSP[6]), .O7(DSP[7]), .SL(address_decoder_1_en12), .CLR(CLR));
  RAM_Register ram_register_5 (
    .I0(n74125_2__8), .I1(n74125_2__11), .I2(n74125_1__8), .I3(n74125_1__11), .I4(n74125_1__3),
    .I5(n74125_1__6), .I6(n74125_2__3), .I7(n74125_2__6), .O0(DSP[0]), .O1(DSP[1]), .O2(DSP[2]), .O3(DSP[3]),
    .O4(DSP[4]), .O5(DSP[5]), .O6(DSP[6]), .O7(DSP[7]), .SL(address_decoder_1_en11), .CLR(CLR));
  RAM_Register ram_register_6 (
    .I0(n74125_2__8), .I1(n74125_2__11), .I2(n74125_1__8), .I3(n74125_1__11), .I4(n74125_1__3),
    .I5(n74125_1__6), .I6(n74125_2__3), .I7(n74125_2__6), .O0(DSP[0]), .O1(DSP[1]), .O2(DSP[2]), .O3(DSP[3]),
    .O4(DSP[4]), .O5(DSP[5]), .O6(DSP[6]), .O7(DSP[7]), .SL(address_decoder_1_en10), .CLR(CLR));
  RAM_Register ram_register_7 (
    .I0(n74125_2__8), .I1(n74125_2__11), .I2(n74125_1__8), .I3(n74125_1__11), .I4(n74125_1__3),
    .I5(n74125_1__6), .I6(n74125_2__3), .I7(n74125_2__6), .O0(DSP[0]), .O1(DSP[1]), .O2(DSP[2]), .O3(DSP[3]),
    .O4(DSP[4]), .O5(DSP[5]), .O6(DSP[6]), .O7(DSP[7]), .SL(address_decoder_1_en9), .CLR(CLR));
  RAM_Register ram_register_8 (
    .I0(n74125_2__8), .I1(n74125_2__11), .I2(n74125_1__8), .I3(n74125_1__11), .I4(n74125_1__3),
    .I5(n74125_1__6), .I6(n74125_2__3), .I7(n74125_2__6), .O0(DSP[0]), .O1(DSP[1]), .O2(DSP[2]), .O3(DSP[3]),
    .O4(DSP[4]), .O5(DSP[5]), .O6(DSP[6]), .O7(DSP[7]), .SL(address_decoder_1_en8), .CLR(CLR));
  Address_Decoder address_decoder_1 (
    .A3(A3), .A2(A2), .A1(A1), .A0(A0), .EN0(address_decoder_1_en0), .EN1(address_decoder_1_en1),
    .EN2(address_decoder_1_en2), .EN3(address_decoder_1_en3), .EN4(address_decoder_1_en4),
    .EN5(address_decoder_1_en5), .EN6(address_decoder_1_en6), .EN7(address_decoder_1_en7),
    .EN8(address_decoder_1_en8), .EN9(address_decoder_1_en9), .EN10(address_decoder_1_en10),
    .EN11(address_decoder_1_en11), .EN12(address_decoder_1_en12), .EN13(address_decoder_1_en13),
    .EN14(address_decoder_1_en14), .EN15(address_decoder_1_en15));
  RAM_Register ram_register_9 (
    .I0(n74125_2__8), .I1(n74125_2__11), .I2(n74125_1__8), .I3(n74125_1__11), .I4(n74125_1__3),
    .I5(n74125_1__6), .I6(n74125_2__3), .I7(n74125_2__6), .O0(DSP[0]), .O1(DSP[1]), .O2(DSP[2]), .O3(DSP[3]),
    .O4(DSP[4]), .O5(DSP[5]), .O6(DSP[6]), .O7(DSP[7]), .SL(address_decoder_1_en0), .CLR(CLR));
  RAM_Register ram_register_10 (
    .I0(n74125_2__8), .I1(n74125_2__11), .I2(n74125_1__8), .I3(n74125_1__11), .I4(n74125_1__3),
    .I5(n74125_1__6), .I6(n74125_2__3), .I7(n74125_2__6), .O0(DSP[0]), .O1(DSP[1]), .O2(DSP[2]), .O3(DSP[3]),
    .O4(DSP[4]), .O5(DSP[5]), .O6(DSP[6]), .O7(DSP[7]), .SL(address_decoder_1_en1), .CLR(CLR));
  RAM_Register ram_register_11 (
    .I0(n74125_2__8), .I1(n74125_2__11), .I2(n74125_1__8), .I3(n74125_1__11), .I4(n74125_1__3),
    .I5(n74125_1__6), .I6(n74125_2__3), .I7(n74125_2__6), .O0(DSP[0]), .O1(DSP[1]), .O2(DSP[2]), .O3(DSP[3]),
    .O4(DSP[4]), .O5(DSP[5]), .O6(DSP[6]), .O7(DSP[7]), .SL(address_decoder_1_en2), .CLR(CLR));
  RAM_Register ram_register_12 (
    .I0(n74125_2__8), .I1(n74125_2__11), .I2(n74125_1__8), .I3(n74125_1__11), .I4(n74125_1__3),
    .I5(n74125_1__6), .I6(n74125_2__3), .I7(n74125_2__6), .O0(DSP[0]), .O1(DSP[1]), .O2(DSP[2]), .O3(DSP[3]),
    .O4(DSP[4]), .O5(DSP[5]), .O6(DSP[6]), .O7(DSP[7]), .SL(address_decoder_1_en3), .CLR(CLR));
  RAM_Register ram_register_13 (
    .I0(n74125_2__8), .I1(n74125_2__11), .I2(n74125_1__8), .I3(n74125_1__11), .I4(n74125_1__3),
    .I5(n74125_1__6), .I6(n74125_2__3), .I7(n74125_2__6), .O0(DSP[0]), .O1(DSP[1]), .O2(DSP[2]), .O3(DSP[3]),
    .O4(DSP[4]), .O5(DSP[5]), .O6(DSP[6]), .O7(DSP[7]), .SL(address_decoder_1_en4), .CLR(CLR));
  RAM_Register ram_register_14 (
    .I0(n74125_2__8), .I1(n74125_2__11), .I2(n74125_1__8), .I3(n74125_1__11), .I4(n74125_1__3),
    .I5(n74125_1__6), .I6(n74125_2__3), .I7(n74125_2__6), .O0(DSP[0]), .O1(DSP[1]), .O2(DSP[2]), .O3(DSP[3]),
    .O4(DSP[4]), .O5(DSP[5]), .O6(DSP[6]), .O7(DSP[7]), .SL(address_decoder_1_en5), .CLR(CLR));
  RAM_Register ram_register_15 (
    .I0(n74125_2__8), .I1(n74125_2__11), .I2(n74125_1__8), .I3(n74125_1__11), .I4(n74125_1__3),
    .I5(n74125_1__6), .I6(n74125_2__3), .I7(n74125_2__6), .O0(DSP[0]), .O1(DSP[1]), .O2(DSP[2]), .O3(DSP[3]),
    .O4(DSP[4]), .O5(DSP[5]), .O6(DSP[6]), .O7(DSP[7]), .SL(address_decoder_1_en6), .CLR(CLR));
  RAM_Register ram_register_16 (
    .I0(n74125_2__8), .I1(n74125_2__11), .I2(n74125_1__8), .I3(n74125_1__11), .I4(n74125_1__3),
    .I5(n74125_1__6), .I6(n74125_2__3), .I7(n74125_2__6), .O0(DSP[0]), .O1(DSP[1]), .O2(DSP[2]), .O3(DSP[3]),
    .O4(DSP[4]), .O5(DSP[5]), .O6(DSP[6]), .O7(DSP[7]), .SL(address_decoder_1_en7), .CLR(CLR));
  Pull_Resistor pull_resistor_1 (.node(A1));
  Pull_Resistor pull_resistor_2 (.node(A0));
  _74125 u_74125_1 (
    .Vcc(Vcc), ._13(not_1_out), ._12(D3), ._11(n74125_1__11), ._10(not_1_out), ._9(D2), ._8(n74125_1__8),
    ._1(not_1_out), ._2(D4), ._3(n74125_1__3), ._4(not_1_out), ._5(D5), ._6(n74125_1__6), .GND(GND));
  _74125 u_74125_2 (
    .Vcc(Vcc), ._13(not_1_out), ._12(D1), ._11(n74125_2__11), ._10(not_1_out), ._9(D0), ._8(n74125_2__8),
    ._1(not_1_out), ._2(D6), ._3(n74125_2__3), ._4(not_1_out), ._5(D7), ._6(n74125_2__6), .GND(GND));
  not not_1 (not_1_out, RI);
  not not_2 (not_2_out, RO);
  _74125 u_74125_3 (
    .Vcc(Vcc), ._13(not_2_out), ._12(DSP[7]), ._11(O7), ._10(not_2_out), ._9(DSP[6]), ._8(O6),
    ._1(not_2_out), ._2(DSP[0]), ._3(O0), ._4(not_2_out), ._5(DSP[1]), ._6(O1), .GND(GND));
  _74125 u_74125_4 (
    .Vcc(Vcc), ._13(not_2_out), ._12(DSP[5]), ._11(O5), ._10(not_2_out), ._9(DSP[4]), ._8(O4),
    ._1(not_2_out), ._2(DSP[2]), ._3(O2), ._4(not_2_out), ._5(DSP[3]), ._6(O3), .GND(GND));
  Pull_Resistor pull_resistor_3 (.node(A3));
  Pull_Resistor pull_resistor_4 (.node(A2));
  Pull_Resistor pull_resistor_5 (.node(CLR));
  Pull_Resistor pull_resistor_6 (.node(RI));
  Pull_Resistor pull_resistor_7 (.node(RO));
  Pull_Resistor pull_resistor_8 (.node(D4));
  Pull_Resistor pull_resistor_9 (.node(D5));
  Pull_Resistor pull_resistor_10 (.node(D6));
  Pull_Resistor pull_resistor_11 (.node(D7));
  Pull_Resistor pull_resistor_12 (.node(D3));
  Pull_Resistor pull_resistor_13 (.node(D1));
  Pull_Resistor pull_resistor_14 (.node(D2));
  Pull_Resistor pull_resistor_15 (.node(D0));
endmodule

// 4-BIT SLCT
module Selector_4_Bit (
  input  A3,
  input  A2,
  input  A1,
  input  A0,
  input  B3,
  input  B2,
  input  B1,
  input  B0,
  input  SL,
  output O3,
  output O2,
  output O1,
  output O0
);

  wire not_1_out;

  Pull_Resistor pull_resistor_1 (.node(A2));
  Pull_Resistor pull_resistor_2 (.node(A1));
  Pull_Resistor pull_resistor_3 (.node(A0));
  Pull_Resistor pull_resistor_4 (.node(A3));
  Pull_Resistor pull_resistor_5 (.node(B2));
  Pull_Resistor pull_resistor_6 (.node(B1));
  Pull_Resistor pull_resistor_7 (.node(B0));
  Pull_Resistor pull_resistor_8 (.node(SL));
  Pull_Resistor pull_resistor_9 (.node(B3));
  not not_1 (not_1_out, SL);
  Multiplexer #(.enable("false")) multiplexer_1 (.in0(A3), .in1(B3), .out(O3), .sel(not_1_out));
  Multiplexer #(.enable("false")) multiplexer_2 (.in0(A2), .in1(B2), .out(O2), .sel(not_1_out));
  Multiplexer #(.enable("false")) multiplexer_3 (.in0(A1), .in1(B1), .out(O1), .sel(not_1_out));
  Multiplexer #(.enable("false")) multiplexer_4 (.in0(A0), .in1(B0), .out(O0), .sel(not_1_out));
  Pull_Resistor pull_resistor_10 (.node(O2));
  Pull_Resistor pull_resistor_11 (.node(O1));
  Pull_Resistor pull_resistor_12 (.node(O0));
  Pull_Resistor pull_resistor_13 (.node(O3));
endmodule

// 8-BIT SLCT
module Selector_8_Bit (
  input  A7,
  input  A6,
  input  A5,
  input  A4,
  input  A3,
  input  A2,
  input  A1,
  input  A0,
  input  B7,
  input  B6,
  input  B5,
  input  B4,
  input  B3,
  input  B2,
  input  B1,
  input  B0,
  input  SL,
  output O7,
  output O6,
  output O5,
  output O4,
  output O3,
  output O2,
  output O1,
  output O0
);

  wire not_1_out;

  Pull_Resistor pull_resistor_1 (.node(B3));
  Pull_Resistor pull_resistor_2 (.node(B0));
  Pull_Resistor pull_resistor_3 (.node(B4));
  Pull_Resistor pull_resistor_4 (.node(B1));
  Pull_Resistor pull_resistor_5 (.node(B2));
  Pull_Resistor pull_resistor_6 (.node(A3));
  Pull_Resistor pull_resistor_7 (.node(A2));
  Pull_Resistor pull_resistor_8 (.node(A1));
  Pull_Resistor pull_resistor_9 (.node(A4));
  Pull_Resistor pull_resistor_10 (.node(A0));
  Pull_Resistor pull_resistor_11 (.node(B6));
  Pull_Resistor pull_resistor_12 (.node(B7));
  Pull_Resistor pull_resistor_13 (.node(B5));
  Pull_Resistor pull_resistor_14 (.node(A6));
  Pull_Resistor pull_resistor_15 (.node(A5));
  Pull_Resistor pull_resistor_16 (.node(A7));
  Pull_Resistor pull_resistor_17 (.node(SL));
  not not_1 (not_1_out, SL);
  Pull_Resistor pull_resistor_18 (.node(O6));
  Pull_Resistor pull_resistor_19 (.node(O7));
  Multiplexer #(.enable("false")) multiplexer_1 (.in0(A7), .in1(B7), .out(O7), .sel(not_1_out));
  Multiplexer #(.enable("false")) multiplexer_2 (.in0(A6), .in1(B6), .out(O6), .sel(not_1_out));
  Multiplexer #(.enable("false")) multiplexer_3 (.in0(A5), .in1(B5), .out(O5), .sel(not_1_out));
  Multiplexer #(.enable("false")) multiplexer_4 (.in0(A4), .in1(B4), .out(O4), .sel(not_1_out));
  Multiplexer #(.enable("false")) multiplexer_5 (.in0(A3), .in1(B3), .out(O3), .sel(not_1_out));
  Multiplexer #(.enable("false")) multiplexer_6 (.in0(A2), .in1(B2), .out(O2), .sel(not_1_out));
  Multiplexer #(.enable("false")) multiplexer_7 (.in0(A1), .in1(B1), .out(O1), .sel(not_1_out));
  Multiplexer #(.enable("false")) multiplexer_8 (.in0(A0), .in1(B0), .out(O0), .sel(not_1_out));
  Pull_Resistor pull_resistor_20 (.node(O2));
  Pull_Resistor pull_resistor_21 (.node(O1));
  Pull_Resistor pull_resistor_22 (.node(O3));
  Pull_Resistor pull_resistor_23 (.node(O0));
  Pull_Resistor pull_resistor_24 (.node(O5));
  Pull_Resistor pull_resistor_25 (.node(O4));
endmodule

module Address_Decoder (
  input  A3,
  input  A2,
  input  A1,
  input  A0,
  output EN0,
  output EN1,
  output EN2,
  output EN3,
  output EN4,
  output EN5,
  output EN6,
  output EN7,
  output EN8,
  output EN9,
  output EN10,
  output EN11,
  output EN12,
  output EN13,
  output EN14,
  output EN15
);

  wire not_1_out, not_2_out, not_3_out, not_4_out, not_5_out, not_6_out, not_7_out, not_8_out, not_9_out,
       not_10_out, not_11_out, not_12_out, not_13_out, not_14_out, not_15_out, not_16_out, not_17_out,
       not_18_out, not_19_out, not_20_out, not_21_out, not_22_out, not_23_out, not_24_out, not_25_out,
       not_26_out, not_27_out, not_28_out, not_29_out, not_30_out, not_31_out, not_32_out;

  not not_1 (not_1_out, A3);
  not not_2 (not_2_out, A2);
  not not_3 (not_3_out, A1);
  not not_4 (not_4_out, A0);
  not not_5 (not_5_out, A3);
  not not_6 (not_6_out, A2);
  not not_7 (not_7_out, A1);
  not not_8 (not_8_out, A3);
  not not_9 (not_9_out, A2);
  not not_10 (not_10_out, A0);
  not not_11 (not_11_out, A3);
  not not_12 (not_12_out, A2);
  not not_13 (not_13_out, A3);
  not not_14 (not_14_out, A1);
  not not_15 (not_15_out, A0);
  not not_16 (not_16_out, A3);
  not not_17 (not_17_out, A1);
  not not_18 (not_18_out, A3);
  not not_19 (not_19_out, A0);
  not not_20 (not_20_out, A3);
  not not_21 (not_21_out, A2);
  not not_22 (not_22_out, A1);
  not not_23 (not_23_out, A0);
  not not_24 (not_24_out, A2);
  not not_25 (not_25_out, A1);
  not not_26 (not_26_out, A2);
  not not_27 (not_27_out, A0);
  not not_28 (not_28_out, A2);
  not not_29 (not_29_out, A1);
  not not_30 (not_30_out, A0);
  not not_31 (not_31_out, A1);
  not not_32 (not_32_out, A0);
  and and_1 (EN15, A3, A2, A1, A0);
  and and_2 (EN0, not_1_out, not_2_out, not_3_out, not_4_out);
  and and_3 (EN1, not_5_out, not_6_out, not_7_out, A0);
  and and_4 (EN2, not_8_out, not_9_out, A1, not_10_out);
  and and_5 (EN3, not_11_out, not_12_out, A1, A0);
  and and_6 (EN4, not_13_out, A2, not_14_out, not_15_out);
  and and_7 (EN5, not_16_out, A2, not_17_out, A0);
  and and_8 (EN6, not_18_out, A2, A1, not_19_out);
  and and_9 (EN7, not_20_out, A2, A1, A0);
  and and_10 (EN8, A3, not_21_out, not_22_out, not_23_out);
  and and_11 (EN9, A3, not_24_out, not_25_out, A0);
  and and_12 (EN10, A3, not_26_out, A1, not_27_out);
  and and_13 (EN11, A3, not_28_out, A1, A0);
  and and_14 (EN12, A3, A2, not_29_out, not_30_out);
  and and_15 (EN13, A3, A2, not_31_out, A0);
  and and_16 (EN14, A3, A2, A1, not_32_out);
endmodule
// 8-BIT BIN TO BCD
module Binary_Decoder (
  input  TGL,
  input  I7,
  input  I6,
  input  I5,
  input  I4,
  input  I3,
  input  I2,
  input  I1,
  input  I0,
  output S,
  output B23,
  output B22,
  output B21,
  output B20,
  output B13,
  output B12,
  output B11,
  output B10,
  output B03,
  output B02,
  output B01,
  output B00
);

  wire and_2_out, and_3_out, and_4_out, and_5_out, and_6_out, and_7_out, and_8_out, and_9_out, and_10_out,
       and_11_out, and_12_out, and_13_out, and_14_out, and_15_out, and_16_out, and_17_out, and_18_out,
       and_19_out, and_20_out, and_21_out, and_22_out, and_23_out, and_24_out, and_25_out, and_26_out,
       and_27_out, and_28_out, and_29_out, and_30_out, and_31_out, and_32_out, and_33_out, and_34_out,
       and_35_out, and_36_out, and_37_out, and_38_out, and_39_out, and_40_out, and_41_out, and_42_out,
       and_43_out, and_44_out, and_45_out, and_46_out, and_47_out, and_48_out, and_49_out, and_50_out,
       and_51_out, and_52_out, and_53_out, and_54_out, and_55_out, and_56_out, and_57_out, and_58_out,
       and_59_out, and_60_out, and_61_out, and_62_out, and_63_out, and_64_out, and_65_out, and_66_out,
       and_67_out, and_68_out, and_69_out, and_70_out, and_71_out, and_72_out, and_73_out, and_74_out,
       and_75_out, and_76_out, and_77_out, and_78_out, and_79_out, and_80_out, and_81_out, and_82_out,
       and_83_out, and_84_out, and_85_out, and_86_out, and_87_out, and_88_out, and_89_out, and_90_out,
       and_91_out, and_92_out, and_93_out, and_94_out, and_95_out, and_96_out, and_97_out, and_98_out,
       and_99_out, and_100_out, and_101_out, and_102_out, and_103_out, and_104_out, and_105_out, and_106_out,
       and_107_out, and_108_out, and_109_out, and_110_out, and_111_out, and_112_out, and_113_out,
       and_114_out, and_115_out, and_116_out, and_117_out, and_118_out, and_119_out, and_120_out,
       and_121_out, and_122_out, and_123_out, and_124_out, and_125_out, and_126_out, and_127_out,
       and_128_out, and_129_out, and_130_out, and_131_out, and_132_out, and_133_out, and_134_out,
       and_135_out, and_136_out, and_137_out, and_138_out, and_139_out, and_140_out, and_141_out,
       and_142_out, and_143_out, and_144_out, and_145_out, and_146_out, and_147_out, and_148_out,
       and_149_out, and_150_out, and_151_out, and_152_out, and_153_out, and_154_out, and_155_out,
       and_156_out, and_157_out, and_158_out, and_159_out, and_160_out, and_161_out, and_162_out,
       and_163_out, and_164_out, and_165_out, and_166_out, and_167_out, and_168_out, and_169_out,
       and_170_out, and_171_out, and_172_out, and_173_out, and_174_out, and_175_out, and_176_out,
       and_177_out, and_178_out, and_179_out, and_180_out, and_181_out, and_182_out, and_183_out,
       and_184_out, and_185_out, and_186_out, and_187_out, and_188_out, and_189_out, and_190_out,
       and_191_out, and_192_out, and_193_out, and_194_out, and_195_out, and_196_out, and_197_out,
       and_198_out, and_199_out, and_200_out, and_201_out, and_202_out, and_203_out, and_204_out,
       and_205_out, and_206_out, and_207_out, and_208_out, and_209_out, and_210_out, and_211_out,
       and_212_out, and_213_out, and_214_out, and_215_out, and_216_out, and_217_out, and_218_out,
       and_219_out, and_220_out, and_221_out, and_222_out, and_223_out, and_224_out, and_225_out,
       and_226_out, and_227_out, and_228_out, and_229_out, and_230_out, and_231_out, and_232_out,
       and_233_out, and_234_out, and_235_out, and_236_out, and_237_out, and_238_out, and_239_out,
       and_240_out, and_241_out, and_242_out, and_243_out, and_244_out, and_245_out, and_246_out,
       and_247_out, and_248_out, and_249_out, and_250_out, and_251_out, and_252_out, and_253_out,
       and_254_out, and_255_out, and_256_out, and_257_out, and_258_out, and_259_out, and_260_out,
       and_261_out, and_262_out, and_263_out, and_264_out, and_265_out, and_266_out, and_267_out,
       and_268_out, and_269_out, and_270_out, and_271_out, and_272_out, and_273_out, and_274_out,
       and_275_out, and_276_out, and_277_out, and_278_out, and_279_out, and_280_out, and_281_out,
       and_282_out, and_283_out, and_284_out, and_285_out, and_286_out, and_287_out, and_288_out,
       and_289_out, and_290_out, and_291_out, and_292_out, and_293_out, and_294_out, and_295_out,
       and_296_out, and_297_out, and_298_out, and_299_out, and_300_out, and_301_out, not_1_out, not_2_out,
       not_3_out, not_4_out, not_5_out, not_6_out, not_7_out, not_8_out, not_9_out, not_10_out, not_11_out,
       not_12_out, not_13_out, not_14_out, not_15_out, not_16_out, not_17_out, not_18_out, not_19_out,
       not_20_out, not_21_out, not_22_out, not_23_out, not_24_out, not_25_out, not_26_out, not_27_out,
       not_28_out, not_29_out, not_30_out, not_31_out, not_32_out, not_33_out, not_34_out, not_35_out,
       not_36_out, not_37_out, not_38_out, not_39_out, not_40_out, not_41_out, not_42_out, not_43_out,
       not_44_out, not_45_out, not_46_out, not_47_out, not_48_out, not_49_out, not_50_out, not_51_out,
       not_52_out, not_53_out, not_54_out, not_55_out, not_56_out, not_57_out, not_58_out, not_59_out,
       not_60_out, not_61_out, not_62_out, not_63_out, not_64_out, not_65_out, not_66_out, not_67_out,
       not_68_out, not_69_out, not_70_out, not_71_out, not_72_out, not_73_out, not_74_out, not_75_out,
       not_76_out, not_77_out, not_78_out, not_79_out, not_80_out, not_81_out, not_82_out, not_83_out,
       not_84_out, not_85_out, not_86_out, not_87_out, not_88_out, not_89_out, not_90_out, not_91_out,
       not_92_out, not_93_out, not_94_out, not_95_out, not_96_out, not_97_out, not_98_out, not_99_out,
       not_100_out, not_101_out, not_102_out, not_103_out, not_104_out, not_105_out, not_106_out,
       not_107_out, not_108_out, not_109_out, not_110_out, not_111_out, not_112_out, not_113_out,
       not_114_out, not_115_out, not_116_out, not_117_out, not_118_out, not_119_out, not_120_out,
       not_121_out, not_122_out, not_123_out, not_124_out, not_125_out, not_126_out, not_127_out,
       not_128_out, not_129_out, not_130_out, not_131_out, not_132_out, not_133_out, not_134_out,
       not_135_out, not_136_out, not_137_out, not_138_out, not_139_out, not_140_out, not_141_out,
       not_142_out, not_143_out, not_144_out, not_145_out, not_146_out, not_147_out, not_148_out,
       not_149_out, not_150_out, not_151_out, not_152_out, not_153_out, not_154_out, not_155_out,
       not_156_out, not_157_out, not_158_out, not_159_out, not_160_out, not_161_out, not_162_out,
       not_163_out, not_164_out, not_165_out, not_166_out, not_167_out, not_168_out, not_169_out,
       not_170_out, not_171_out, not_172_out, not_173_out, not_174_out, not_175_out, not_176_out,
       not_177_out, not_178_out, not_179_out, not_180_out, not_181_out, not_182_out, not_183_out,
       not_184_out, not_185_out, not_186_out, not_187_out, not_188_out, not_189_out, not_190_out,
       not_191_out, not_192_out, not_193_out, not_194_out, not_195_out, not_196_out, not_197_out,
       not_198_out, not_199_out, not_200_out, not_201_out, not_202_out, not_203_out, not_204_out,
       not_205_out, not_206_out, not_207_out, not_208_out, not_209_out, not_210_out, not_211_out,
       not_212_out, not_213_out, not_214_out, not_215_out, not_216_out, not_217_out, not_218_out,
       not_219_out, not_220_out, not_221_out, not_222_out, not_223_out, not_224_out, not_225_out,
       not_226_out, not_227_out, not_228_out, not_229_out, not_230_out, not_231_out, not_232_out,
       not_233_out, not_234_out, not_235_out, not_236_out, not_237_out, not_238_out, not_239_out,
       not_240_out, not_241_out, not_242_out, not_243_out, not_244_out, not_245_out, not_246_out,
       not_247_out, not_248_out, not_249_out, not_250_out, not_251_out, not_252_out, not_253_out,
       not_254_out, not_255_out, not_256_out, not_257_out, not_258_out, not_259_out, not_260_out,
       not_261_out, not_262_out, not_263_out, not_264_out, not_265_out, not_266_out, not_267_out,
       not_268_out, not_269_out, not_270_out, not_271_out, not_272_out, not_273_out, not_274_out,
       not_275_out, not_276_out, not_277_out, not_278_out, not_279_out, not_280_out, not_281_out,
       not_282_out, not_283_out, not_284_out, not_285_out, not_286_out, not_287_out, not_288_out,
       not_289_out, not_290_out, not_291_out, not_292_out, not_293_out, not_294_out, not_295_out,
       not_296_out, not_297_out, not_298_out, not_299_out, not_300_out, not_301_out, not_302_out,
       not_303_out, not_304_out, not_305_out, not_306_out, not_307_out, not_308_out, not_309_out,
       not_310_out, not_311_out, not_312_out, not_313_out, not_314_out, not_315_out, not_316_out,
       not_317_out, not_318_out, not_319_out, not_320_out, not_321_out, not_322_out, not_323_out,
       not_324_out, not_325_out, not_326_out, not_327_out, not_328_out, not_329_out, not_330_out,
       not_331_out, not_332_out, not_333_out, not_334_out, not_335_out, not_336_out, not_337_out,
       not_338_out, not_339_out, not_340_out, not_341_out, not_342_out, not_343_out, not_344_out,
       not_345_out, not_346_out, not_347_out, not_348_out, not_349_out, not_350_out, not_351_out,
       not_352_out, not_353_out, not_354_out, not_355_out, not_356_out, not_357_out, not_358_out,
       not_359_out, not_360_out, not_361_out, not_362_out, not_363_out, not_364_out, not_365_out,
       not_366_out, not_367_out, not_368_out, not_369_out, not_370_out, not_371_out, not_372_out,
       not_373_out, not_374_out, not_375_out, not_376_out, not_377_out, not_378_out, not_379_out,
       not_380_out, not_381_out, not_382_out, not_383_out, not_384_out, not_385_out, not_386_out,
       not_387_out, not_388_out, not_389_out, not_390_out, not_391_out, not_392_out, not_393_out,
       not_394_out, not_395_out, not_396_out, not_397_out, not_398_out, not_399_out, not_400_out,
       not_401_out, not_402_out, not_403_out, not_404_out, not_405_out, not_406_out, not_407_out,
       not_408_out, not_409_out, not_410_out, not_411_out, not_412_out, not_413_out, not_414_out,
       not_415_out, not_416_out, not_417_out, not_418_out, not_419_out, not_420_out, not_421_out,
       not_422_out, not_423_out, not_424_out, not_425_out, not_426_out, not_427_out, not_428_out,
       not_429_out, not_430_out, not_431_out, not_432_out, not_433_out, not_434_out, not_435_out,
       not_436_out, not_437_out, not_438_out, not_439_out, not_440_out, not_441_out, not_442_out,
       not_443_out, not_444_out, not_445_out, not_446_out, not_447_out, not_448_out, not_449_out,
       not_450_out, not_451_out, not_452_out, not_453_out, not_454_out, not_455_out, not_456_out,
       not_457_out, not_458_out, not_459_out, not_460_out, not_461_out, not_462_out, not_463_out,
       not_464_out, not_465_out, not_466_out, not_467_out, not_468_out, not_469_out, not_470_out,
       not_471_out, not_472_out, not_473_out, not_474_out, not_475_out, not_476_out, not_477_out,
       not_478_out, not_479_out, not_480_out, not_481_out, not_482_out, not_483_out, not_484_out,
       not_485_out, not_486_out, not_487_out, not_488_out, not_489_out, not_490_out, not_491_out,
       not_492_out, not_493_out, not_494_out, not_495_out, not_496_out, not_497_out, not_498_out,
       not_499_out, not_500_out, not_501_out, not_502_out, not_503_out, not_504_out, not_505_out,
       not_506_out, not_507_out, not_508_out, not_509_out, not_510_out, not_511_out, not_512_out,
       not_513_out, not_514_out, not_515_out, not_516_out, not_517_out, not_518_out, not_519_out,
       not_520_out, not_521_out, not_522_out, not_523_out, not_524_out, not_525_out, not_526_out,
       not_527_out, not_528_out, not_529_out, not_530_out, not_531_out, not_532_out, not_533_out,
       not_534_out, not_535_out, not_536_out, not_537_out, not_538_out, not_539_out, not_540_out,
       not_541_out, not_542_out, not_543_out, not_544_out, not_545_out, not_546_out, not_547_out,
       not_548_out, not_549_out, not_550_out, not_551_out, not_552_out, not_553_out, not_554_out,
       not_555_out, not_556_out, not_557_out, not_558_out, not_559_out, not_560_out, not_561_out,
       not_562_out, not_563_out, not_564_out, not_565_out, not_566_out, not_567_out, not_568_out,
       not_569_out, not_570_out, not_571_out, not_572_out, not_573_out, not_574_out, not_575_out,
       not_576_out, not_577_out, not_578_out, not_579_out, not_580_out, not_581_out, not_582_out,
       not_583_out, not_584_out, not_585_out, not_586_out, not_587_out, not_588_out, not_589_out,
       not_590_out, not_591_out, not_592_out, not_593_out, not_594_out, not_595_out, not_596_out,
       not_597_out, not_598_out, not_599_out, not_600_out, not_601_out, not_602_out, not_603_out,
       not_604_out, not_605_out, not_606_out, not_607_out, not_608_out, not_609_out, not_610_out,
       not_611_out, not_612_out, not_613_out, not_614_out, not_615_out, not_616_out, not_617_out,
       not_618_out, not_619_out, not_620_out, not_621_out, not_622_out, not_623_out, not_624_out,
       not_625_out, not_626_out, not_627_out, not_628_out, not_629_out, not_630_out, not_631_out,
       not_632_out, not_633_out, not_634_out, not_635_out, not_636_out, not_637_out, not_638_out,
       not_639_out, not_640_out, not_641_out, not_642_out, not_643_out, not_644_out, not_645_out,
       not_646_out, not_647_out, not_648_out, not_649_out, not_650_out, not_651_out, not_652_out,
       not_653_out, not_654_out, not_655_out, not_656_out, not_657_out, not_658_out, not_659_out,
       not_660_out, not_661_out, not_662_out, not_663_out, not_664_out, not_665_out, not_666_out,
       not_667_out, not_668_out, not_669_out, not_670_out, not_671_out, not_672_out, not_673_out,
       not_674_out, not_675_out, not_676_out, not_677_out, not_678_out, not_679_out, not_680_out,
       not_681_out, not_682_out, not_683_out, not_684_out, not_685_out, not_686_out, not_687_out,
       not_688_out, not_689_out, not_690_out, not_691_out, not_692_out, not_693_out, not_694_out,
       not_695_out, not_696_out, not_697_out, not_698_out, not_699_out, not_700_out, not_701_out,
       not_702_out, not_703_out, not_704_out, not_705_out, not_706_out, not_707_out, not_708_out,
       not_709_out, not_710_out, not_711_out, not_712_out, not_713_out, not_714_out, not_715_out,
       not_716_out, not_717_out, not_718_out, not_719_out, not_720_out, not_721_out, not_722_out,
       not_723_out, not_724_out, not_725_out, not_726_out, not_727_out, not_728_out, not_729_out,
       not_730_out, not_731_out, not_732_out, not_733_out, not_734_out, not_735_out, not_736_out,
       not_737_out, not_738_out, not_739_out, not_740_out, not_741_out, not_742_out, not_743_out,
       not_744_out, not_745_out, not_746_out, not_747_out, not_748_out, not_749_out, not_750_out,
       not_751_out, not_752_out, not_753_out, not_754_out, not_755_out, not_756_out, not_757_out,
       not_758_out, not_759_out, not_760_out, not_761_out, not_762_out, not_763_out, not_764_out,
       not_765_out, not_766_out, not_767_out, not_768_out, not_769_out, not_770_out, not_771_out,
       not_772_out, not_773_out, not_774_out, not_775_out, not_776_out, not_777_out, not_778_out,
       not_779_out, not_780_out, not_781_out, not_782_out, not_783_out, not_784_out, not_785_out,
       not_786_out, not_787_out, not_788_out, not_789_out, not_790_out, not_791_out, not_792_out,
       not_793_out, not_794_out, not_795_out, not_796_out, not_797_out, not_798_out, not_799_out,
       not_800_out, not_801_out, not_802_out, not_803_out, not_804_out, not_805_out, not_806_out,
       not_807_out, not_808_out, not_809_out, not_810_out, not_811_out, not_812_out, not_813_out,
       not_814_out, not_815_out, not_816_out, not_817_out, not_818_out, not_819_out, not_820_out,
       not_821_out, not_822_out, not_823_out, not_824_out, not_825_out, not_826_out, not_827_out,
       not_828_out, not_829_out, not_830_out, not_831_out, not_832_out, not_833_out, not_834_out,
       not_835_out, not_836_out, not_837_out, not_838_out, not_839_out, not_840_out, not_841_out,
       not_842_out, not_843_out, not_844_out, not_845_out, not_846_out, not_847_out, not_848_out,
       not_849_out, not_850_out, not_851_out, not_852_out, not_853_out, not_854_out, not_855_out,
       not_856_out, not_857_out, not_858_out, not_859_out, not_860_out, not_861_out, not_862_out,
       not_863_out, not_864_out, not_865_out, not_866_out, not_867_out, not_868_out, not_869_out,
       not_870_out, not_871_out, not_872_out, not_873_out, not_874_out, not_875_out, not_876_out,
       not_877_out, not_878_out, not_879_out, not_880_out, not_881_out, not_882_out, not_883_out,
       not_884_out, not_885_out, not_886_out, not_887_out, not_888_out, not_889_out, not_890_out,
       not_891_out, not_892_out, not_893_out, not_894_out, not_895_out, not_896_out, not_897_out,
       not_898_out, not_899_out, not_900_out, not_901_out, not_902_out, not_903_out, not_904_out,
       not_905_out, not_906_out, not_907_out, not_908_out, not_909_out, not_910_out, not_911_out,
       not_912_out, not_913_out, not_914_out, not_915_out, not_916_out, not_917_out, not_918_out,
       not_919_out, not_920_out, not_921_out, not_922_out, not_923_out, not_924_out, not_925_out,
       not_926_out, not_927_out, not_928_out, not_929_out, not_930_out, not_931_out, not_932_out,
       not_933_out, not_934_out, not_935_out, not_936_out, not_937_out, not_938_out, not_939_out,
       not_940_out, not_941_out, not_942_out, not_943_out, not_944_out, not_945_out, not_946_out,
       not_947_out, not_948_out, not_949_out, or_6_out, or_7_out, or_8_out, or_9_out, or_10_out, or_11_out,
       or_12_out, or_13_out, or_14_out, or_15_out;

  and and_1 (S, TGL, I7);
  not not_1 (not_1_out, TGL);
  not not_2 (not_2_out, TGL);
  not not_3 (not_3_out, TGL);
  not not_4 (not_4_out, I7);
  not not_5 (not_5_out, I7);
  not not_6 (not_6_out, I7);
  not not_7 (not_7_out, TGL);
  not not_8 (not_8_out, I6);
  not not_9 (not_9_out, TGL);
  not not_10 (not_10_out, I5);
  not not_11 (not_11_out, I4);
  not not_12 (not_12_out, I3);
  not not_13 (not_13_out, I6);
  not not_14 (not_14_out, I5);
  not not_15 (not_15_out, I4);
  not not_16 (not_16_out, I6);
  not not_17 (not_17_out, I5);
  not not_18 (not_18_out, I3);
  not not_19 (not_19_out, I6);
  not not_20 (not_20_out, I5);
  not not_21 (not_21_out, I2);
  not not_22 (not_22_out, I6);
  not not_23 (not_23_out, I5);
  not not_24 (not_24_out, I1);
  not not_25 (not_25_out, I0);
  not not_26 (not_26_out, I7);
  not not_27 (not_27_out, I5);
  not not_28 (not_28_out, I7);
  not not_29 (not_29_out, I4);
  not not_30 (not_30_out, I3);
  not not_31 (not_31_out, I2);
  not not_32 (not_32_out, TGL);
  not not_33 (not_33_out, I6);
  not not_34 (not_34_out, TGL);
  not not_35 (not_35_out, I6);
  not not_36 (not_36_out, TGL);
  not not_37 (not_37_out, I5);
  not not_38 (not_38_out, I4);
  not not_39 (not_39_out, I3);
  not not_40 (not_40_out, I6);
  not not_41 (not_41_out, I5);
  not not_42 (not_42_out, I6);
  not not_43 (not_43_out, I5);
  not not_44 (not_44_out, I6);
  not not_45 (not_45_out, I4);
  not not_46 (not_46_out, I6);
  not not_47 (not_47_out, I3);
  not not_48 (not_48_out, I2);
  not not_49 (not_49_out, I1);
  not not_50 (not_50_out, I0);
  not not_51 (not_51_out, I7);
  not not_52 (not_52_out, I6);
  not not_53 (not_53_out, I7);
  not not_54 (not_54_out, I6);
  not not_55 (not_55_out, I7);
  not not_56 (not_56_out, I5);
  not not_57 (not_57_out, I4);
  not not_58 (not_58_out, TGL);
  not not_59 (not_59_out, I6);
  not not_60 (not_60_out, I5);
  not not_61 (not_61_out, TGL);
  not not_62 (not_62_out, I6);
  not not_63 (not_63_out, I5);
  not not_64 (not_64_out, TGL);
  not not_65 (not_65_out, I6);
  not not_66 (not_66_out, I4);
  not not_67 (not_67_out, TGL);
  not not_68 (not_68_out, I6);
  not not_69 (not_69_out, I3);
  not not_70 (not_70_out, I2);
  not not_71 (not_71_out, TGL);
  not not_72 (not_72_out, I6);
  not not_73 (not_73_out, I6);
  not not_74 (not_74_out, I6);
  not not_75 (not_75_out, I6);
  not not_76 (not_76_out, I5);
  not not_77 (not_77_out, I4);
  not not_78 (not_78_out, I5);
  not not_79 (not_79_out, I3);
  not not_80 (not_80_out, I5);
  not not_81 (not_81_out, I2);
  not not_82 (not_82_out, I1);
  not not_83 (not_83_out, I0);
  not not_84 (not_84_out, I7);
  not not_85 (not_85_out, I6);
  not not_86 (not_86_out, I5);
  not not_87 (not_87_out, I7);
  not not_88 (not_88_out, I6);
  not not_89 (not_89_out, I5);
  not not_90 (not_90_out, I7);
  not not_91 (not_91_out, I6);
  not not_92 (not_92_out, I7);
  not not_93 (not_93_out, I6);
  not not_94 (not_94_out, I4);
  not not_95 (not_95_out, I3);
  not not_96 (not_96_out, I7);
  not not_97 (not_97_out, I5);
  not not_98 (not_98_out, I4);
  not not_99 (not_99_out, I7);
  not not_100 (not_100_out, TGL);
  not not_101 (not_101_out, I6);
  not not_102 (not_102_out, I4);
  not not_103 (not_103_out, I2);
  not not_104 (not_104_out, I6);
  not not_105 (not_105_out, I5);
  not not_106 (not_106_out, I4);
  not not_107 (not_107_out, I3);
  not not_108 (not_108_out, I6);
  not not_109 (not_109_out, I5);
  not not_110 (not_110_out, I4);
  not not_111 (not_111_out, I2);
  not not_112 (not_112_out, I1);
  not not_113 (not_113_out, I0);
  not not_114 (not_114_out, TGL);
  not not_115 (not_115_out, I6);
  not not_116 (not_116_out, I3);
  not not_117 (not_117_out, I2);
  not not_118 (not_118_out, TGL);
  not not_119 (not_119_out, I4);
  not not_120 (not_120_out, I5);
  not not_121 (not_121_out, I4);
  not not_122 (not_122_out, I3);
  not not_123 (not_123_out, I4);
  not not_124 (not_124_out, I2);
  not not_125 (not_125_out, I4);
  not not_126 (not_126_out, I1);
  not not_127 (not_127_out, I0);
  not not_128 (not_128_out, I5);
  not not_129 (not_129_out, I4);
  not not_130 (not_130_out, I3);
  not not_131 (not_131_out, I2);
  not not_132 (not_132_out, I5);
  not not_133 (not_133_out, I4);
  not not_134 (not_134_out, I3);
  not not_135 (not_135_out, I1);
  not not_136 (not_136_out, I0);
  not not_137 (not_137_out, I6);
  not not_138 (not_138_out, I6);
  not not_139 (not_139_out, I6);
  not not_140 (not_140_out, I6);
  not not_141 (not_141_out, I5);
  not not_142 (not_142_out, I5);
  not not_143 (not_143_out, I6);
  not not_144 (not_144_out, I5);
  not not_145 (not_145_out, I4);
  not not_146 (not_146_out, I2);
  not not_147 (not_147_out, I7);
  not not_148 (not_148_out, I5);
  not not_149 (not_149_out, I4);
  not not_150 (not_150_out, I7);
  not not_151 (not_151_out, I5);
  not not_152 (not_152_out, I7);
  not not_153 (not_153_out, I6);
  not not_154 (not_154_out, I5);
  not not_155 (not_155_out, I3);
  not not_156 (not_156_out, I2);
  not not_157 (not_157_out, I7);
  not not_158 (not_158_out, I6);
  not not_159 (not_159_out, I4);
  not not_160 (not_160_out, I3);
  not not_161 (not_161_out, I7);
  not not_162 (not_162_out, I6);
  not not_163 (not_163_out, I3);
  not not_164 (not_164_out, I7);
  not not_165 (not_165_out, I3);
  not not_166 (not_166_out, I7);
  not not_167 (not_167_out, I6);
  not not_168 (not_168_out, I2);
  not not_169 (not_169_out, I5);
  not not_170 (not_170_out, I4);
  not not_171 (not_171_out, I3);
  not not_172 (not_172_out, I7);
  not not_173 (not_173_out, I5);
  not not_174 (not_174_out, I4);
  not not_175 (not_175_out, I7);
  not not_176 (not_176_out, I5);
  not not_177 (not_177_out, I7);
  not not_178 (not_178_out, I5);
  not not_179 (not_179_out, I7);
  not not_180 (not_180_out, I3);
  not not_181 (not_181_out, I2);
  not not_182 (not_182_out, I4);
  not not_183 (not_183_out, TGL);
  not not_184 (not_184_out, I5);
  not not_185 (not_185_out, I4);
  not not_186 (not_186_out, I3);
  not not_187 (not_187_out, TGL);
  not not_188 (not_188_out, I5);
  not not_189 (not_189_out, I4);
  not not_190 (not_190_out, I3);
  not not_191 (not_191_out, TGL);
  not not_192 (not_192_out, I5);
  not not_193 (not_193_out, I3);
  not not_194 (not_194_out, TGL);
  not not_195 (not_195_out, I6);
  not not_196 (not_196_out, I5);
  not not_197 (not_197_out, I2);
  not not_198 (not_198_out, I6);
  not not_199 (not_199_out, I5);
  not not_200 (not_200_out, I4);
  not not_201 (not_201_out, I2);
  not not_202 (not_202_out, TGL);
  not not_203 (not_203_out, I6);
  not not_204 (not_204_out, I5);
  not not_205 (not_205_out, TGL);
  not not_206 (not_206_out, I5);
  not not_207 (not_207_out, I2);
  not not_208 (not_208_out, TGL);
  not not_209 (not_209_out, I4);
  not not_210 (not_210_out, TGL);
  not not_211 (not_211_out, I4);
  not not_212 (not_212_out, TGL);
  not not_213 (not_213_out, TGL);
  not not_214 (not_214_out, I6);
  not not_215 (not_215_out, I3);
  not not_216 (not_216_out, I2);
  not not_217 (not_217_out, TGL);
  not not_218 (not_218_out, I5);
  not not_219 (not_219_out, I4);
  not not_220 (not_220_out, I3);
  not not_221 (not_221_out, TGL);
  not not_222 (not_222_out, I5);
  not not_223 (not_223_out, I3);
  not not_224 (not_224_out, TGL);
  not not_225 (not_225_out, I5);
  not not_226 (not_226_out, I3);
  not not_227 (not_227_out, I5);
  not not_228 (not_228_out, I4);
  not not_229 (not_229_out, I3);
  not not_230 (not_230_out, TGL);
  not not_231 (not_231_out, I4);
  not not_232 (not_232_out, I3);
  not not_233 (not_233_out, TGL);
  not not_234 (not_234_out, I4);
  not not_235 (not_235_out, TGL);
  not not_236 (not_236_out, TGL);
  not not_237 (not_237_out, I4);
  not not_238 (not_238_out, I6);
  not not_239 (not_239_out, I5);
  not not_240 (not_240_out, I4);
  not not_241 (not_241_out, I6);
  not not_242 (not_242_out, I5);
  not not_243 (not_243_out, I6);
  not not_244 (not_244_out, I5);
  not not_245 (not_245_out, I3);
  not not_246 (not_246_out, I2);
  not not_247 (not_247_out, I1);
  not not_248 (not_248_out, I6);
  not not_249 (not_249_out, I5);
  not not_250 (not_250_out, I3);
  not not_251 (not_251_out, I2);
  not not_252 (not_252_out, I0);
  not not_253 (not_253_out, I6);
  not not_254 (not_254_out, I4);
  not not_255 (not_255_out, I3);
  not not_256 (not_256_out, I1);
  not not_257 (not_257_out, I6);
  not not_258 (not_258_out, I4);
  not not_259 (not_259_out, I3);
  not not_260 (not_260_out, I0);
  not not_261 (not_261_out, I4);
  not not_262 (not_262_out, I3);
  not not_263 (not_263_out, I2);
  not not_264 (not_264_out, I0);
  not not_265 (not_265_out, I6);
  not not_266 (not_266_out, I3);
  not not_267 (not_267_out, I2);
  not not_268 (not_268_out, I6);
  not not_269 (not_269_out, I3);
  not not_270 (not_270_out, I6);
  not not_271 (not_271_out, I2);
  not not_272 (not_272_out, I1);
  not not_273 (not_273_out, I6);
  not not_274 (not_274_out, I2);
  not not_275 (not_275_out, I0);
  not not_276 (not_276_out, I5);
  not not_277 (not_277_out, I4);
  not not_278 (not_278_out, I1);
  not not_279 (not_279_out, I5);
  not not_280 (not_280_out, I4);
  not not_281 (not_281_out, I0);
  not not_282 (not_282_out, I5);
  not not_283 (not_283_out, I2);
  not not_284 (not_284_out, I5);
  not not_285 (not_285_out, I3);
  not not_286 (not_286_out, I2);
  not not_287 (not_287_out, I1);
  not not_288 (not_288_out, I3);
  not not_289 (not_289_out, I1);
  not not_290 (not_290_out, I3);
  not not_291 (not_291_out, I0);
  not not_292 (not_292_out, I6);
  not not_293 (not_293_out, I5);
  not not_294 (not_294_out, I3);
  not not_295 (not_295_out, I2);
  not not_296 (not_296_out, I5);
  not not_297 (not_297_out, I2);
  not not_298 (not_298_out, I7);
  not not_299 (not_299_out, I6);
  not not_300 (not_300_out, I5);
  not not_301 (not_301_out, I4);
  not not_302 (not_302_out, I2);
  not not_303 (not_303_out, I1);
  not not_304 (not_304_out, I7);
  not not_305 (not_305_out, I6);
  not not_306 (not_306_out, I5);
  not not_307 (not_307_out, I3);
  not not_308 (not_308_out, I2);
  not not_309 (not_309_out, I7);
  not not_310 (not_310_out, I6);
  not not_311 (not_311_out, I5);
  not not_312 (not_312_out, I1);
  not not_313 (not_313_out, I7);
  not not_314 (not_314_out, I6);
  not not_315 (not_315_out, I4);
  not not_316 (not_316_out, I3);
  not not_317 (not_317_out, I7);
  not not_318 (not_318_out, I6);
  not not_319 (not_319_out, I3);
  not not_320 (not_320_out, I2);
  not not_321 (not_321_out, I1);
  not not_322 (not_322_out, I7);
  not not_323 (not_323_out, I6);
  not not_324 (not_324_out, I2);
  not not_325 (not_325_out, I7);
  not not_326 (not_326_out, I5);
  not not_327 (not_327_out, I4);
  not not_328 (not_328_out, I3);
  not not_329 (not_329_out, I1);
  not not_330 (not_330_out, I7);
  not not_331 (not_331_out, I5);
  not not_332 (not_332_out, I4);
  not not_333 (not_333_out, I7);
  not not_334 (not_334_out, I5);
  not not_335 (not_335_out, I2);
  not not_336 (not_336_out, I1);
  not not_337 (not_337_out, I7);
  not not_338 (not_338_out, I4);
  not not_339 (not_339_out, I3);
  not not_340 (not_340_out, I2);
  not not_341 (not_341_out, I7);
  not not_342 (not_342_out, I4);
  not not_343 (not_343_out, I1);
  not not_344 (not_344_out, I7);
  not not_345 (not_345_out, I3);
  not not_346 (not_346_out, TGL);
  not not_347 (not_347_out, I6);
  not not_348 (not_348_out, I5);
  not not_349 (not_349_out, I4);
  not not_350 (not_350_out, I3);
  not not_351 (not_351_out, I2);
  not not_352 (not_352_out, I1);
  not not_353 (not_353_out, I6);
  not not_354 (not_354_out, I5);
  not not_355 (not_355_out, I4);
  not not_356 (not_356_out, I3);
  not not_357 (not_357_out, I2);
  not not_358 (not_358_out, I1);
  not not_359 (not_359_out, I0);
  not not_360 (not_360_out, TGL);
  not not_361 (not_361_out, I6);
  not not_362 (not_362_out, I5);
  not not_363 (not_363_out, I4);
  not not_364 (not_364_out, I2);
  not not_365 (not_365_out, I6);
  not not_366 (not_366_out, I5);
  not not_367 (not_367_out, I4);
  not not_368 (not_368_out, I2);
  not not_369 (not_369_out, I0);
  not not_370 (not_370_out, TGL);
  not not_371 (not_371_out, I6);
  not not_372 (not_372_out, I5);
  not not_373 (not_373_out, I3);
  not not_374 (not_374_out, I1);
  not not_375 (not_375_out, I6);
  not not_376 (not_376_out, I5);
  not not_377 (not_377_out, I3);
  not not_378 (not_378_out, I1);
  not not_379 (not_379_out, I0);
  not not_380 (not_380_out, TGL);
  not not_381 (not_381_out, I6);
  not not_382 (not_382_out, I5);
  not not_383 (not_383_out, I6);
  not not_384 (not_384_out, I5);
  not not_385 (not_385_out, I0);
  not not_386 (not_386_out, TGL);
  not not_387 (not_387_out, I6);
  not not_388 (not_388_out, I4);
  not not_389 (not_389_out, I2);
  not not_390 (not_390_out, I1);
  not not_391 (not_391_out, I6);
  not not_392 (not_392_out, I4);
  not not_393 (not_393_out, I2);
  not not_394 (not_394_out, I1);
  not not_395 (not_395_out, I0);
  not not_396 (not_396_out, TGL);
  not not_397 (not_397_out, I6);
  not not_398 (not_398_out, I3);
  not not_399 (not_399_out, I2);
  not not_400 (not_400_out, I6);
  not not_401 (not_401_out, I3);
  not not_402 (not_402_out, I2);
  not not_403 (not_403_out, I0);
  not not_404 (not_404_out, TGL);
  not not_405 (not_405_out, I6);
  not not_406 (not_406_out, I1);
  not not_407 (not_407_out, I6);
  not not_408 (not_408_out, I1);
  not not_409 (not_409_out, I0);
  not not_410 (not_410_out, TGL);
  not not_411 (not_411_out, I5);
  not not_412 (not_412_out, I4);
  not not_413 (not_413_out, I3);
  not not_414 (not_414_out, I5);
  not not_415 (not_415_out, I4);
  not not_416 (not_416_out, I3);
  not not_417 (not_417_out, I0);
  not not_418 (not_418_out, TGL);
  not not_419 (not_419_out, I5);
  not not_420 (not_420_out, I3);
  not not_421 (not_421_out, I2);
  not not_422 (not_422_out, I1);
  not not_423 (not_423_out, I5);
  not not_424 (not_424_out, I3);
  not not_425 (not_425_out, I2);
  not not_426 (not_426_out, I1);
  not not_427 (not_427_out, I0);
  not not_428 (not_428_out, TGL);
  not not_429 (not_429_out, I5);
  not not_430 (not_430_out, I2);
  not not_431 (not_431_out, I5);
  not not_432 (not_432_out, I2);
  not not_433 (not_433_out, I0);
  not not_434 (not_434_out, TGL);
  not not_435 (not_435_out, I4);
  not not_436 (not_436_out, I3);
  not not_437 (not_437_out, I1);
  not not_438 (not_438_out, I4);
  not not_439 (not_439_out, I3);
  not not_440 (not_440_out, I1);
  not not_441 (not_441_out, I0);
  not not_442 (not_442_out, TGL);
  not not_443 (not_443_out, I4);
  not not_444 (not_444_out, I4);
  not not_445 (not_445_out, I0);
  not not_446 (not_446_out, TGL);
  not not_447 (not_447_out, I2);
  not not_448 (not_448_out, I1);
  not not_449 (not_449_out, I2);
  not not_450 (not_450_out, I1);
  not not_451 (not_451_out, I0);
  not not_452 (not_452_out, I6);
  not not_453 (not_453_out, I5);
  not not_454 (not_454_out, I4);
  not not_455 (not_455_out, I2);
  not not_456 (not_456_out, I1);
  not not_457 (not_457_out, I6);
  not not_458 (not_458_out, I5);
  not not_459 (not_459_out, I3);
  not not_460 (not_460_out, I2);
  not not_461 (not_461_out, I6);
  not not_462 (not_462_out, I5);
  not not_463 (not_463_out, I1);
  not not_464 (not_464_out, I6);
  not not_465 (not_465_out, I4);
  not not_466 (not_466_out, I3);
  not not_467 (not_467_out, I6);
  not not_468 (not_468_out, I3);
  not not_469 (not_469_out, I2);
  not not_470 (not_470_out, I1);
  not not_471 (not_471_out, I6);
  not not_472 (not_472_out, I2);
  not not_473 (not_473_out, I5);
  not not_474 (not_474_out, I4);
  not not_475 (not_475_out, I3);
  not not_476 (not_476_out, I1);
  not not_477 (not_477_out, I5);
  not not_478 (not_478_out, I4);
  not not_479 (not_479_out, I5);
  not not_480 (not_480_out, I2);
  not not_481 (not_481_out, I1);
  not not_482 (not_482_out, I4);
  not not_483 (not_483_out, I3);
  not not_484 (not_484_out, I2);
  not not_485 (not_485_out, I4);
  not not_486 (not_486_out, I1);
  not not_487 (not_487_out, I3);
  not not_488 (not_488_out, I7);
  not not_489 (not_489_out, I6);
  not not_490 (not_490_out, I5);
  not not_491 (not_491_out, I4);
  not not_492 (not_492_out, I3);
  not not_493 (not_493_out, TGL);
  not not_494 (not_494_out, I6);
  not not_495 (not_495_out, I5);
  not not_496 (not_496_out, I4);
  not not_497 (not_497_out, I3);
  not not_498 (not_498_out, I7);
  not not_499 (not_499_out, I6);
  not not_500 (not_500_out, I4);
  not not_501 (not_501_out, I7);
  not not_502 (not_502_out, I6);
  not not_503 (not_503_out, I5);
  not not_504 (not_504_out, I2);
  not not_505 (not_505_out, I1);
  not not_506 (not_506_out, I7);
  not not_507 (not_507_out, I6);
  not not_508 (not_508_out, I5);
  not not_509 (not_509_out, I2);
  not not_510 (not_510_out, I7);
  not not_511 (not_511_out, I6);
  not not_512 (not_512_out, I2);
  not not_513 (not_513_out, I1);
  not not_514 (not_514_out, I7);
  not not_515 (not_515_out, I6);
  not not_516 (not_516_out, I4);
  not not_517 (not_517_out, I3);
  not not_518 (not_518_out, I2);
  not not_519 (not_519_out, I7);
  not not_520 (not_520_out, I6);
  not not_521 (not_521_out, I4);
  not not_522 (not_522_out, I1);
  not not_523 (not_523_out, I7);
  not not_524 (not_524_out, I6);
  not not_525 (not_525_out, I3);
  not not_526 (not_526_out, I7);
  not not_527 (not_527_out, I5);
  not not_528 (not_528_out, I4);
  not not_529 (not_529_out, I3);
  not not_530 (not_530_out, I2);
  not not_531 (not_531_out, TGL);
  not not_532 (not_532_out, I5);
  not not_533 (not_533_out, I4);
  not not_534 (not_534_out, I3);
  not not_535 (not_535_out, I2);
  not not_536 (not_536_out, I7);
  not not_537 (not_537_out, I4);
  not not_538 (not_538_out, I2);
  not not_539 (not_539_out, I7);
  not not_540 (not_540_out, I5);
  not not_541 (not_541_out, I4);
  not not_542 (not_542_out, I1);
  not not_543 (not_543_out, I7);
  not not_544 (not_544_out, I5);
  not not_545 (not_545_out, I3);
  not not_546 (not_546_out, TGL);
  not not_547 (not_547_out, I5);
  not not_548 (not_548_out, I3);
  not not_549 (not_549_out, I7);
  not not_550 (not_550_out, I7);
  not not_551 (not_551_out, I4);
  not not_552 (not_552_out, I2);
  not not_553 (not_553_out, I1);
  not not_554 (not_554_out, I7);
  not not_555 (not_555_out, I3);
  not not_556 (not_556_out, I2);
  not not_557 (not_557_out, I7);
  not not_558 (not_558_out, I1);
  not not_559 (not_559_out, TGL);
  not not_560 (not_560_out, I6);
  not not_561 (not_561_out, I5);
  not not_562 (not_562_out, I4);
  not not_563 (not_563_out, I2);
  not not_564 (not_564_out, I1);
  not not_565 (not_565_out, TGL);
  not not_566 (not_566_out, I6);
  not not_567 (not_567_out, I5);
  not not_568 (not_568_out, I3);
  not not_569 (not_569_out, I2);
  not not_570 (not_570_out, TGL);
  not not_571 (not_571_out, I6);
  not not_572 (not_572_out, I2);
  not not_573 (not_573_out, TGL);
  not not_574 (not_574_out, I6);
  not not_575 (not_575_out, I5);
  not not_576 (not_576_out, I1);
  not not_577 (not_577_out, TGL);
  not not_578 (not_578_out, I6);
  not not_579 (not_579_out, I4);
  not not_580 (not_580_out, I3);
  not not_581 (not_581_out, TGL);
  not not_582 (not_582_out, I6);
  not not_583 (not_583_out, I4);
  not not_584 (not_584_out, TGL);
  not not_585 (not_585_out, I6);
  not not_586 (not_586_out, I2);
  not not_587 (not_587_out, I1);
  not not_588 (not_588_out, TGL);
  not not_589 (not_589_out, I5);
  not not_590 (not_590_out, I4);
  not not_591 (not_591_out, I1);
  not not_592 (not_592_out, TGL);
  not not_593 (not_593_out, I5);
  not not_594 (not_594_out, I4);
  not not_595 (not_595_out, TGL);
  not not_596 (not_596_out, I4);
  not not_597 (not_597_out, I1);
  not not_598 (not_598_out, TGL);
  not not_599 (not_599_out, I5);
  not not_600 (not_600_out, I2);
  not not_601 (not_601_out, I1);
  not not_602 (not_602_out, TGL);
  not not_603 (not_603_out, I4);
  not not_604 (not_604_out, I3);
  not not_605 (not_605_out, I2);
  not not_606 (not_606_out, TGL);
  not not_607 (not_607_out, I4);
  not not_608 (not_608_out, I2);
  not not_609 (not_609_out, TGL);
  not not_610 (not_610_out, I3);
  not not_611 (not_611_out, TGL);
  not not_612 (not_612_out, I6);
  not not_613 (not_613_out, I5);
  not not_614 (not_614_out, I4);
  not not_615 (not_615_out, I3);
  not not_616 (not_616_out, I1);
  not not_617 (not_617_out, I0);
  not not_618 (not_618_out, I6);
  not not_619 (not_619_out, I5);
  not not_620 (not_620_out, I2);
  not not_621 (not_621_out, I1);
  not not_622 (not_622_out, I0);
  not not_623 (not_623_out, I5);
  not not_624 (not_624_out, I4);
  not not_625 (not_625_out, I3);
  not not_626 (not_626_out, I2);
  not not_627 (not_627_out, I1);
  not not_628 (not_628_out, I0);
  not not_629 (not_629_out, I5);
  not not_630 (not_630_out, I3);
  not not_631 (not_631_out, I1);
  not not_632 (not_632_out, I0);
  not not_633 (not_633_out, I6);
  not not_634 (not_634_out, I5);
  not not_635 (not_635_out, I4);
  not not_636 (not_636_out, I3);
  not not_637 (not_637_out, I2);
  not not_638 (not_638_out, I6);
  not not_639 (not_639_out, I5);
  not not_640 (not_640_out, I4);
  not not_641 (not_641_out, I3);
  not not_642 (not_642_out, I2);
  not not_643 (not_643_out, I6);
  not not_644 (not_644_out, I5);
  not not_645 (not_645_out, I4);
  not not_646 (not_646_out, I2);
  not not_647 (not_647_out, I6);
  not not_648 (not_648_out, I5);
  not not_649 (not_649_out, I4);
  not not_650 (not_650_out, I1);
  not not_651 (not_651_out, I6);
  not not_652 (not_652_out, I5);
  not not_653 (not_653_out, I4);
  not not_654 (not_654_out, I0);
  not not_655 (not_655_out, I6);
  not not_656 (not_656_out, I4);
  not not_657 (not_657_out, I1);
  not not_658 (not_658_out, I0);
  not not_659 (not_659_out, I6);
  not not_660 (not_660_out, I5);
  not not_661 (not_661_out, I3);
  not not_662 (not_662_out, I6);
  not not_663 (not_663_out, I5);
  not not_664 (not_664_out, I3);
  not not_665 (not_665_out, I6);
  not not_666 (not_666_out, I5);
  not not_667 (not_667_out, I6);
  not not_668 (not_668_out, I4);
  not not_669 (not_669_out, I3);
  not not_670 (not_670_out, I2);
  not not_671 (not_671_out, I1);
  not not_672 (not_672_out, I6);
  not not_673 (not_673_out, I4);
  not not_674 (not_674_out, I2);
  not not_675 (not_675_out, I0);
  not not_676 (not_676_out, I6);
  not not_677 (not_677_out, I4);
  not not_678 (not_678_out, I2);
  not not_679 (not_679_out, I6);
  not not_680 (not_680_out, I3);
  not not_681 (not_681_out, I2);
  not not_682 (not_682_out, I6);
  not not_683 (not_683_out, I3);
  not not_684 (not_684_out, I1);
  not not_685 (not_685_out, I6);
  not not_686 (not_686_out, I0);
  not not_687 (not_687_out, I6);
  not not_688 (not_688_out, I4);
  not not_689 (not_689_out, I3);
  not not_690 (not_690_out, I5);
  not not_691 (not_691_out, I4);
  not not_692 (not_692_out, I2);
  not not_693 (not_693_out, I1);
  not not_694 (not_694_out, I5);
  not not_695 (not_695_out, I4);
  not not_696 (not_696_out, I2);
  not not_697 (not_697_out, I0);
  not not_698 (not_698_out, I4);
  not not_699 (not_699_out, I2);
  not not_700 (not_700_out, I1);
  not not_701 (not_701_out, I0);
  not not_702 (not_702_out, I5);
  not not_703 (not_703_out, I3);
  not not_704 (not_704_out, I2);
  not not_705 (not_705_out, I5);
  not not_706 (not_706_out, I3);
  not not_707 (not_707_out, I2);
  not not_708 (not_708_out, I5);
  not not_709 (not_709_out, I2);
  not not_710 (not_710_out, I5);
  not not_711 (not_711_out, I1);
  not not_712 (not_712_out, I5);
  not not_713 (not_713_out, I0);
  not not_714 (not_714_out, I1);
  not not_715 (not_715_out, I0);
  not not_716 (not_716_out, I4);
  not not_717 (not_717_out, I3);
  not not_718 (not_718_out, I4);
  not not_719 (not_719_out, I3);
  not not_720 (not_720_out, I4);
  not not_721 (not_721_out, I3);
  not not_722 (not_722_out, I2);
  not not_723 (not_723_out, I1);
  not not_724 (not_724_out, I2);
  not not_725 (not_725_out, I0);
  not not_726 (not_726_out, I2);
  not not_727 (not_727_out, I7);
  not not_728 (not_728_out, I6);
  not not_729 (not_729_out, I5);
  not not_730 (not_730_out, I4);
  not not_731 (not_731_out, I3);
  not not_732 (not_732_out, I7);
  not not_733 (not_733_out, I5);
  not not_734 (not_734_out, I4);
  not not_735 (not_735_out, I1);
  not not_736 (not_736_out, I7);
  not not_737 (not_737_out, I6);
  not not_738 (not_738_out, I5);
  not not_739 (not_739_out, I3);
  not not_740 (not_740_out, I2);
  not not_741 (not_741_out, I1);
  not not_742 (not_742_out, I7);
  not not_743 (not_743_out, I5);
  not not_744 (not_744_out, I3);
  not not_745 (not_745_out, I7);
  not not_746 (not_746_out, I6);
  not not_747 (not_747_out, I5);
  not not_748 (not_748_out, I2);
  not not_749 (not_749_out, I7);
  not not_750 (not_750_out, I6);
  not not_751 (not_751_out, I4);
  not not_752 (not_752_out, I3);
  not not_753 (not_753_out, I1);
  not not_754 (not_754_out, I7);
  not not_755 (not_755_out, I6);
  not not_756 (not_756_out, I4);
  not not_757 (not_757_out, I7);
  not not_758 (not_758_out, I3);
  not not_759 (not_759_out, I1);
  not not_760 (not_760_out, I7);
  not not_761 (not_761_out, I6);
  not not_762 (not_762_out, I2);
  not not_763 (not_763_out, I1);
  not not_764 (not_764_out, I7);
  not not_765 (not_765_out, I7);
  not not_766 (not_766_out, I5);
  not not_767 (not_767_out, I3);
  not not_768 (not_768_out, I2);
  not not_769 (not_769_out, I7);
  not not_770 (not_770_out, I5);
  not not_771 (not_771_out, I4);
  not not_772 (not_772_out, I1);
  not not_773 (not_773_out, I7);
  not not_774 (not_774_out, I5);
  not not_775 (not_775_out, I1);
  not not_776 (not_776_out, I7);
  not not_777 (not_777_out, I3);
  not not_778 (not_778_out, I2);
  not not_779 (not_779_out, I1);
  not not_780 (not_780_out, I7);
  not not_781 (not_781_out, I4);
  not not_782 (not_782_out, I3);
  not not_783 (not_783_out, I7);
  not not_784 (not_784_out, I2);
  not not_785 (not_785_out, TGL);
  not not_786 (not_786_out, I5);
  not not_787 (not_787_out, I4);
  not not_788 (not_788_out, I3);
  not not_789 (not_789_out, I1);
  not not_790 (not_790_out, TGL);
  not not_791 (not_791_out, I6);
  not not_792 (not_792_out, I5);
  not not_793 (not_793_out, I2);
  not not_794 (not_794_out, I1);
  not not_795 (not_795_out, TGL);
  not not_796 (not_796_out, I5);
  not not_797 (not_797_out, I4);
  not not_798 (not_798_out, TGL);
  not not_799 (not_799_out, I6);
  not not_800 (not_800_out, I5);
  not not_801 (not_801_out, I3);
  not not_802 (not_802_out, I2);
  not not_803 (not_803_out, TGL);
  not not_804 (not_804_out, I6);
  not not_805 (not_805_out, I5);
  not not_806 (not_806_out, I1);
  not not_807 (not_807_out, TGL);
  not not_808 (not_808_out, I5);
  not not_809 (not_809_out, I2);
  not not_810 (not_810_out, I1);
  not not_811 (not_811_out, I6);
  not not_812 (not_812_out, I5);
  not not_813 (not_813_out, I2);
  not not_814 (not_814_out, I1);
  not not_815 (not_815_out, TGL);
  not not_816 (not_816_out, I6);
  not not_817 (not_817_out, I4);
  not not_818 (not_818_out, I3);
  not not_819 (not_819_out, TGL);
  not not_820 (not_820_out, I4);
  not not_821 (not_821_out, I1);
  not not_822 (not_822_out, TGL);
  not not_823 (not_823_out, I6);
  not not_824 (not_824_out, I3);
  not not_825 (not_825_out, I2);
  not not_826 (not_826_out, I1);
  not not_827 (not_827_out, TGL);
  not not_828 (not_828_out, I3);
  not not_829 (not_829_out, TGL);
  not not_830 (not_830_out, I6);
  not not_831 (not_831_out, I2);
  not not_832 (not_832_out, TGL);
  not not_833 (not_833_out, I5);
  not not_834 (not_834_out, I4);
  not not_835 (not_835_out, I3);
  not not_836 (not_836_out, I1);
  not not_837 (not_837_out, TGL);
  not not_838 (not_838_out, I5);
  not not_839 (not_839_out, I3);
  not not_840 (not_840_out, I1);
  not not_841 (not_841_out, TGL);
  not not_842 (not_842_out, I5);
  not not_843 (not_843_out, I4);
  not not_844 (not_844_out, TGL);
  not not_845 (not_845_out, I5);
  not not_846 (not_846_out, TGL);
  not not_847 (not_847_out, I3);
  not not_848 (not_848_out, I2);
  not not_849 (not_849_out, TGL);
  not not_850 (not_850_out, I4);
  not not_851 (not_851_out, I1);
  not not_852 (not_852_out, TGL);
  not not_853 (not_853_out, I1);
  not not_854 (not_854_out, I6);
  not not_855 (not_855_out, I5);
  not not_856 (not_856_out, I4);
  not not_857 (not_857_out, I3);
  not not_858 (not_858_out, I0);
  not not_859 (not_859_out, I5);
  not not_860 (not_860_out, I4);
  not not_861 (not_861_out, I1);
  not not_862 (not_862_out, I0);
  not not_863 (not_863_out, I6);
  not not_864 (not_864_out, I5);
  not not_865 (not_865_out, I3);
  not not_866 (not_866_out, I2);
  not not_867 (not_867_out, I1);
  not not_868 (not_868_out, I0);
  not not_869 (not_869_out, I5);
  not not_870 (not_870_out, I3);
  not not_871 (not_871_out, I0);
  not not_872 (not_872_out, I6);
  not not_873 (not_873_out, I5);
  not not_874 (not_874_out, I2);
  not not_875 (not_875_out, I0);
  not not_876 (not_876_out, I6);
  not not_877 (not_877_out, I4);
  not not_878 (not_878_out, I3);
  not not_879 (not_879_out, I1);
  not not_880 (not_880_out, I0);
  not not_881 (not_881_out, I6);
  not not_882 (not_882_out, I4);
  not not_883 (not_883_out, I0);
  not not_884 (not_884_out, I3);
  not not_885 (not_885_out, I1);
  not not_886 (not_886_out, I0);
  not not_887 (not_887_out, I6);
  not not_888 (not_888_out, I2);
  not not_889 (not_889_out, I1);
  not not_890 (not_890_out, I0);
  not not_891 (not_891_out, I0);
  not not_892 (not_892_out, I5);
  not not_893 (not_893_out, I3);
  not not_894 (not_894_out, I2);
  not not_895 (not_895_out, I0);
  not not_896 (not_896_out, I5);
  not not_897 (not_897_out, I4);
  not not_898 (not_898_out, I1);
  not not_899 (not_899_out, I0);
  not not_900 (not_900_out, I5);
  not not_901 (not_901_out, I1);
  not not_902 (not_902_out, I0);
  not not_903 (not_903_out, I3);
  not not_904 (not_904_out, I2);
  not not_905 (not_905_out, I1);
  not not_906 (not_906_out, I0);
  not not_907 (not_907_out, I4);
  not not_908 (not_908_out, I3);
  not not_909 (not_909_out, I0);
  not not_910 (not_910_out, I2);
  not not_911 (not_911_out, I0);
  not not_912 (not_912_out, I6);
  not not_913 (not_913_out, I5);
  not not_914 (not_914_out, I4);
  not not_915 (not_915_out, I3);
  not not_916 (not_916_out, I1);
  not not_917 (not_917_out, I6);
  not not_918 (not_918_out, I5);
  not not_919 (not_919_out, I4);
  not not_920 (not_920_out, I5);
  not not_921 (not_921_out, I3);
  not not_922 (not_922_out, I1);
  not not_923 (not_923_out, I5);
  not not_924 (not_924_out, I6);
  not not_925 (not_925_out, I3);
  not not_926 (not_926_out, I2);
  not not_927 (not_927_out, I6);
  not not_928 (not_928_out, I4);
  not not_929 (not_929_out, I1);
  not not_930 (not_930_out, I6);
  not not_931 (not_931_out, I3);
  not not_932 (not_932_out, I3);
  not not_933 (not_933_out, I2);
  not not_934 (not_934_out, I1);
  not not_935 (not_935_out, I5);
  not not_936 (not_936_out, I3);
  not not_937 (not_937_out, I2);
  not not_938 (not_938_out, I1);
  not not_939 (not_939_out, I5);
  not not_940 (not_940_out, I4);
  not not_941 (not_941_out, I3);
  not not_942 (not_942_out, I5);
  not not_943 (not_943_out, I2);
  not not_944 (not_944_out, I4);
  not not_945 (not_945_out, I3);
  not not_946 (not_946_out, I1);
  not not_947 (not_947_out, I2);
  not not_948 (not_948_out, I1);
  not not_949 (not_949_out, I4);
  and and_2 (and_2_out, not_1_out, I7, I6, I3);
  and and_3 (and_3_out, not_2_out, I7, I6, I4);
  and and_4 (and_4_out, not_3_out, I7, I6, I5);
  and and_5 (and_5_out, not_4_out, I6, I5, I2);
  and and_6 (and_6_out, not_5_out, I6, I5, I3);
  and and_7 (and_7_out, not_6_out, I6, I5, I4);
  and and_8 (and_8_out, not_7_out, I7, not_8_out);
  and and_9 (and_9_out, not_9_out, I7, not_10_out, not_11_out, not_12_out);
  and and_10 (and_10_out, I7, not_13_out, not_14_out, not_15_out);
  and and_11 (and_11_out, I7, not_16_out, not_17_out, not_18_out);
  and and_12 (and_12_out, I7, not_19_out, not_20_out, not_21_out);
  and and_13 (and_13_out, I7, not_22_out, not_23_out, not_24_out, not_25_out);
  and and_14 (and_14_out, not_26_out, I6, not_27_out, I4);
  and and_15 (and_15_out, not_28_out, I6, I5, not_29_out, not_30_out, not_31_out);
  and and_16 (and_16_out, not_32_out, I7, not_33_out, I5, I4, I2);
  and and_17 (and_17_out, not_34_out, I7, not_35_out, I5, I4, I3);
  and and_18 (and_18_out, not_36_out, I7, I6, not_37_out, not_38_out, not_39_out);
  and and_19 (and_19_out, TGL, I7, not_40_out, not_41_out, I4, I3, I2, I0);
  and and_20 (and_20_out, TGL, I7, not_42_out, not_43_out, I4, I3, I2, I1);
  and and_21 (and_21_out, TGL, I7, not_44_out, I5, not_45_out);
  and and_22 (and_22_out, TGL, I7, not_46_out, I5, not_47_out, not_48_out, not_49_out, not_50_out);
  and and_23 (and_23_out, not_51_out, not_52_out, I5, I3);
  and and_24 (and_24_out, not_53_out, not_54_out, I5, I4);
  and and_25 (and_25_out, not_55_out, I6, not_56_out, not_57_out);
  and and_26 (and_26_out, not_58_out, I7, not_59_out, not_60_out, I3, I2);
  and and_27 (and_27_out, not_61_out, I7, not_62_out, not_63_out, I4);
  and and_28 (and_28_out, not_64_out, I7, not_65_out, I5, not_66_out);
  and and_29 (and_29_out, not_67_out, I7, not_68_out, I5, not_69_out, not_70_out);
  and and_30 (and_30_out, not_71_out, I7, I6, I5, I4);
  and and_31 (and_31_out, TGL, not_72_out, I5, I4, I0);
  and and_32 (and_32_out, TGL, not_73_out, I5, I4, I1);
  and and_33 (and_33_out, TGL, not_74_out, I5, I4, I2);
  and and_34 (and_34_out, TGL, not_75_out, I5, I4, I3);
  and and_35 (and_35_out, TGL, I6, not_76_out, not_77_out);
  and and_36 (and_36_out, TGL, I7, I6, not_78_out, not_79_out);
  and and_37 (and_37_out, TGL, I7, I6, not_80_out, not_81_out, not_82_out, not_83_out);
  and and_38 (and_38_out, not_84_out, not_85_out, not_86_out, I4, I2);
  and and_39 (and_39_out, not_87_out, not_88_out, not_89_out, I4, I3);
  and and_40 (and_40_out, not_90_out, not_91_out, I4, I3, I2);
  and and_41 (and_41_out, not_92_out, not_93_out, I5, not_94_out, not_95_out);
  and and_42 (and_42_out, not_96_out, I6, not_97_out, not_98_out);
  and and_43 (and_43_out, not_99_out, I6, I5, I4, I3);
  and and_44 (and_44_out, not_100_out, I7, not_101_out, not_102_out, not_103_out);
  and and_45 (and_45_out, I7, not_104_out, not_105_out, not_106_out, not_107_out);
  and and_46 (and_46_out, I7, not_108_out, not_109_out, not_110_out, not_111_out, not_112_out, not_113_out);
  and and_47 (and_47_out, not_114_out, I7, not_115_out, I5, not_116_out, not_117_out);
  and and_48 (and_48_out, not_118_out, I7, I5, not_119_out);
  and and_49 (and_49_out, I7, I6, not_120_out, I4, I3, I2);
  and and_50 (and_50_out, I7, I6, I5, not_121_out, not_122_out);
  and and_51 (and_51_out, I7, I6, I5, not_123_out, not_124_out);
  and and_52 (and_52_out, I7, I6, I5, not_125_out, not_126_out, not_127_out);
  and and_53 (and_53_out, TGL, I7, not_128_out, not_129_out, not_130_out, not_131_out);
  and and_54 (and_54_out, TGL, I7, not_132_out, not_133_out, not_134_out, not_135_out, not_136_out);
  and and_55 (and_55_out, TGL, I7, not_137_out, I5, I4, I0);
  and and_56 (and_56_out, TGL, I7, not_138_out, I5, I4, I1);
  and and_57 (and_57_out, TGL, I7, not_139_out, I5, I4, I2);
  and and_58 (and_58_out, TGL, I7, not_140_out, I5, I4, I3);
  and and_59 (and_59_out, TGL, I7, I6, not_141_out, I4, I3, I0);
  and and_60 (and_60_out, TGL, I7, I6, not_142_out, I4, I3, I1);
  and and_61 (and_61_out, not_143_out, not_144_out, not_145_out, I3, not_146_out, I1);
  and and_62 (and_62_out, not_147_out, not_148_out, not_149_out, I3, I2);
  and and_63 (and_63_out, not_150_out, not_151_out, I3, I2, I1);
  and and_64 (and_64_out, not_152_out, not_153_out, not_154_out, I4, not_155_out, not_156_out);
  and and_65 (and_65_out, not_157_out, not_158_out, I5, not_159_out, not_160_out);
  and and_66 (and_66_out, not_161_out, not_162_out, I5, not_163_out, I1);
  and and_67 (and_67_out, not_164_out, I5, I4, not_165_out, I2);
  and and_68 (and_68_out, not_166_out, not_167_out, I5, I4, I3, not_168_out);
  and and_69 (and_69_out, I6, not_169_out, not_170_out, not_171_out, I2, I1);
  and and_70 (and_70_out, not_172_out, I6, not_173_out, not_174_out, I3);
  and and_71 (and_71_out, not_175_out, I6, not_176_out, I3, I1);
  and and_72 (and_72_out, not_177_out, I6, not_178_out, I3, I2);
  and and_73 (and_73_out, not_179_out, I6, I5, not_180_out, not_181_out);
  and and_74 (and_74_out, I6, I5, not_182_out, I3, I2, I1);
  and and_75 (and_75_out, not_183_out, I7, not_184_out, not_185_out, not_186_out, I1);
  and and_76 (and_76_out, not_187_out, I7, not_188_out, not_189_out, not_190_out, I2);
  and and_77 (and_77_out, not_191_out, I7, not_192_out, not_193_out, I2, I1);
  and and_78 (and_78_out, not_194_out, I7, not_195_out, not_196_out, I3, not_197_out);
  and and_79 (and_79_out, I7, not_198_out, not_199_out, not_200_out, I3, not_201_out, I0);
  and and_80 (and_80_out, not_202_out, I7, not_203_out, not_204_out, I4, I3);
  and and_81 (and_81_out, not_205_out, I7, not_206_out, I4, I3, not_207_out);
  and and_82 (and_82_out, not_208_out, I7, I5, not_209_out, I3, I1);
  and and_83 (and_83_out, not_210_out, I7, I5, not_211_out, I3, I2);
  and and_84 (and_84_out, not_212_out, I7, I5, I3, I2, I1);
  and and_85 (and_85_out, not_213_out, I7, not_214_out, I5, I4, not_215_out, not_216_out);
  and and_86 (and_86_out, not_217_out, I7, I6, not_218_out, not_219_out, not_220_out);
  and and_87 (and_87_out, not_221_out, I7, I6, not_222_out, not_223_out, I1);
  and and_88 (and_88_out, not_224_out, I7, I6, not_225_out, not_226_out, I2);
  and and_89 (and_89_out, I7, I6, not_227_out, not_228_out, not_229_out, I2, I0);
  and and_90 (and_90_out, not_230_out, I7, I6, not_231_out, not_232_out, I2, I1);
  and and_91 (and_91_out, not_233_out, I7, I6, I5, not_234_out, I3);
  and and_92 (and_92_out, not_235_out, I7, I6, I5, I3, I1);
  and and_93 (and_93_out, not_236_out, I7, I6, I5, I3, I2);
  and and_94 (and_94_out, I7, I6, I5, not_237_out, I3, I2, I0);
  and and_95 (and_95_out, TGL, not_238_out, not_239_out, not_240_out, I3, I2);
  and and_96 (and_96_out, TGL, not_241_out, not_242_out, I3, I2, I1);
  and and_97 (and_97_out, TGL, not_243_out, not_244_out, I4, not_245_out, not_246_out, not_247_out);
  and and_98 (and_98_out, TGL, not_248_out, not_249_out, I4, not_250_out, not_251_out, not_252_out);
  and and_99 (and_99_out, TGL, not_253_out, I5, not_254_out, not_255_out, not_256_out);
  and and_100 (and_100_out, TGL, not_257_out, I5, not_258_out, not_259_out, not_260_out);
  and and_101 (and_101_out, TGL, I5, not_261_out, not_262_out, not_263_out, not_264_out);
  and and_102 (and_102_out, TGL, not_265_out, I5, not_266_out, not_267_out, I1);
  and and_103 (and_103_out, TGL, not_268_out, I5, I4, not_269_out, I2);
  and and_104 (and_104_out, TGL, not_270_out, I5, I4, I3, not_271_out, not_272_out);
  and and_105 (and_105_out, TGL, not_273_out, I5, I4, I3, not_274_out, not_275_out);
  and and_106 (and_106_out, TGL, I6, not_276_out, not_277_out, I3, not_278_out);
  and and_107 (and_107_out, TGL, I6, not_279_out, not_280_out, I3, not_281_out);
  and and_108 (and_108_out, TGL, I6, not_282_out, I3, not_283_out, I1);
  and and_109 (and_109_out, TGL, I6, not_284_out, I4, I3, I2);
  and and_110 (and_110_out, TGL, I6, I5, not_285_out, not_286_out, not_287_out);
  and and_111 (and_111_out, TGL, I6, I5, I4, not_288_out, not_289_out);
  and and_112 (and_112_out, TGL, I6, I5, I4, not_290_out, not_291_out);
  and and_113 (and_113_out, TGL, I7, not_292_out, not_293_out, I3, I2, I0);
  and and_114 (and_114_out, TGL, I7, I5, I4, not_294_out, not_295_out, I0);
  and and_115 (and_115_out, TGL, I7, I6, not_296_out, I3, not_297_out, I0);
  and and_116 (and_116_out, not_298_out, not_299_out, not_300_out, not_301_out, I3, not_302_out, not_303_out);
  and and_117 (and_117_out, not_304_out, not_305_out, not_306_out, I4, not_307_out, not_308_out, I1);
  and and_118 (and_118_out, not_309_out, not_310_out, not_311_out, I4, I3, I2, not_312_out);
  and and_119 (and_119_out, not_313_out, not_314_out, I5, not_315_out, not_316_out, I2, I1);
  and and_120 (and_120_out, not_317_out, not_318_out, I5, I4, not_319_out, not_320_out, not_321_out);
  and and_121 (and_121_out, not_322_out, not_323_out, I5, I4, I3, not_324_out, I1);
  and and_122 (and_122_out, not_325_out, I6, not_326_out, not_327_out, not_328_out, I2, not_329_out);
  and and_123 (and_123_out, not_330_out, I6, not_331_out, not_332_out, I3, I2, I1);
  and and_124 (and_124_out, not_333_out, I6, not_334_out, I4, I3, not_335_out, not_336_out);
  and and_125 (and_125_out, not_337_out, I6, I5, not_338_out, not_339_out, not_340_out, I1);
  and and_126 (and_126_out, not_341_out, I6, I5, not_342_out, I3, I2, not_343_out);
  and and_127 (and_127_out, not_344_out, I6, I5, I4, not_345_out, I2, I1);
  and and_128 (and_128_out, not_346_out, I7, not_347_out, not_348_out, not_349_out, not_350_out, not_351_out, not_352_out);
  and and_129 (and_129_out, I7, not_353_out, not_354_out, not_355_out, not_356_out, not_357_out, not_358_out, not_359_out);
  and and_130 (and_130_out, not_360_out, I7, not_361_out, not_362_out, not_363_out, I3, not_364_out, I1);
  and and_131 (and_131_out, I7, not_365_out, not_366_out, not_367_out, I3, not_368_out, I1, not_369_out);
  and and_132 (and_132_out, not_370_out, I7, not_371_out, not_372_out, I4, not_373_out, I2, not_374_out);
  and and_133 (and_133_out, I7, not_375_out, not_376_out, I4, not_377_out, I2, not_378_out, not_379_out);
  and and_134 (and_134_out, not_380_out, I7, not_381_out, not_382_out, I4, I3, I2, I1);
  and and_135 (and_135_out, I7, not_383_out, not_384_out, I4, I3, I2, I1, not_385_out);
  and and_136 (and_136_out, not_386_out, I7, not_387_out, I5, not_388_out, I3, not_389_out, not_390_out);
  and and_137 (and_137_out, I7, not_391_out, I5, not_392_out, I3, not_393_out, not_394_out, not_395_out);
  and and_138 (and_138_out, not_396_out, I7, not_397_out, I5, I4, not_398_out, not_399_out, I1);
  and and_139 (and_139_out, I7, not_400_out, I5, I4, not_401_out, not_402_out, I1, not_403_out);
  and and_140 (and_140_out, not_404_out, I7, not_405_out, I5, I4, I3, I2, not_406_out);
  and and_141 (and_141_out, I7, not_407_out, I5, I4, I3, I2, not_408_out, not_409_out);
  and and_142 (and_142_out, not_410_out, I7, I6, not_411_out, not_412_out, not_413_out, I2, I1);
  and and_143 (and_143_out, I7, I6, not_414_out, not_415_out, not_416_out, I2, I1, not_417_out);
  and and_144 (and_144_out, not_418_out, I7, I6, not_419_out, I4, not_420_out, not_421_out, not_422_out);
  and and_145 (and_145_out, I7, I6, not_423_out, I4, not_424_out, not_425_out, not_426_out, not_427_out);
  and and_146 (and_146_out, not_428_out, I7, I6, not_429_out, I4, I3, not_430_out, I1);
  and and_147 (and_147_out, I7, I6, not_431_out, I4, I3, not_432_out, I1, not_433_out);
  and and_148 (and_148_out, not_434_out, I7, I6, I5, not_435_out, not_436_out, I2, not_437_out);
  and and_149 (and_149_out, I7, I6, I5, not_438_out, not_439_out, I2, not_440_out, not_441_out);
  and and_150 (and_150_out, not_442_out, I7, I6, I5, not_443_out, I3, I2, I1);
  and and_151 (and_151_out, I7, I6, I5, not_444_out, I3, I2, I1, not_445_out);
  and and_152 (and_152_out, not_446_out, I7, I6, I5, I4, I3, not_447_out, not_448_out);
  and and_153 (and_153_out, I7, I6, I5, I4, I3, not_449_out, not_450_out, not_451_out);
  and and_154 (and_154_out, TGL, not_452_out, not_453_out, not_454_out, I3, not_455_out, not_456_out, I0);
  and and_155 (and_155_out, TGL, not_457_out, not_458_out, I4, not_459_out, not_460_out, I1, I0);
  and and_156 (and_156_out, TGL, not_461_out, not_462_out, I4, I3, I2, not_463_out, I0);
  and and_157 (and_157_out, TGL, not_464_out, I5, not_465_out, not_466_out, I2, I1, I0);
  and and_158 (and_158_out, TGL, not_467_out, I5, I4, not_468_out, not_469_out, not_470_out, I0);
  and and_159 (and_159_out, TGL, not_471_out, I5, I4, I3, not_472_out, I1, I0);
  and and_160 (and_160_out, TGL, I6, not_473_out, not_474_out, not_475_out, I2, not_476_out, I0);
  and and_161 (and_161_out, TGL, I6, not_477_out, not_478_out, I3, I2, I1, I0);
  and and_162 (and_162_out, TGL, I6, not_479_out, I4, I3, not_480_out, not_481_out, I0);
  and and_163 (and_163_out, TGL, I6, I5, not_482_out, not_483_out, not_484_out, I1, I0);
  and and_164 (and_164_out, TGL, I6, I5, not_485_out, I3, I2, not_486_out, I0);
  and and_165 (and_165_out, TGL, I6, I5, I4, not_487_out, I2, I1, I0);
  and and_166 (and_166_out, not_488_out, not_489_out, not_490_out, not_491_out, not_492_out, I2);
  and and_167 (and_167_out, not_493_out, not_494_out, not_495_out, not_496_out, not_497_out, I2, I1);
  and and_168 (and_168_out, not_498_out, not_499_out, not_500_out, I3, I2, I1);
  and and_169 (and_169_out, not_501_out, not_502_out, not_503_out, I4, not_504_out, not_505_out);
  and and_170 (and_170_out, not_506_out, not_507_out, not_508_out, I4, I3, not_509_out);
  and and_171 (and_171_out, not_510_out, not_511_out, I4, I3, not_512_out, not_513_out);
  and and_172 (and_172_out, not_514_out, not_515_out, I5, not_516_out, not_517_out, not_518_out, I1);
  and and_173 (and_173_out, not_519_out, not_520_out, I5, not_521_out, I2, not_522_out);
  and and_174 (and_174_out, not_523_out, not_524_out, I5, I4, not_525_out, I2, I1);
  and and_175 (and_175_out, not_526_out, I6, not_527_out, not_528_out, not_529_out, not_530_out);
  and and_176 (and_176_out, not_531_out, I6, not_532_out, not_533_out, not_534_out, not_535_out, I1);
  and and_177 (and_177_out, not_536_out, I6, not_537_out, I3, not_538_out, I1);
  and and_178 (and_178_out, not_539_out, I6, not_540_out, not_541_out, I3, I2, not_542_out);
  and and_179 (and_179_out, not_543_out, I6, not_544_out, I4, not_545_out, I2);
  and and_180 (and_180_out, not_546_out, I6, not_547_out, I4, not_548_out, I2, I1);
  and and_181 (and_181_out, not_549_out, I6, I4, I3, I2, I1);
  and and_182 (and_182_out, not_550_out, I6, I5, not_551_out, not_552_out, not_553_out);
  and and_183 (and_183_out, not_554_out, I6, I5, I4, not_555_out, not_556_out, I1);
  and and_184 (and_184_out, not_557_out, I6, I5, I4, I2, not_558_out);
  and and_185 (and_185_out, not_559_out, I7, not_560_out, not_561_out, not_562_out, I3, not_563_out, not_564_out);
  and and_186 (and_186_out, not_565_out, I7, not_566_out, not_567_out, I4, not_568_out, not_569_out);
  and and_187 (and_187_out, not_570_out, I7, not_571_out, I4, I3, not_572_out, I1);
  and and_188 (and_188_out, not_573_out, I7, not_574_out, not_575_out, I4, I3, I2, not_576_out);
  and and_189 (and_189_out, not_577_out, I7, not_578_out, I5, not_579_out, not_580_out, I2);
  and and_190 (and_190_out, not_581_out, I7, not_582_out, I5, not_583_out, I2, I1);
  and and_191 (and_191_out, not_584_out, I7, not_585_out, I5, I4, not_586_out, not_587_out);
  and and_192 (and_192_out, not_588_out, I7, I6, not_589_out, not_590_out, I2, not_591_out);
  and and_193 (and_193_out, not_592_out, I7, I6, not_593_out, not_594_out, I3, I2);
  and and_194 (and_194_out, not_595_out, I7, I6, not_596_out, I3, I2, not_597_out);
  and and_195 (and_195_out, not_598_out, I7, I6, not_599_out, I4, I3, not_600_out, not_601_out);
  and and_196 (and_196_out, not_602_out, I7, I6, I5, not_603_out, not_604_out, not_605_out);
  and and_197 (and_197_out, not_606_out, I7, I6, I5, not_607_out, not_608_out, I1);
  and and_198 (and_198_out, not_609_out, I7, I6, I5, I4, not_610_out, I2);
  and and_199 (and_199_out, not_611_out, I7, I6, I5, I4, I2, I1);
  and and_200 (and_200_out, TGL, not_612_out, not_613_out, not_614_out, not_615_out, I2, not_616_out, not_617_out);
  and and_201 (and_201_out, TGL, not_618_out, not_619_out, I4, I3, not_620_out, not_621_out, not_622_out);
  and and_202 (and_202_out, TGL, I6, not_623_out, not_624_out, not_625_out, not_626_out, not_627_out, not_628_out);
  and and_203 (and_203_out, TGL, I6, not_629_out, I4, not_630_out, I2, not_631_out, not_632_out);
  and and_204 (and_204_out, TGL, I7, not_633_out, not_634_out, not_635_out, not_636_out, not_637_out, I0);
  and and_205 (and_205_out, TGL, I7, not_638_out, not_639_out, not_640_out, not_641_out, not_642_out, I1);
  and and_206 (and_206_out, TGL, I7, not_643_out, not_644_out, not_645_out, not_646_out, I1, I0);
  and and_207 (and_207_out, TGL, I7, not_647_out, not_648_out, not_649_out, I3, I2, not_650_out);
  and and_208 (and_208_out, TGL, I7, not_651_out, not_652_out, not_653_out, I3, I2, not_654_out);
  and and_209 (and_209_out, TGL, I7, not_655_out, not_656_out, I3, I2, not_657_out, not_658_out);
  and and_210 (and_210_out, TGL, I7, not_659_out, not_660_out, I4, not_661_out, I2, I0);
  and and_211 (and_211_out, TGL, I7, not_662_out, not_663_out, I4, not_664_out, I2, I1);
  and and_212 (and_212_out, TGL, I7, not_665_out, not_666_out, I4, I2, I1, I0);
  and and_213 (and_213_out, TGL, I7, not_667_out, I5, not_668_out, not_669_out, not_670_out, not_671_out);
  and and_214 (and_214_out, TGL, I7, not_672_out, I5, not_673_out, not_674_out, I1, not_675_out);
  and and_215 (and_215_out, TGL, I7, not_676_out, I5, not_677_out, I3, not_678_out, I0);
  and and_216 (and_216_out, TGL, I7, not_679_out, I5, I4, not_680_out, not_681_out, I1, I0);
  and and_217 (and_217_out, TGL, I7, not_682_out, I5, I4, not_683_out, I2, not_684_out);
  and and_218 (and_218_out, TGL, I7, not_685_out, I5, I4, I2, I1, not_686_out);
  and and_219 (and_219_out, TGL, I7, not_687_out, I5, I4, I3, I2, I0);
  and and_220 (and_220_out, TGL, I7, I6, not_688_out, not_689_out, I2, I1, I0);
  and and_221 (and_221_out, TGL, I7, I6, not_690_out, not_691_out, I3, not_692_out, not_693_out);
  and and_222 (and_222_out, TGL, I7, I6, not_694_out, not_695_out, I3, not_696_out, not_697_out);
  and and_223 (and_223_out, TGL, I7, I6, not_698_out, I3, not_699_out, not_700_out, not_701_out);
  and and_224 (and_224_out, TGL, I7, I6, not_702_out, I4, not_703_out, not_704_out, I0);
  and and_225 (and_225_out, TGL, I7, I6, not_705_out, I4, not_706_out, not_707_out, I1);
  and and_226 (and_226_out, TGL, I7, I6, not_708_out, I4, not_709_out, I1, I0);
  and and_227 (and_227_out, TGL, I7, I6, not_710_out, I4, I3, I2, not_711_out);
  and and_228 (and_228_out, TGL, I7, I6, not_712_out, I4, I3, I2, not_713_out);
  and and_229 (and_229_out, TGL, I7, I6, I4, I3, I2, not_714_out, not_715_out);
  and and_230 (and_230_out, TGL, I7, I6, I5, not_716_out, not_717_out, I2, I0);
  and and_231 (and_231_out, TGL, I7, I6, I5, not_718_out, not_719_out, I2, I1);
  and and_232 (and_232_out, TGL, I7, I6, I5, not_720_out, I2, I1, I0);
  and and_233 (and_233_out, TGL, I7, I6, I5, I4, not_721_out, not_722_out, not_723_out);
  and and_234 (and_234_out, TGL, I7, I6, I5, I4, not_724_out, I1, not_725_out);
  and and_235 (and_235_out, TGL, I7, I6, I5, I4, I3, not_726_out, I0);
  and and_236 (and_236_out, not_727_out, not_728_out, not_729_out, not_730_out, not_731_out, I1);
  and and_237 (and_237_out, not_732_out, not_733_out, not_734_out, I3, I2, not_735_out);
  and and_238 (and_238_out, not_736_out, not_737_out, not_738_out, I4, not_739_out, not_740_out, not_741_out);
  and and_239 (and_239_out, not_742_out, not_743_out, I4, not_744_out, I2, I1);
  and and_240 (and_240_out, not_745_out, not_746_out, not_747_out, I4, I3, not_748_out, I1);
  and and_241 (and_241_out, not_749_out, not_750_out, I5, not_751_out, not_752_out, not_753_out);
  and and_242 (and_242_out, not_754_out, not_755_out, I5, not_756_out, I3, I1);
  and and_243 (and_243_out, not_757_out, I5, I4, not_758_out, I2, not_759_out);
  and and_244 (and_244_out, not_760_out, not_761_out, I5, I4, I3, not_762_out, not_763_out);
  and and_245 (and_245_out, not_764_out, I5, I4, I3, I2, I1);
  and and_246 (and_246_out, not_765_out, I6, not_766_out, not_767_out, not_768_out, I1);
  and and_247 (and_247_out, not_769_out, I6, not_770_out, not_771_out, I3, not_772_out);
  and and_248 (and_248_out, not_773_out, I6, not_774_out, I3, I2, not_775_out);
  and and_249 (and_249_out, not_776_out, I6, I5, not_777_out, not_778_out, not_779_out);
  and and_250 (and_250_out, not_780_out, I6, I5, not_781_out, not_782_out, I2, I1);
  and and_251 (and_251_out, not_783_out, I6, I5, I3, not_784_out, I1);
  and and_252 (and_252_out, not_785_out, I7, not_786_out, not_787_out, not_788_out, I2, not_789_out);
  and and_253 (and_253_out, not_790_out, I7, not_791_out, not_792_out, I3, not_793_out, not_794_out);
  and and_254 (and_254_out, not_795_out, I7, not_796_out, not_797_out, I3, I2, I1);
  and and_255 (and_255_out, not_798_out, I7, not_799_out, not_800_out, I4, not_801_out, not_802_out, I1);
  and and_256 (and_256_out, not_803_out, I7, not_804_out, not_805_out, I4, I3, not_806_out);
  and and_257 (and_257_out, not_807_out, I7, not_808_out, I4, I3, not_809_out, not_810_out);
  and and_258 (and_258_out, I7, not_811_out, not_812_out, I4, I3, not_813_out, not_814_out, I0);
  and and_259 (and_259_out, not_815_out, I7, not_816_out, I5, not_817_out, not_818_out, I1);
  and and_260 (and_260_out, not_819_out, I7, I5, not_820_out, I3, I2, not_821_out);
  and and_261 (and_261_out, not_822_out, I7, not_823_out, I5, I4, not_824_out, not_825_out, not_826_out);
  and and_262 (and_262_out, not_827_out, I7, I5, I4, not_828_out, I2, I1);
  and and_263 (and_263_out, not_829_out, I7, not_830_out, I5, I4, I3, not_831_out, I1);
  and and_264 (and_264_out, not_832_out, I7, I6, not_833_out, not_834_out, not_835_out, not_836_out);
  and and_265 (and_265_out, not_837_out, I7, I6, not_838_out, not_839_out, I2, not_840_out);
  and and_266 (and_266_out, not_841_out, I7, I6, not_842_out, not_843_out, I3, I1);
  and and_267 (and_267_out, not_844_out, I7, I6, not_845_out, I3, I2, I1);
  and and_268 (and_268_out, not_846_out, I7, I6, I5, not_847_out, not_848_out, I1);
  and and_269 (and_269_out, not_849_out, I7, I6, I5, not_850_out, I3, not_851_out);
  and and_270 (and_270_out, not_852_out, I7, I6, I5, I3, I2, not_853_out);
  and and_271 (and_271_out, TGL, not_854_out, not_855_out, not_856_out, not_857_out, I1, not_858_out);
  and and_272 (and_272_out, TGL, not_859_out, not_860_out, I3, I2, not_861_out, not_862_out);
  and and_273 (and_273_out, TGL, not_863_out, not_864_out, I4, not_865_out, not_866_out, not_867_out, not_868_out);
  and and_274 (and_274_out, TGL, not_869_out, I4, not_870_out, I2, I1, not_871_out);
  and and_275 (and_275_out, TGL, not_872_out, not_873_out, I4, I3, not_874_out, I1, not_875_out);
  and and_276 (and_276_out, TGL, not_876_out, I5, not_877_out, not_878_out, not_879_out, not_880_out);
  and and_277 (and_277_out, TGL, not_881_out, I5, not_882_out, I3, I1, not_883_out);
  and and_278 (and_278_out, TGL, I5, I4, not_884_out, I2, not_885_out, not_886_out);
  and and_279 (and_279_out, TGL, not_887_out, I5, I4, I3, not_888_out, not_889_out, not_890_out);
  and and_280 (and_280_out, TGL, I5, I4, I3, I2, I1, not_891_out);
  and and_281 (and_281_out, TGL, I6, not_892_out, not_893_out, not_894_out, I1, not_895_out);
  and and_282 (and_282_out, TGL, I6, not_896_out, not_897_out, I3, not_898_out, not_899_out);
  and and_283 (and_283_out, TGL, I6, not_900_out, I3, I2, not_901_out, not_902_out);
  and and_284 (and_284_out, TGL, I6, I5, not_903_out, not_904_out, not_905_out, not_906_out);
  and and_285 (and_285_out, TGL, I6, I5, not_907_out, not_908_out, I2, I1, not_909_out);
  and and_286 (and_286_out, TGL, I6, I5, I3, not_910_out, I1, not_911_out);
  and and_287 (and_287_out, TGL, I7, not_912_out, not_913_out, not_914_out, not_915_out, not_916_out, I0);
  and and_288 (and_288_out, TGL, I7, not_917_out, not_918_out, not_919_out, I3, I1, I0);
  and and_289 (and_289_out, TGL, I7, not_920_out, I4, not_921_out, I2, not_922_out, I0);
  and and_290 (and_290_out, TGL, I7, not_923_out, I4, I3, I2, I1, I0);
  and and_291 (and_291_out, TGL, I7, not_924_out, I5, not_925_out, not_926_out, I1, I0);
  and and_292 (and_292_out, TGL, I7, not_927_out, I5, not_928_out, I3, not_929_out, I0);
  and and_293 (and_293_out, TGL, I7, not_930_out, I5, I4, not_931_out, I1, I0);
  and and_294 (and_294_out, TGL, I7, I5, I4, not_932_out, not_933_out, I1, I0);
  and and_295 (and_295_out, TGL, I7, I5, I4, I3, I2, not_934_out, I0);
  and and_296 (and_296_out, TGL, I7, I6, not_935_out, not_936_out, not_937_out, not_938_out, I0);
  and and_297 (and_297_out, TGL, I7, I6, not_939_out, not_940_out, not_941_out, I2, I1, I0);
  and and_298 (and_298_out, TGL, I7, I6, not_942_out, I3, not_943_out, I1, I0);
  and and_299 (and_299_out, TGL, I7, I6, I5, not_944_out, not_945_out, I2, not_946_out, I0);
  and and_300 (and_300_out, TGL, I7, I6, I5, I3, not_947_out, not_948_out, I0);
  and and_301 (and_301_out, TGL, I7, I6, I5, not_949_out, I3, I2, I1, I0);
  or or_1 (B21, and_2_out, and_3_out, and_4_out);
  or or_2 (B20, and_5_out, and_6_out, and_7_out, and_8_out, and_9_out, and_10_out, and_11_out, and_12_out, and_13_out);
  or or_3 (B13, and_14_out, and_15_out, and_16_out, and_17_out, and_18_out, and_19_out, and_20_out, and_21_out, and_22_out);
  or or_4 (B12, and_23_out, and_24_out, and_25_out, and_26_out, and_27_out, and_28_out, and_29_out, and_30_out, and_31_out, and_32_out, and_33_out, and_34_out, and_35_out, and_36_out, and_37_out);
  or or_5 (B11, and_38_out, and_39_out, and_40_out, and_41_out, and_42_out, and_43_out, and_44_out, and_45_out, and_46_out, and_47_out, and_48_out, and_49_out, and_50_out, and_51_out, and_52_out, and_53_out, and_54_out, and_55_out, and_56_out, and_57_out, and_58_out, and_59_out, and_60_out);
  or or_6 (or_6_out, and_61_out, and_62_out, and_63_out, and_64_out, and_65_out, and_66_out, and_67_out, and_68_out, and_69_out, and_70_out, and_71_out, and_72_out, and_73_out, and_74_out, and_75_out, and_76_out, and_77_out, and_78_out, and_79_out, and_80_out, and_81_out, and_82_out, and_83_out, and_84_out, and_85_out, and_86_out, and_87_out, and_88_out);
  or or_7 (or_7_out, and_89_out, and_90_out, and_91_out, and_92_out, and_93_out, and_94_out, and_95_out, and_96_out, and_97_out, and_98_out, and_99_out, and_100_out, and_101_out, and_102_out, and_103_out, and_104_out, and_105_out, and_106_out, and_107_out, and_108_out, and_109_out, and_110_out, and_111_out, and_112_out, and_113_out, and_114_out, and_115_out);
  or or_8 (or_8_out, and_116_out, and_117_out, and_118_out, and_119_out, and_120_out, and_121_out, and_122_out, and_123_out, and_124_out, and_125_out, and_126_out, and_127_out, and_128_out, and_129_out, and_130_out, and_131_out, and_132_out, and_133_out, and_134_out, and_135_out, and_136_out, and_137_out, and_138_out, and_139_out, and_140_out);
  or or_9 (or_9_out, and_141_out, and_142_out, and_143_out, and_144_out, and_145_out, and_146_out, and_147_out, and_148_out, and_149_out, and_150_out, and_151_out, and_152_out, and_153_out, and_154_out, and_155_out, and_156_out, and_157_out, and_158_out, and_159_out, and_160_out, and_161_out, and_162_out, and_163_out, and_164_out, and_165_out);
  or or_10 (or_10_out, and_166_out, and_167_out, and_168_out, and_169_out, and_170_out, and_171_out, and_172_out, and_173_out, and_174_out, and_175_out, and_176_out, and_177_out, and_178_out, and_179_out, and_180_out, and_181_out, and_182_out, and_183_out, and_184_out, and_185_out, and_186_out, and_187_out, and_188_out, and_189_out);
  or or_11 (or_11_out, and_190_out, and_191_out, and_192_out, and_193_out, and_194_out, and_195_out, and_196_out, and_197_out, and_198_out, and_199_out, and_200_out, and_201_out, and_202_out, and_203_out, and_204_out, and_205_out, and_206_out, and_207_out, and_208_out, and_209_out, and_210_out, and_211_out, and_212_out);
  or or_12 (or_12_out, and_213_out, and_214_out, and_215_out, and_216_out, and_217_out, and_218_out, and_219_out, and_220_out, and_221_out, and_222_out, and_223_out, and_224_out, and_225_out, and_226_out, and_227_out, and_228_out, and_229_out, and_230_out, and_231_out, and_232_out, and_233_out, and_234_out, and_235_out);
  or or_13 (or_13_out, and_236_out, and_237_out, and_238_out, and_239_out, and_240_out, and_241_out, and_242_out, and_243_out, and_244_out, and_245_out, and_246_out, and_247_out, and_248_out, and_249_out, and_250_out, and_251_out, and_252_out, and_253_out, and_254_out, and_255_out, and_256_out, and_257_out);
  or or_14 (or_14_out, and_258_out, and_259_out, and_260_out, and_261_out, and_262_out, and_263_out, and_264_out, and_265_out, and_266_out, and_267_out, and_268_out, and_269_out, and_270_out, and_271_out, and_272_out, and_273_out, and_274_out, and_275_out, and_276_out, and_277_out, and_278_out, and_279_out);
  or or_15 (or_15_out, and_280_out, and_281_out, and_282_out, and_283_out, and_284_out, and_285_out, and_286_out, and_287_out, and_288_out, and_289_out, and_290_out, and_291_out, and_292_out, and_293_out, and_294_out, and_295_out, and_296_out, and_297_out, and_298_out, and_299_out, and_300_out, and_301_out);
  or or_16 (B10, or_6_out, or_7_out);
  or or_17 (B03, or_8_out, or_9_out);
  or or_18 (B02, or_10_out, or_11_out, or_12_out);
  or or_19 (B01, or_13_out, or_14_out, or_15_out);

  assign B00 = I0;
  assign B22 = 1'b0;
  assign B23 = 1'b0;
endmodule

// ZERO DETECT
module Zero_Detector (
  input  I7,
  input  I6,
  input  I5,
  input  I4,
  input  I3,
  input  I2,
  input  I1,
  input  I0,
  output OUT
);

  wire and_1_out, and_2_out, nor_1_out, nor_2_out, nor_3_out, nor_4_out;

  Pull_Resistor pull_resistor_1 (.node(I0));
  Pull_Resistor pull_resistor_2 (.node(I7));
  Pull_Resistor pull_resistor_3 (.node(I5));
  Pull_Resistor pull_resistor_4 (.node(I6));
  Pull_Resistor pull_resistor_5 (.node(I4));
  Pull_Resistor pull_resistor_6 (.node(I1));
  Pull_Resistor pull_resistor_7 (.node(I3));
  Pull_Resistor pull_resistor_8 (.node(I2));
  nor nor_1 (nor_1_out, I7, I6);
  nor nor_2 (nor_2_out, I5, I4);
  nor nor_3 (nor_3_out, I3, I2);
  nor nor_4 (nor_4_out, I1, I0);
  and and_1 (and_1_out, nor_1_out, nor_2_out);
  and and_2 (and_2_out, nor_3_out, nor_4_out);
  and and_3 (OUT, and_1_out, and_2_out);
endmodule

module _74125 (
  input  Vcc,
  input  _13,
  input  _12,
  input  _10,
  input  _9,
  input  _1,
  input  _2,
  input  _4,
  input  _5,
  input  GND,
  output _11,
  output _8,
  output _3,
  output _6
);

  assign _3 = ~_1 ? _2 : 1'bz;  // Controlled_Buffer controlled_buffer_1
  assign _8 = ~_10 ? _9 : 1'bz;  // Controlled_Buffer controlled_buffer_2
  assign _11 = ~_13 ? _12 : 1'bz;  // Controlled_Buffer controlled_buffer_3
  assign _6 = ~_4 ? _5 : 1'bz;  // Controlled_Buffer controlled_buffer_4
endmodule

module Clock (
  input  TK,
  input  TGL,
  input  HT,
  output OUT
);

  wire clock_1_out, multiplexer_1_out, not_1_out;

  Clock_part clock_1 (.out(clock_1_out));
  not not_1 (not_1_out, HT);
  Multiplexer #(.enable("false")) multiplexer_1 (.in0(clock_1_out), .in1(TK), .out(multiplexer_1_out), .sel(TGL));
  and and_1 (OUT, multiplexer_1_out, not_1_out);
endmodule
