// Logisim project SAP1 Redesigned.circ as structural Verilog: 15 circuits, main circuit main
module main (
);

  wire accumulator_1_s0, accumulator_1_s1, accumulator_1_s2, accumulator_1_s3, accumulator_1_s4,
       accumulator_1_s5, accumulator_1_s6, accumulator_1_s7, ADDRESS_p1, ADDRESS_p2, ADDRESS_p3, ADDRESS_p4,
       auxilliary_1_clk, auxilliary_1_clr, auxilliary_1_o0, auxilliary_1_o1, auxilliary_1_o2,
       auxilliary_1_o3, auxilliary_1_str, b_register_1_o0, b_register_1_o1, b_register_1_o2, b_register_1_o3,
       b_register_1_o4, b_register_1_o5, b_register_1_o6, b_register_1_o7, CLK_out, CLR_out,
       controlled_buffer_1_out, controllersequencer_1_halt, DATA_p1, DATA_p2, DATA_p3, DATA_p4, DATA_p5,
       DATA_p6, DATA_p7, DATA_p8, instructionregister_1_o4, instructionregister_1_o5,
       instructionregister_1_o6, instructionregister_1_o7, mar_1_o0, mar_1_o1, mar_1_o2, mar_1_o3,
       programcounter_1_o0, programcounter_1_o1, programcounter_1_o2, programcounter_1_o3, ram_1_o4,
       ram_1_o5, ram_1_o6, ram_1_o7, RST_out, RUN_p1, WR_out;
  wire [3:0] controllersequencer_1_ea, controllersequencer_1_nce, controllersequencer_1_nlo,
       output_register_1_o0, output_register_1_o4;

  // DipSwitch ADDRESS: pin names not known; wires that end beside it: ADDRESS_p1, ADDRESS_p2, ADDRESS_p3, ADDRESS_p4
  // DipSwitch #(.NSwitches(8)) DATA: pin names not known; wires that end beside it: DATA_p1, DATA_p2, DATA_p3, DATA_p4, DATA_p5, DATA_p6, DATA_p7, DATA_p8
  Button CLR (.out(CLR_out));
  Button WR (.out(WR_out));
  // DipSwitch #(.NSwitches(1)) RUN: pin names not known; wires that end beside it: RUN_p1
  assign controlled_buffer_1_out = ~controllersequencer_1_halt ? CLK_out : 1'bz;  // Controlled_Buffer controlled_buffer_1
  Clock CLK (.out(CLK_out));
  Hex_Digit_Display hex_digit_display_1 (.value(controllersequencer_1_ea));  // open: dp
  Hex_Digit_Display hex_digit_display_2 (.value(controllersequencer_1_nce));  // open: dp
  Button RST (.out(RST_out));
  DotMatrix #(.matrixcols(8), .matrixrows(1)) dotmatrix_1 (
    .col0(ram_1_o7), .col1(ram_1_o6), .col2(ram_1_o5), .col3(ram_1_o4), .col4(programcounter_1_o3),
    .col5(programcounter_1_o2), .col6(programcounter_1_o1), .col7(programcounter_1_o0));
  ProgramCounter programcounter_1 (
    .Cp(controllersequencer_1_nce[3]), .nCLK(controlled_buffer_1_out), .Ep(controllersequencer_1_nce[2]),
    .CLR(RST_out), .O0(programcounter_1_o0), .O1(programcounter_1_o1), .O2(programcounter_1_o2),
    .O3(programcounter_1_o3));
  MAR mar_1 (
    .CLK(controlled_buffer_1_out), .nLm(controllersequencer_1_nce[1]), .CLR(RST_out), .O0(mar_1_o0),
    .O1(mar_1_o1), .O2(mar_1_o2), .O3(mar_1_o3), .I3(programcounter_1_o3), .I2(programcounter_1_o2),
    .I1(programcounter_1_o1), .I0(programcounter_1_o0));
  Auxilliary auxilliary_1 (
    .I3(mar_1_o3), .I2(mar_1_o2), .I1(mar_1_o1), .I0(mar_1_o0), .O3(auxilliary_1_o3), .O2(auxilliary_1_o2),
    .O1(auxilliary_1_o1), .O0(auxilliary_1_o0), .STR(auxilliary_1_str), .CLK(auxilliary_1_clk),
    .CLR(auxilliary_1_clr), .PM(RUN_p1), .C_RAM(CLR_out), .WR(WR_out), .A0(ADDRESS_p4), .A1(ADDRESS_p3),
    .A2(ADDRESS_p2), .A3(ADDRESS_p1));
  RAM ram_1 (
    .nCE(controllersequencer_1_nce[0]), .O0(programcounter_1_o0), .O1(programcounter_1_o1),
    .O2(programcounter_1_o2), .O3(programcounter_1_o3), .O4(ram_1_o4), .O5(ram_1_o5), .O6(ram_1_o6),
    .O7(ram_1_o7), .I7(DATA_p1), .I6(DATA_p2), .I5(DATA_p3), .I4(DATA_p4), .I3(DATA_p5), .I2(DATA_p6),
    .I1(DATA_p7), .I0(DATA_p8), .A0(auxilliary_1_o0), .A1(auxilliary_1_o1), .A2(auxilliary_1_o2),
    .A3(auxilliary_1_o3), .CLR(auxilliary_1_clr), .CLK(auxilliary_1_clk), .STR(auxilliary_1_str));
  InstructionRegister instructionregister_1 (
    .CLK(controlled_buffer_1_out), .CLR(RST_out), .nLi(controllersequencer_1_ea[3]),
    .nEi(controllersequencer_1_ea[2]), .O0(programcounter_1_o0), .O1(programcounter_1_o1),
    .O2(programcounter_1_o2), .O3(programcounter_1_o3), .I7(ram_1_o7), .I6(ram_1_o6), .I5(ram_1_o5),
    .I4(ram_1_o4), .I3(programcounter_1_o3), .I2(programcounter_1_o2), .I1(programcounter_1_o1),
    .I0(programcounter_1_o0), .O7(instructionregister_1_o7), .O6(instructionregister_1_o6),
    .O5(instructionregister_1_o5), .O4(instructionregister_1_o4));
  ControllerSequencer controllersequencer_1 (
    .CLK(controlled_buffer_1_out), .I7(instructionregister_1_o7), ._16(instructionregister_1_o6),
    .I5(instructionregister_1_o5), .I4(instructionregister_1_o4), .Cp(controllersequencer_1_nce[3]),
    .Ep(controllersequencer_1_nce[2]), .nLm(controllersequencer_1_nce[1]),
    .nCE(controllersequencer_1_nce[0]), .nLi(controllersequencer_1_ea[3]), .nEi(controllersequencer_1_ea[2]),
    .nLa(controllersequencer_1_ea[1]), .Ea(controllersequencer_1_ea[0]), .Su(controllersequencer_1_nlo[3]),
    .Eu(controllersequencer_1_nlo[2]), .nLb(controllersequencer_1_nlo[1]),
    .nLo(controllersequencer_1_nlo[0]), .HALT(controllersequencer_1_halt), .CLR(RST_out));
  Pull_Resistor pull_resistor_1 (.node(ram_1_o5));
  Pull_Resistor pull_resistor_2 (.node(ram_1_o7));
  Pull_Resistor pull_resistor_3 (.node(ram_1_o6));
  Hex_Digit_Display hex_digit_display_3 (.value(controllersequencer_1_nlo));  // open: dp
  Pull_Resistor pull_resistor_4 (.node(ram_1_o4));
  Pull_Resistor pull_resistor_5 (.node(programcounter_1_o3));
  Pull_Resistor pull_resistor_6 (.node(programcounter_1_o1));
  Pull_Resistor pull_resistor_7 (.node(programcounter_1_o2));
  Pull_Resistor pull_resistor_8 (.node(programcounter_1_o0));
  Hex_Digit_Display hex_digit_display_4 (.value(output_register_1_o4));  // open: dp
  Accumulator accumulator_1 (
    .nLa(controllersequencer_1_ea[1]), .Ea(controllersequencer_1_ea[0]), .CLK(controlled_buffer_1_out),
    .CLR(RST_out), .O0(programcounter_1_o0), .O1(programcounter_1_o1), .O2(programcounter_1_o2),
    .O3(programcounter_1_o3), .O4(ram_1_o4), .O5(ram_1_o5), .O6(ram_1_o6), .O7(ram_1_o7),
    .S7(accumulator_1_s7), .S6(accumulator_1_s6), .S5(accumulator_1_s5), .S4(accumulator_1_s4),
    .S3(accumulator_1_s3), .S2(accumulator_1_s2), .S1(accumulator_1_s1), .S0(accumulator_1_s0),
    .I7(ram_1_o7), .I6(ram_1_o6), .I5(ram_1_o5), .I4(ram_1_o4), .I3(programcounter_1_o3),
    .I2(programcounter_1_o2), .I1(programcounter_1_o1), .I0(programcounter_1_o0));
  AdderSubtractor addersubtractor_1 (
    .Su(controllersequencer_1_nlo[3]), .Eu(controllersequencer_1_nlo[2]), .O0(ram_1_o7), .O1(ram_1_o6),
    .O2(ram_1_o5), .O3(ram_1_o4), .O4(programcounter_1_o3), .O5(programcounter_1_o2),
    .O6(programcounter_1_o1), .O7(programcounter_1_o0), .A7(accumulator_1_s7), .A6(accumulator_1_s6),
    .A5(accumulator_1_s5), .A4(accumulator_1_s4), .A3(accumulator_1_s3), .A2(accumulator_1_s2),
    .A1(accumulator_1_s1), .A0(accumulator_1_s0), .B7(b_register_1_o7), .B6(b_register_1_o6),
    .B5(b_register_1_o5), .B4(b_register_1_o4), .B3(b_register_1_o3), .B2(b_register_1_o2),
    .B1(b_register_1_o1), .B0(b_register_1_o0));
  B_Register b_register_1 (
    .CLK(controlled_buffer_1_out), .nLb(controllersequencer_1_nlo[1]), .CLR(RST_out), .O0(b_register_1_o0),
    .O1(b_register_1_o1), .O2(b_register_1_o2), .O3(b_register_1_o3), .O4(b_register_1_o4),
    .O5(b_register_1_o5), .O6(b_register_1_o6), .O7(b_register_1_o7), .I7(ram_1_o7), .I6(ram_1_o6),
    .I5(ram_1_o5), .I4(ram_1_o4), .I3(programcounter_1_o3), .I2(programcounter_1_o2),
    .I1(programcounter_1_o1), .I0(programcounter_1_o0));
  Output_Register output_register_1 (
    .CLK(controlled_buffer_1_out), .nLo(controllersequencer_1_nlo[0]), .CLR(RST_out),
    .O0(output_register_1_o0[0]), .O1(output_register_1_o0[1]), .O2(output_register_1_o0[2]),
    .O3(output_register_1_o0[3]), .O4(output_register_1_o4[0]), .O5(output_register_1_o4[1]),
    .O6(output_register_1_o4[2]), .O7(output_register_1_o4[3]), .I7(ram_1_o7), .I6(ram_1_o6), .I5(ram_1_o5),
    .I4(ram_1_o4), .I3(programcounter_1_o3), .I2(programcounter_1_o2), .I1(programcounter_1_o1),
    .I0(programcounter_1_o0));
  Hex_Digit_Display hex_digit_display_5 (.value(output_register_1_o0));  // open: dp
endmodule

// PC
module ProgramCounter (
  input  Cp,
  input  nCLK,
  input  Ep,
  input  CLR,
  output O0,
  output O1,
  output O2,
  output O3
);

  wire half_adder_1_sum, half_adder_2_carry, half_adder_2_sum, half_adder_3_carry, half_adder_3_sum,
       half_adder_4_carry, half_adder_4_sum, not_1_out;
  wire [3:0] d_ff_4_q;

  not not_1 (not_1_out, nCLK);
  half_adder half_adder_1 (.A(half_adder_2_carry), .Sum(half_adder_1_sum), .B(d_ff_4_q[3]));  // open: Carry
  D_Flip_Flop #(.Pre_Clr_Positions("LEGACY"), .enable("true"), .NewFFLayout("false")) d_ff_1 (
    .clk(not_1_out), .D(half_adder_1_sum), .Q(d_ff_4_q[3]), .reset(CLR));  // open: Qn, preset, en
  half_adder half_adder_2 (.A(half_adder_3_carry), .Sum(half_adder_2_sum), .B(d_ff_4_q[2]), .Carry(half_adder_2_carry));
  D_Flip_Flop #(.Pre_Clr_Positions("LEGACY"), .enable("true"), .NewFFLayout("false")) d_ff_2 (
    .clk(not_1_out), .D(half_adder_2_sum), .Q(d_ff_4_q[2]), .reset(CLR));  // open: Qn, preset, en
  half_adder half_adder_3 (.A(half_adder_4_carry), .Sum(half_adder_3_sum), .B(d_ff_4_q[1]), .Carry(half_adder_3_carry));
  D_Flip_Flop #(.Pre_Clr_Positions("LEGACY"), .enable("true"), .NewFFLayout("false")) d_ff_3 (
    .clk(not_1_out), .D(half_adder_3_sum), .Q(d_ff_4_q[1]), .reset(CLR));  // open: Qn, preset, en
  half_adder half_adder_4 (.A(Cp), .Sum(half_adder_4_sum), .B(d_ff_4_q[0]), .Carry(half_adder_4_carry));
  D_Flip_Flop #(.Pre_Clr_Positions("LEGACY"), .enable("true"), .NewFFLayout("false")) d_ff_4 (
    .clk(not_1_out), .D(half_adder_4_sum), .Q(d_ff_4_q[0]), .reset(CLR));  // open: Qn, preset, en
  assign {O3, O2, O1, O0} = Ep ? d_ff_4_q : 4'bz;  // Controlled_Buffer controlled_buffer_1
endmodule

module MAR (
  input  CLK,
  input  CLR,
  input  I3,
  input  I2,
  input  I1,
  input  I0,
  input  nLm,
  output O0,
  output O1,
  output O2,
  output O3
);

  wire not_1_out;
  wire [3:0] controlled_buffer_1_out;

  assign controlled_buffer_1_out = not_1_out ? {I3, I2, I1, I0} : 4'bz;  // Controlled_Buffer controlled_buffer_1
  not not_1 (not_1_out, nLm);
  D_Flip_Flop #(.Pre_Clr_Positions("LEGACY"), .enable("true"), .NewFFLayout("false")) d_ff_1 (
    .clk(CLK), .D(controlled_buffer_1_out[3]), .Q(O3), .reset(CLR));  // open: Qn, preset, en
  D_Flip_Flop #(.Pre_Clr_Positions("LEGACY"), .enable("true"), .NewFFLayout("false")) d_ff_2 (
    .clk(CLK), .D(controlled_buffer_1_out[2]), .Q(O2), .reset(CLR));  // open: Qn, preset, en
  D_Flip_Flop #(.Pre_Clr_Positions("LEGACY"), .enable("true"), .NewFFLayout("false")) d_ff_3 (
    .clk(CLK), .D(controlled_buffer_1_out[1]), .Q(O1), .reset(CLR));  // open: Qn, preset, en
  D_Flip_Flop #(.Pre_Clr_Positions("LEGACY"), .enable("true"), .NewFFLayout("false")) D0 (
    .clk(CLK), .D(controlled_buffer_1_out[0]), .Q(O0), .reset(CLR));  // open: Qn, preset, en
endmodule

module RAM (
  input  A0,
  input  A1,
  input  A2,
  input  A3,
  input  I7,
  input  I6,
  input  I5,
  input  I4,
  input  I3,
  input  I2,
  input  I1,
  input  I0,
  input  nCE,
  input  STR,
  input  CLK,
  input  CLR,
  output O0,
  output O1,
  output O2,
  output O3,
  output O4,
  output O5,
  output O6,
  output O7
);

  wire not_1_out;

  not not_1 (not_1_out, nCE);
  RAM_part #(.addrWidth(4), .bus("separate"), .Select("high")) ram_1 (
    .addr({A0, A1, A2, A3}), .din({I7, I6, I5, I4, I3, I2, I1, I0}), .data({O7, O6, O5, O4, O3, O2, O1, O0}),
    .str(STR), .clk(CLK), .ld(not_1_out), .clr(CLR));  // open: sel
endmodule

// I-REG
module InstructionRegister (
  input  nEi,
  input  CLK,
  input  CLR,
  input  I7,
  input  I6,
  input  I5,
  input  I4,
  input  I3,
  input  I2,
  input  I1,
  input  I0,
  input  nLi,
  output O0,
  output O1,
  output O2,
  output O3,
  output O7,
  output O6,
  output O5,
  output O4
);

  wire not_1_out, not_2_out;
  wire [3:0] D0_q;
  wire [7:0] controlled_buffer_1_out;

  D_Flip_Flop #(.Pre_Clr_Positions("LEGACY"), .enable("true"), .NewFFLayout("false")) D7 (
    .clk(CLK), .D(controlled_buffer_1_out[7]), .Q(O7), .reset(CLR));  // open: Qn, preset, en
  D_Flip_Flop #(.Pre_Clr_Positions("LEGACY"), .enable("true"), .NewFFLayout("false")) d_ff_1 (
    .clk(CLK), .D(controlled_buffer_1_out[6]), .Q(O6), .reset(CLR));  // open: Qn, preset, en
  assign controlled_buffer_1_out = not_1_out ? {I7, I6, I5, I4, I3, I2, I1, I0} : 8'bz;  // Controlled_Buffer controlled_buffer_1
  not not_1 (not_1_out, nLi);
  D_Flip_Flop #(.Pre_Clr_Positions("LEGACY"), .enable("true"), .NewFFLayout("false")) d_ff_2 (
    .clk(CLK), .D(controlled_buffer_1_out[5]), .Q(O5), .reset(CLR));  // open: Qn, preset, en
  D_Flip_Flop #(.Pre_Clr_Positions("LEGACY"), .enable("true"), .NewFFLayout("false")) d_ff_3 (
    .clk(CLK), .D(controlled_buffer_1_out[4]), .Q(O4), .reset(CLR));  // open: Qn, preset, en
  D_Flip_Flop #(.Pre_Clr_Positions("LEGACY"), .enable("true"), .NewFFLayout("false")) d_ff_4 (
    .clk(CLK), .D(controlled_buffer_1_out[3]), .Q(D0_q[3]), .reset(CLR));  // open: Qn, preset, en
  assign {O3, O2, O1, O0} = not_2_out ? D0_q : 4'bz;  // Controlled_Buffer controlled_buffer_2
  not not_2 (not_2_out, nEi);
  D_Flip_Flop #(.Pre_Clr_Positions("LEGACY"), .enable("true"), .NewFFLayout("false")) d_ff_5 (
    .clk(CLK), .D(controlled_buffer_1_out[2]), .Q(D0_q[2]), .reset(CLR));  // open: Qn, preset, en
  D_Flip_Flop #(.Pre_Clr_Positions("LEGACY"), .enable("true"), .NewFFLayout("false")) d_ff_6 (
    .clk(CLK), .D(controlled_buffer_1_out[1]), .Q(D0_q[1]), .reset(CLR));  // open: Qn, preset, en
  D_Flip_Flop #(.Pre_Clr_Positions("LEGACY"), .enable("true"), .NewFFLayout("false")) D0 (
    .clk(CLK), .D(controlled_buffer_1_out[0]), .Q(D0_q[0]), .reset(CLR));  // open: Qn, preset, en
endmodule

// CONTROLLER
module ControllerSequencer (
  input  CLK,
  input  CLR,
  input  I5,
  input  _16,
  input  I4,
  input  I7,
  output Cp,
  output Ep,
  output nLm,
  output nCE,
  output nLi,
  output nEi,
  output nLa,
  output Ea,
  output Su,
  output Eu,
  output nLb,
  output nLo,
  output HALT
);

  wire and_1_out, and_2_out, and_3_out, and_4_out, and_5_out, and_6_out, and_7_out, and_8_out, and_9_out,
       and_10_out, and_11_out, and_13_out, and_14_out, and_16_out, and_17_out, and_18_out,
       instruction_decoder_1_add, instruction_decoder_1_lda, instruction_decoder_1_out,
       instruction_decoder_1_sub, ring_counter_1_t3, ring_counter_1_t4, ring_counter_1_t5, ring_counter_1_t6;

  Clock clock_1 ();  // open: out
  ring_counter ring_counter_1 (
    .CLK(CLK), .CLR(CLR), .T1(Ep), .T2(Cp), .T3(ring_counter_1_t3), .T4(ring_counter_1_t4),
    .T5(ring_counter_1_t5), .T6(ring_counter_1_t6));
  instruction_decoder instruction_decoder_1 (
    .I7(I7), .I6(_16), .I5(I5), .I4(I4), .LDA(instruction_decoder_1_lda), .ADD(instruction_decoder_1_add),
    .SUB(instruction_decoder_1_sub), .OUT(instruction_decoder_1_out), .HLT(HALT));
  and and_1 (and_1_out, ring_counter_1_t4, instruction_decoder_1_lda);
  and and_2 (and_2_out, ring_counter_1_t4, instruction_decoder_1_add);
  nor nor_1 (nLm, and_1_out, and_2_out, and_4_out, Ep);
  and and_3 (and_3_out, ring_counter_1_t5, instruction_decoder_1_lda);
  and and_4 (and_4_out, ring_counter_1_t4, instruction_decoder_1_sub);
  Hex_Digit_Display hex_digit_display_1 (.value({Cp, Ep, nLm, nCE}));  // open: dp
  and and_5 (and_5_out, instruction_decoder_1_add, ring_counter_1_t5);
  and and_6 (and_6_out, instruction_decoder_1_sub, ring_counter_1_t5);
  nor nor_2 (nCE, and_3_out, and_5_out, and_6_out, ring_counter_1_t3);
  and and_7 (and_7_out, ring_counter_1_t4, instruction_decoder_1_lda);
  not not_1 (nLi, ring_counter_1_t3);
  and and_8 (and_8_out, ring_counter_1_t4, instruction_decoder_1_sub);
  and and_9 (and_9_out, ring_counter_1_t4, instruction_decoder_1_add);
  nor nor_3 (nEi, and_7_out, and_9_out, and_8_out);
  and and_10 (and_10_out, ring_counter_1_t5, instruction_decoder_1_lda);
  and and_11 (and_11_out, instruction_decoder_1_add, ring_counter_1_t6);
  nor nor_4 (nLa, and_10_out, and_11_out, and_13_out);
  Hex_Digit_Display hex_digit_display_2 (.value({nLi, nEi, nLa, Ea}));  // open: dp
  and and_12 (Ea, ring_counter_1_t4, instruction_decoder_1_out);
  and and_13 (and_13_out, instruction_decoder_1_sub, ring_counter_1_t6);
  and and_14 (and_14_out, ring_counter_1_t6, instruction_decoder_1_add);
  and and_15 (Su, ring_counter_1_t6, instruction_decoder_1_sub);
  or or_1 (Eu, and_14_out, and_17_out);
  and and_16 (and_16_out, ring_counter_1_t5, instruction_decoder_1_add);
  and and_17 (and_17_out, ring_counter_1_t6, instruction_decoder_1_sub);
  nor nor_5 (nLb, and_16_out, and_18_out);
  and and_18 (and_18_out, ring_counter_1_t5, instruction_decoder_1_sub);
  nand nand_1 (nLo, instruction_decoder_1_out, ring_counter_1_t4);
  Hex_Digit_Display hex_digit_display_3 (.value({Su, Eu, nLb, nLo}));  // open: dp
endmodule

// ACC
module Accumulator (
  input  Ea,
  input  CLK,
  input  CLR,
  input  I7,
  input  I6,
  input  I5,
  input  I4,
  input  I3,
  input  I2,
  input  I1,
  input  I0,
  input  nLa,
  output S7,
  output S6,
  output S5,
  output S4,
  output S3,
  output S2,
  output S1,
  output S0,
  output O0,
  output O1,
  output O2,
  output O3,
  output O4,
  output O5,
  output O6,
  output O7
);

  wire not_1_out;
  wire [7:0] controlled_buffer_1_out;

  D_Flip_Flop #(.Pre_Clr_Positions("LEGACY"), .enable("true"), .NewFFLayout("false")) D7 (
    .clk(CLK), .D(controlled_buffer_1_out[7]), .Q(S7), .reset(CLR));  // open: Qn, preset, en
  D_Flip_Flop #(.Pre_Clr_Positions("LEGACY"), .enable("true"), .NewFFLayout("false")) d_ff_1 (
    .clk(CLK), .D(controlled_buffer_1_out[6]), .Q(S6), .reset(CLR));  // open: Qn, preset, en
  assign controlled_buffer_1_out = not_1_out ? {I7, I6, I5, I4, I3, I2, I1, I0} : 8'bz;  // Controlled_Buffer controlled_buffer_1
  not not_1 (not_1_out, nLa);
  D_Flip_Flop #(.Pre_Clr_Positions("LEGACY"), .enable("true"), .NewFFLayout("false")) d_ff_2 (
    .clk(CLK), .D(controlled_buffer_1_out[5]), .Q(S5), .reset(CLR));  // open: Qn, preset, en
  D_Flip_Flop #(.Pre_Clr_Positions("LEGACY"), .enable("true"), .NewFFLayout("false")) d_ff_3 (
    .clk(CLK), .D(controlled_buffer_1_out[4]), .Q(S4), .reset(CLR));  // open: Qn, preset, en
  assign {O7, O6, O5, O4, O3, O2, O1, O0} = Ea ? {S7, S6, S5, S4, S3, S2, S1, S0} : 8'bz;  // Controlled_Buffer controlled_buffer_2
  D_Flip_Flop #(.Pre_Clr_Positions("LEGACY"), .enable("true"), .NewFFLayout("false")) d_ff_4 (
    .clk(CLK), .D(controlled_buffer_1_out[3]), .Q(S3), .reset(CLR));  // open: Qn, preset, en
  D_Flip_Flop #(.Pre_Clr_Positions("LEGACY"), .enable("true"), .NewFFLayout("false")) d_ff_5 (
    .clk(CLK), .D(controlled_buffer_1_out[2]), .Q(S2), .reset(CLR));  // open: Qn, preset, en
  D_Flip_Flop #(.Pre_Clr_Positions("LEGACY"), .enable("true"), .NewFFLayout("false")) d_ff_6 (
    .clk(CLK), .D(controlled_buffer_1_out[1]), .Q(S1), .reset(CLR));  // open: Qn, preset, en
  D_Flip_Flop #(.Pre_Clr_Positions("LEGACY"), .enable("true"), .NewFFLayout("false")) D0 (
    .clk(CLK), .D(controlled_buffer_1_out[0]), .Q(S0), .reset(CLR));  // open: Qn, preset, en
endmodule

// ALU
module AdderSubtractor (
  input  B7,
  input  B6,
  input  B5,
  input  B4,
  input  B3,
  input  B2,
  input  B1,
  input  B0,
  input  Su,
  input  Eu,
  input  A7,
  input  A6,
  input  A5,
  input  A4,
  input  A3,
  input  A2,
  input  A1,
  input  A0,
  output O0,
  output O1,
  output O2,
  output O3,
  output O4,
  output O5,
  output O6,
  output O7
);

  wire full_adder_2_cout, full_adder_3_cout, full_adder_4_cout, full_adder_5_cout, full_adder_6_cout,
       full_adder_7_cout, full_adder_8_cout, xor_1_out, xor_2_out, xor_3_out, xor_4_out, xor_5_out,
       xor_6_out, xor_7_out, xor_8_out;
  wire [7:0] full_adder_8_sum;

  assign {O0, O1, O2, O3, O4, O5, O6, O7} = Eu ? full_adder_8_sum : 8'bz;  // Controlled_Buffer controlled_buffer_1
  xor xor_1 (xor_1_out, Su, B7);
  full_adder full_adder_1 (.A(A7), .B(xor_1_out), .Cin(full_adder_2_cout), .Sum(full_adder_8_sum[7]));  // open: Cout
  xor xor_2 (xor_2_out, Su, B6);
  full_adder full_adder_2 (
    .A(A6), .B(xor_2_out), .Cin(full_adder_3_cout), .Sum(full_adder_8_sum[6]), .Cout(full_adder_2_cout));
  xor xor_3 (xor_3_out, Su, B5);
  full_adder full_adder_3 (
    .A(A5), .B(xor_3_out), .Cin(full_adder_4_cout), .Sum(full_adder_8_sum[5]), .Cout(full_adder_3_cout));
  xor xor_4 (xor_4_out, Su, B4);
  full_adder full_adder_4 (
    .A(A4), .B(xor_4_out), .Cin(full_adder_5_cout), .Sum(full_adder_8_sum[4]), .Cout(full_adder_4_cout));
  xor xor_5 (xor_5_out, Su, B3);
  full_adder full_adder_5 (
    .A(A3), .B(xor_5_out), .Cin(full_adder_6_cout), .Sum(full_adder_8_sum[3]), .Cout(full_adder_5_cout));
  xor xor_6 (xor_6_out, Su, B2);
  full_adder full_adder_6 (
    .A(A2), .B(xor_6_out), .Cin(full_adder_7_cout), .Sum(full_adder_8_sum[2]), .Cout(full_adder_6_cout));
  full_adder full_adder_7 (
    .A(A1), .B(xor_7_out), .Cin(full_adder_8_cout), .Sum(full_adder_8_sum[1]), .Cout(full_adder_7_cout));
  xor xor_7 (xor_7_out, Su, B1);
  full_adder full_adder_8 (.A(A0), .B(xor_8_out), .Cin(Su), .Sum(full_adder_8_sum[0]), .Cout(full_adder_8_cout));
  xor xor_8 (xor_8_out, Su, B0);
endmodule

// B-REG
module B_Register (
  input  CLK,
  input  CLR,
  input  I7,
  input  I6,
  input  I5,
  input  I4,
  input  I3,
  input  I2,
  input  I1,
  input  I0,
  input  nLb,
  output O0,
  output O1,
  output O2,
  output O3,
  output O4,
  output O5,
  output O6,
  output O7
);

  wire not_1_out;
  wire [7:0] controlled_buffer_1_out;

  D_Flip_Flop #(.Pre_Clr_Positions("LEGACY"), .enable("true"), .NewFFLayout("false")) D7 (
    .clk(CLK), .D(controlled_buffer_1_out[7]), .Q(O7), .reset(CLR));  // open: Qn, preset, en
  D_Flip_Flop #(.Pre_Clr_Positions("LEGACY"), .enable("true"), .NewFFLayout("false")) d_ff_1 (
    .clk(CLK), .D(controlled_buffer_1_out[6]), .Q(O6), .reset(CLR));  // open: Qn, preset, en
  assign controlled_buffer_1_out = not_1_out ? {I7, I6, I5, I4, I3, I2, I1, I0} : 8'bz;  // Controlled_Buffer controlled_buffer_1
  not not_1 (not_1_out, nLb);
  D_Flip_Flop #(.Pre_Clr_Positions("LEGACY"), .enable("true"), .NewFFLayout("false")) d_ff_2 (
    .clk(CLK), .D(controlled_buffer_1_out[5]), .Q(O5), .reset(CLR));  // open: Qn, preset, en
  D_Flip_Flop #(.Pre_Clr_Positions("LEGACY"), .enable("true"), .NewFFLayout("false")) d_ff_3 (
    .clk(CLK), .D(controlled_buffer_1_out[4]), .Q(O4), .reset(CLR));  // open: Qn, preset, en
  D_Flip_Flop #(.Pre_Clr_Positions("LEGACY"), .enable("true"), .NewFFLayout("false")) d_ff_4 (
    .clk(CLK), .D(controlled_buffer_1_out[3]), .Q(O3), .reset(CLR));  // open: Qn, preset, en
  D_Flip_Flop #(.Pre_Clr_Positions("LEGACY"), .enable("true"), .NewFFLayout("false")) d_ff_5 (
    .clk(CLK), .D(controlled_buffer_1_out[2]), .Q(O2), .reset(CLR));  // open: Qn, preset, en
  D_Flip_Flop #(.Pre_Clr_Positions("LEGACY"), .enable("true"), .NewFFLayout("false")) d_ff_6 (
    .clk(CLK), .D(controlled_buffer_1_out[1]), .Q(O1), .reset(CLR));  // open: Qn, preset, en
  D_Flip_Flop #(.Pre_Clr_Positions("LEGACY"), .enable("true"), .NewFFLayout("false")) D0 (
    .clk(CLK), .D(controlled_buffer_1_out[0]), .Q(O0), .reset(CLR));  // open: Qn, preset, en
endmodule

// OUT-REG
module Output_Register (
  input  CLK,
  input  CLR,
  input  I7,
  input  I6,
  input  I5,
  input  I4,
  input  I3,
  input  I2,
  input  I1,
  input  I0,
  input  nLo,
  output O0,
  output O1,
  output O2,
  output O3,
  output O4,
  output O5,
  output O6,
  output O7
);

  wire not_1_out;
  wire [7:0] controlled_buffer_1_out;

  D_Flip_Flop #(.Pre_Clr_Positions("LEGACY"), .enable("true"), .NewFFLayout("false")) D7 (
    .clk(CLK), .D(controlled_buffer_1_out[7]), .Q(O7), .reset(CLR));  // open: Qn, preset, en
  D_Flip_Flop #(.Pre_Clr_Positions("LEGACY"), .enable("true"), .NewFFLayout("false")) d_ff_1 (
    .clk(CLK), .D(controlled_buffer_1_out[6]), .Q(O6), .reset(CLR));  // open: Qn, preset, en
  not not_1 (not_1_out, nLo);
  D_Flip_Flop #(.Pre_Clr_Positions("LEGACY"), .enable("true"), .NewFFLayout("false")) d_ff_2 (
    .clk(CLK), .D(controlled_buffer_1_out[5]), .Q(O5), .reset(CLR));  // open: Qn, preset, en
  assign controlled_buffer_1_out = not_1_out ? {I7, I6, I5, I4, I3, I2, I1, I0} : 8'bz;  // Controlled_Buffer controlled_buffer_1
  D_Flip_Flop #(.Pre_Clr_Positions("LEGACY"), .enable("true"), .NewFFLayout("false")) d_ff_3 (
    .clk(CLK), .D(controlled_buffer_1_out[4]), .Q(O4), .reset(CLR));  // open: Qn, preset, en
  D_Flip_Flop #(.Pre_Clr_Positions("LEGACY"), .enable("true"), .NewFFLayout("false")) d_ff_4 (
    .clk(CLK), .D(controlled_buffer_1_out[3]), .Q(O3), .reset(CLR));  // open: Qn, preset, en
  D_Flip_Flop #(.Pre_Clr_Positions("LEGACY"), .enable("true"), .NewFFLayout("false")) d_ff_5 (
    .clk(CLK), .D(controlled_buffer_1_out[2]), .Q(O2), .reset(CLR));  // open: Qn, preset, en
  D_Flip_Flop #(.Pre_Clr_Positions("LEGACY"), .enable("true"), .NewFFLayout("false")) d_ff_6 (
    .clk(CLK), .D(controlled_buffer_1_out[1]), .Q(O1), .reset(CLR));  // open: Qn, preset, en
  D_Flip_Flop #(.Pre_Clr_Positions("LEGACY"), .enable("true"), .NewFFLayout("false")) D0 (
    .clk(CLK), .D(controlled_buffer_1_out[0]), .Q(O0), .reset(CLR));  // open: Qn, preset, en
endmodule

// Instruction Decoder
module instruction_decoder (
  input  I7,
  input  I6,
  input  I5,
  input  I4,
  output LDA,
  output ADD,
  output SUB,
  output OUT,
  output HLT
);

  wire not_1_out, not_2_out, not_3_out, not_4_out, not_5_out, not_6_out, not_7_out, not_8_out, not_9_out,
       not_10_out, not_11_out;

  not not_1 (not_1_out, I7);
  not not_2 (not_2_out, I6);
  not not_3 (not_3_out, I5);
  not not_4 (not_4_out, I4);
  not not_5 (not_5_out, I7);
  not not_6 (not_6_out, I6);
  not not_7 (not_7_out, I5);
  not not_8 (not_8_out, I7);
  not not_9 (not_9_out, I6);
  not not_10 (not_10_out, I4);
  not not_11 (not_11_out, I4);
  and and_1 (HLT, I7, I6, I5, I4);
  and and_2 (LDA, not_1_out, not_2_out, not_3_out, not_4_out);
  and and_3 (ADD, not_5_out, not_6_out, not_7_out, I4);
  and and_4 (SUB, not_8_out, not_9_out, I5, not_10_out);
  and and_5 (OUT, I7, I6, I5, not_11_out);
endmodule

// HA
module half_adder (
  input  A,
  input  B,
  output Sum,
  output Carry
);

  xor xor_1 (Sum, A, B);
  and and_1 (Carry, B, A);
endmodule

// Ring Counter
module ring_counter (
  input  CLK,
  input  CLR,
  output T1,
  output T2,
  output T3,
  output T4,
  output T5,
  output T6
);

  wire nor_1_out;

  nor nor_1 (nor_1_out, T1, T2, T3, T4, T5, T6);
  D_Flip_Flop #(.Pre_Clr_Positions("LEGACY"), .enable("true"), .NewFFLayout("false")) D1 (
    .clk(CLK), .D(nor_1_out), .Q(T1), .reset(CLR));  // open: Qn, preset, en
  D_Flip_Flop #(.Pre_Clr_Positions("LEGACY"), .enable("true"), .NewFFLayout("false")) d_ff_1 (
    .clk(CLK), .D(T1), .Q(T2), .reset(CLR));  // open: Qn, preset, en
  D_Flip_Flop #(.Pre_Clr_Positions("LEGACY"), .enable("true"), .NewFFLayout("false")) d_ff_2 (
    .clk(CLK), .D(T2), .Q(T3), .reset(CLR));  // open: Qn, preset, en
  D_Flip_Flop #(.Pre_Clr_Positions("LEGACY"), .enable("true"), .NewFFLayout("false")) d_ff_3 (
    .clk(CLK), .D(T3), .Q(T4), .reset(CLR));  // open: Qn, preset, en
  D_Flip_Flop #(.Pre_Clr_Positions("LEGACY"), .enable("true"), .NewFFLayout("false")) d_ff_4 (
    .clk(CLK), .D(T4), .Q(T5), .reset(CLR));  // open: Qn, preset, en
  D_Flip_Flop #(.Pre_Clr_Positions("LEGACY"), .enable("true"), .NewFFLayout("false")) d_ff_5 (
    .clk(CLK), .D(T5), .Q(T6), .reset(CLR));  // open: Qn, preset, en
endmodule

// FA
module full_adder (
  input  A,
  input  B,
  input  Cin,
  output Sum,
  output Cout
);

  wire and_1_out, and_2_out, xor_1_out;

  xor xor_1 (xor_1_out, A, B);
  and and_1 (and_1_out, A, B);
  xor xor_2 (Sum, xor_1_out, Cin);
  and and_2 (and_2_out, xor_1_out, Cin);
  or or_1 (Cout, and_2_out, and_1_out);
endmodule

// AUX
module Auxilliary (
  input  I3,
  input  I2,
  input  I1,
  input  I0,
  input  PM,
  input  C_RAM,
  input  A0,
  input  A1,
  input  A2,
  input  WR,
  input  A3,
  output STR,
  output CLK,
  output CLR,
  output O3,
  output O2,
  output O1,
  output O0
);

  and and_1 (CLR, ~PM, C_RAM);  // AND_Gate
  and and_2 (CLK, ~PM, WR);  // AND_Gate
  not not_1 (STR, PM);
  Multiplexer #(.width(4)) multiplexer_1 (
    .in0({A3, A2, A1, A0}), .in1({I3, I2, I1, I0}), .out({O3, O2, O1, O0}), .sel(PM));  // open: en
endmodule
